// Digital circuit 74TypeFlipFlop.dig as structural Verilog
module _74TypeFlipFlop (
  input  CLK,
  input  Data,
  input  Load_A,
  input  Load_B,
  input  Reset,
  output Always,
  output Loaded_A,
  output Loaded_B
);

  wire nand_1_out, nand_2_out, nand_3_out, nand_4_out, nand_6_out, not_1_out;

  not not_1 (not_1_out, Reset);
  nand nand_1 (nand_1_out, nand_4_out, nand_2_out);
  nand nand_2 (nand_2_out, nand_1_out, CLK);
  nand nand_3 (nand_3_out, nand_2_out, not_1_out, CLK, nand_4_out);
  nand nand_4 (nand_4_out, nand_3_out, Data);
  nand nand_5 (Always, nand_2_out, nand_6_out);
  nand nand_6 (nand_6_out, Always, not_1_out, nand_3_out);
  assign Loaded_A = Load_A ? Always : 1'bz;  // Driver driver_1
  assign Loaded_B = Load_B ? Always : 1'bz;  // Driver driver_2

  // Notes on the sheet:
  //   Edge Flop
  //   CLK
  //   D
  //   A
  //   B
  //   Latch
  //   Alw
endmodule
