// Digital circuit LEG.dig as structural Verilog
module LEG (
  input  C_0,
  input  C_1,
  input  C_2,
  input  [7:0] A_0,
  input  [7:0] B_0,
  input  [7:0] OPCODE,
  input  [7:0] ARG2,
  input  [7:0] ARG1,
  input  [7:0] DESTINATION,
  input  clk,
  input  [7:0] TestAdvRegister,
  input  [7:0] NormalRegTest,
  output [7:0] C_Arith,
  output [7:0] TAR_loadB,
  output [7:0] TAR_loadA,
  output [7:0] TAR_always,
  output [31:0] OPCODE_read,
  output [7:0] TAR_loadB_2,
  output [7:0] TAR_always_2,
  output [7:0] TAR_loadB_3,
  output [7:0] TAR_always_3
);

  wire _74typeflipflop_1_always, _74typeflipflop_18_loaded_a, _74typeflipflop_18_loaded_b,
       _74typeflipflop_19_loaded_a, _74typeflipflop_19_loaded_b, _74typeflipflop_20_loaded_a,
       _74typeflipflop_20_loaded_b, _74typeflipflop_21_loaded_a, _74typeflipflop_21_loaded_b,
       _74typeflipflop_22_loaded_a, _74typeflipflop_22_loaded_b, _74typeflipflop_23_loaded_a,
       _74typeflipflop_23_loaded_b, _74typeflipflop_24_loaded_a, _74typeflipflop_24_loaded_b,
       _74typeflipflop_25_loaded_a, _74typeflipflop_25_loaded_b, _74typeflipflop_34_always,
       _74typeflipflop_35_always, _74typeflipflop_36_always, _74typeflipflop_37_always,
       _74typeflipflop_38_always, _74typeflipflop_39_always, _74typeflipflop_40_always,
       _74typeflipflop_41_always, _74typeflipflop_42_always, _74typeflipflop_43_always,
       _74typeflipflop_44_always, _74typeflipflop_45_always, _74typeflipflop_46_always,
       _74typeflipflop_47_always, _74typeflipflop_48_always, _74typeflipflop_49_always,
       _74typeflipflop_50_always, _74typeflipflop_51_always, _74typeflipflop_52_always,
       _74typeflipflop_53_always, _74typeflipflop_54_always, _74typeflipflop_55_always,
       _74typeflipflop_56_always, _74typeflipflop_57_always, _74typeflipflop_58_always,
       _74typeflipflop_59_always, _74typeflipflop_60_always, _74typeflipflop_61_always,
       _74typeflipflop_62_always, _74typeflipflop_63_always, _74typeflipflop_64_always,
       _74typeflipflop_65_always, _74typeflipflop_66_always, _74typeflipflop_67_always,
       _74typeflipflop_68_always, _74typeflipflop_69_always, _74typeflipflop_70_always,
       _74typeflipflop_71_always, _74typeflipflop_72_always, _74typeflipflop_73_always, and_1_out, and_2_out,
       and_3_out, and_4_out, and_5_out, and_6_out, and_7_out, and_8_out, and_9_out, and_10_out, and_11_out,
       and_12_out, and_13_out, and_14_out, and_15_out, and_16_out, and_17_out, and_18_out, and_20_out,
       and_21_out, and_22_out, and_24_out, and_25_out, and_27_out, and_28_out, and_31_out, and_32_out,
       and_33_out, and_36_out, and_37_out, and_38_out, and_40_out, and_41_out, and_43_out, and_44_out,
       and_45_out, and_46_out, and_47_out, and_48_out, and_49_out, and_50_out, and_51_out, and_52_out,
       and_53_out, and_54_out, and_55_out, and_56_out, and_57_out, and_58_out, and_59_out, and_60_out,
       and_61_out, and_62_out, and_63_out, and_64_out, and_65_out, and_66_out, and_67_out, and_68_out,
       and_69_out, and_70_out, and_71_out, and_72_out, and_73_out, and_74_out, and_75_out, and_76_out,
       and_77_out, and_78_out, and_79_out, and_80_out, and_81_out, and_82_out, and_83_out, and_84_out,
       and_85_out, and_86_out, and_87_out, and_88_out, and_89_out, and_90_out, and_91_out, and_92_out,
       and_93_out, and_94_out, and_95_out, and_96_out, and_97_out, and_98_out, and_99_out, and_100_out,
       and_103_out, and_104_out, and_105_out, and_106_out, and_107_out, and_108_out, and_109_out,
       and_110_out, and_112_out, and_113_out, and_114_out, and_115_out, and_116_out, and_117_out,
       and_118_out, and_119_out, and_120_out, and_121_out, and_122_out, and_123_out, and_124_out,
       and_125_out, and_126_out, and_127_out, and_128_out, and_129_out, and_130_out, and_131_out,
       and_132_out, and_133_out, and_134_out, and_135_out, and_136_out, and_137_out, and_139_out,
       and_140_out, and_141_out, and_142_out, and_143_out, and_144_out, and_145_out, and_146_out,
       and_147_out, and_148_out, and_149_out, and_150_out, and_154_out, and_155_out, and_157_out,
       and_158_out, and_159_out, and_160_out, and_161_out, and_162_out, and_163_out, and_164_out,
       and_165_out, and_166_out, and_167_out, and_168_out, and_169_out, and_170_out, and_171_out,
       and_172_out, and_173_out, and_174_out, and_175_out, and_176_out, and_177_out, and_178_out,
       and_179_out, and_180_out, and_181_out, and_182_out, and_183_out, and_184_out, and_185_out,
       and_186_out, and_187_out, and_188_out, and_189_out, and_190_out, and_191_out, and_192_out,
       and_193_out, and_194_out, and_195_out, and_196_out, and_197_out, and_198_out, and_199_out,
       and_200_out, and_201_out, and_202_out, and_203_out, and_204_out, and_205_out, and_206_out,
       and_207_out, and_208_out, and_209_out, and_210_out, and_211_out, and_213_out, and_214_out,
       and_215_out, and_216_out, and_217_out, and_218_out, and_219_out, and_220_out, and_221_out,
       and_222_out, and_223_out, and_224_out, and_225_out, and_226_out, and_227_out, and_229_out,
       and_230_out, and_231_out, and_232_out, and_233_out, and_234_out, and_235_out, and_236_out,
       and_237_out, and_238_out, and_239_out, and_240_out, and_241_out, and_242_out, and_243_out,
       and_244_out, and_245_out, and_246_out, and_247_out, and_248_out, and_249_out, and_253_out,
       and_254_out, and_255_out, and_256_out, and_257_out, and_258_out, and_259_out, and_260_out,
       and_261_out, and_262_out, and_263_out, and_264_out, and_265_out, and_266_out, and_267_out,
       and_268_out, and_269_out, and_270_out, and_271_out, and_272_out, and_273_out, and_274_out,
       and_275_out, and_276_out, and_277_out, and_278_out, and_282_out, and_283_out, and_284_out,
       and_285_out, and_286_out, and_287_out, and_288_out, and_289_out, and_290_out, and_291_out,
       and_292_out, and_293_out, and_294_out, and_295_out, and_296_out, and_297_out, and_298_out,
       and_299_out, and_300_out, and_301_out, and_303_out, and_304_out, and_305_out, and_306_out,
       and_307_out, and_308_out, and_310_out, and_311_out, and_312_out, and_313_out, and_314_out,
       and_315_out, and_316_out, and_317_out, and_318_out, and_319_out, and_320_out, and_321_out,
       and_322_out, and_323_out, and_324_out, and_325_out, and_326_out, and_327_out, and_328_out,
       and_330_out, and_331_out, and_332_out, and_333_out, and_334_out, and_335_out, and_336_out,
       and_337_out, and_338_out, and_339_out, and_340_out, and_341_out, and_342_out, and_343_out,
       and_344_out, and_345_out, and_346_out, and_347_out, and_348_out, and_349_out, and_350_out,
       and_351_out, and_352_out, and_353_out, and_354_out, and_355_out, and_356_out, and_357_out,
       and_358_out, and_359_out, and_360_out, and_361_out, and_362_out, and_363_out, and_364_out,
       and_365_out, and_366_out, and_367_out, and_368_out, and_369_out, and_370_out, and_371_out,
       and_372_out, and_373_out, and_374_out, and_375_out, and_376_out, and_378_out, and_379_out,
       and_380_out, and_381_out, and_382_out, and_383_out, and_384_out, and_385_out, and_386_out,
       and_387_out, and_388_out, and_389_out, and_390_out, and_391_out, and_392_out, and_393_out,
       and_394_out, and_395_out, and_396_out, and_397_out, and_398_out, and_399_out, and_400_out,
       and_401_out, and_402_out, and_403_out, and_404_out, and_405_out, and_406_out, and_407_out,
       and_408_out, and_409_out, and_410_out, and_411_out, and_412_out, button_1_out, dipswitch_1_out,
       dipswitch_2_out, dipswitch_3_out, dipswitch_4_out, dipswitch_5_out, dipswitch_6_out, dipswitch_7_out,
       dipswitch_8_out, dipswitch_9_out, dipswitch_10_out, dipswitch_11_out, dipswitch_12_out,
       dipswitch_13_out, dipswitch_14_out, dipswitch_15_out, dipswitch_16_out, dipswitch_17_out,
       dipswitch_18_out, driver_153_out, driver_154_out, driver_155_out, driver_156_out, driver_157_out,
       driver_158_out, driver_159_out, driver_160_out, driver_161_out, driver_162_out, driver_163_out,
       driver_164_out, driver_165_out, driver_166_out, driver_167_out, driver_168_out, driver_169_out,
       driver_170_out, driver_171_out, driver_172_out, driver_173_out, driver_174_out, driver_175_out,
       driver_176_out, nand_17_out, nand_18_out, nand_19_out, nand_20_out, nand_21_out, nand_22_out,
       nand_23_out, nand_24_out, nand_25_out, nand_26_out, nand_27_out, nand_28_out, nand_29_out,
       nand_30_out, nand_31_out, nand_32_out, nand_33_out, nand_34_out, nand_35_out, nand_36_out,
       nand_37_out, nand_38_out, nand_39_out, nand_40_out, nand_41_out, nand_42_out, nand_43_out,
       nand_44_out, nand_45_out, nand_46_out, nand_47_out, nand_48_out, nand_49_out, nand_50_out,
       nand_51_out, nand_52_out, nand_53_out, nand_54_out, nand_55_out, nand_56_out, nand_57_out,
       nand_58_out, nand_59_out, nand_60_out, nand_61_out, nand_62_out, nand_63_out, nand_64_out,
       nand_65_out, nand_66_out, nand_67_out, nand_68_out, nand_69_out, nand_70_out, nand_71_out,
       nand_72_out, nor_17_out, nor_18_out, nor_19_out, nor_20_out, nor_21_out, nor_22_out, nor_23_out,
       nor_24_out, nor_25_out, nor_26_out, nor_27_out, nor_28_out, nor_29_out, nor_30_out, nor_31_out,
       nor_32_out, nor_33_out, nor_34_out, nor_35_out, nor_36_out, nor_37_out, nor_38_out, nor_39_out,
       nor_40_out, nor_41_out, nor_42_out, not_1_out, not_2_out, not_3_out, not_4_out, not_5_out, not_6_out,
       not_7_out, not_8_out, not_9_out, not_10_out, not_11_out, not_12_out, not_13_out, not_14_out,
       not_15_out, not_16_out, not_17_out, not_18_out, not_19_out, not_20_out, not_21_out, not_22_out,
       not_23_out, not_24_out, not_25_out, not_26_out, not_27_out, not_28_out, not_29_out, not_30_out,
       not_31_out, not_32_out, not_33_out, not_34_out, not_35_out, not_36_out, not_37_out, not_38_out,
       not_39_out, not_40_out, not_41_out, not_42_out, not_43_out, not_44_out, not_45_out, not_46_out,
       not_47_out, not_48_out, not_49_out, not_50_out, not_51_out, not_52_out, not_53_out, not_54_out,
       not_55_out, not_56_out, not_57_out, not_58_out, not_59_out, not_60_out, not_61_out, not_62_out,
       not_63_out, not_64_out, not_65_out, not_66_out, not_67_out, not_68_out, not_69_out, not_70_out,
       not_71_out, notconnected_1_out, notconnected_2_out, notconnected_3_out, notconnected_7_out,
       notconnected_9_out, notconnected_10_out, notconnected_14_out, notconnected_19_out,
       notconnected_23_out, notconnected_24_out, notconnected_25_out, notconnected_26_out,
       notconnected_28_out, or_2_out, or_3_out, or_4_out, or_5_out, or_6_out, or_7_out, or_8_out, or_9_out,
       or_16_out, or_17_out, or_19_out, or_20_out, or_22_out, or_23_out, or_24_out, or_25_out, or_26_out,
       or_27_out, or_28_out, or_29_out, or_30_out, or_31_out, or_32_out, or_33_out, or_34_out, or_35_out,
       or_36_out, or_37_out, or_38_out, or_39_out, or_40_out, or_41_out, or_42_out, or_43_out, or_44_out,
       or_45_out, or_46_out, or_47_out, or_48_out, or_49_out, or_50_out, or_51_out, or_52_out, or_53_out,
       or_54_out, or_55_out, or_56_out, or_57_out, or_58_out, or_59_out, or_60_out, or_61_out, or_62_out,
       or_63_out, or_64_out, or_65_out, or_66_out, or_67_out, or_68_out, or_69_out, or_70_out, or_71_out,
       or_72_out, or_73_out, or_75_out, or_76_out, or_77_out, or_84_out, or_85_out, or_87_out, or_88_out,
       or_89_out, or_90_out, or_91_out, or_92_out, or_93_out, or_94_out, or_96_out, or_97_out, or_98_out,
       or_99_out, or_100_out, or_101_out, or_102_out, or_103_out, or_104_out, or_105_out, or_106_out,
       or_107_out, or_108_out, or_109_out, or_110_out, or_111_out, or_112_out, or_113_out, or_114_out,
       or_115_out, or_116_out, or_117_out, or_118_out, or_119_out, or_120_out, or_121_out, or_122_out,
       or_123_out, or_124_out, or_125_out, or_126_out, or_127_out, or_128_out, or_129_out, or_130_out,
       reset_1_out, reset_2_out, reset_3_out, reset_4_out, reset_5_out, reset_6_out, reset_7_out,
       reset_8_out, reset_9_out, reset_10_out, reset_20_out, xor_1_out, xor_2_out, xor_3_out, xor_4_out,
       xor_5_out, xor_6_out, xor_7_out, xor_8_out, xor_17_out, xor_18_out, xor_19_out, xor_20_out,
       xor_21_out, xor_22_out, xor_23_out, xor_24_out, xor_25_out, xor_26_out, xor_27_out, xor_28_out,
       xor_29_out, xor_30_out, xor_31_out, xor_32_out, xor_33_out, xor_34_out, xor_35_out, xor_36_out,
       xor_37_out, xor_38_out, xor_39_out, xor_40_out, xor_43_out, xor_44_out, xor_45_out, xor_46_out,
       xor_47_out, xor_48_out, xor_49_out, xor_50_out, xor_73_out, xor_74_out, xor_75_out, xor_76_out,
       xor_77_out, xor_78_out, xor_79_out, xor_80_out, xor_81_out, xor_82_out, xor_83_out, xor_84_out,
       xor_85_out, xor_86_out, xor_87_out, xor_88_out, xor_89_out, xor_90_out, xor_91_out, xor_92_out,
       xor_93_out, xor_94_out, xor_95_out, xor_96_out, xor_97_out, xor_98_out, xor_99_out, xor_100_out,
       xor_101_out, xor_102_out, xor_103_out, xor_104_out, xor_111_out, xor_112_out, xor_113_out,
       xor_114_out, xor_115_out, xor_116_out, xor_117_out, xor_118_out, xor_129_out, xor_130_out,
       xor_131_out, xor_132_out, xor_133_out, xor_134_out, xor_135_out, xor_136_out, xor_137_out,
       xor_138_out, xor_139_out, xor_140_out, xor_141_out, xor_142_out, xor_143_out, xor_144_out,
       xor_145_out, xor_146_out, xor_147_out, xor_148_out, xor_149_out, xor_150_out, xor_151_out,
       xor_152_out, xor_153_out, xor_154_out, xor_155_out, xor_156_out, xor_157_out, xor_158_out,
       xor_159_out, xor_160_out, xor_161_out, xor_162_out, xor_163_out, xor_164_out, xor_165_out,
       xor_166_out, xor_167_out, xor_168_out;
  wire [7:0] _74typeflipflop_9_loaded_a, _74typeflipflop_17_loaded_a, _74typeflipflop_25_always,
       _74typeflipflop_26_loaded_b, _74typeflipflop_33_always, _74typeflipflop_33_loaded_a, and_42_out,
       and_156_out, and_309_out, delay_1_out, driver_8_out, driver_80_out, driver_104_out, nand_8_out,
       nand_16_out, nor_8_out, nor_16_out, notconnected_4_out, notconnected_6_out, notconnected_8_out,
       notconnected_11_out, notconnected_12_out, notconnected_13_out, notconnected_15_out,
       notconnected_16_out, notconnected_17_out, notconnected_18_out, notconnected_20_out,
       notconnected_21_out, notconnected_22_out, notconnected_27_out, or_21_out, or_95_out, rom_1_d,
       xor_16_out, xor_56_out, xor_57_out, xor_69_out, xor_124_out, xor_128_out;
  wire [31:0] Program_Memory_d;

  and and_1 (and_1_out, 1'b0, _74typeflipflop_25_always[7]);
  xor xor_1 (xor_1_out, _74typeflipflop_25_always[7], 1'b0);
  and and_2 (and_2_out, 1'b0, _74typeflipflop_25_always[6]);
  xor xor_2 (xor_2_out, _74typeflipflop_25_always[6], 1'b0);
  and and_3 (and_3_out, 1'b0, _74typeflipflop_25_always[5]);
  xor xor_3 (xor_3_out, _74typeflipflop_25_always[5], 1'b0);
  and and_4 (and_4_out, 1'b0, _74typeflipflop_25_always[4]);
  xor xor_4 (xor_4_out, _74typeflipflop_25_always[4], 1'b0);
  and and_5 (and_5_out, 1'b0, _74typeflipflop_25_always[3]);
  xor xor_5 (xor_5_out, _74typeflipflop_25_always[3], 1'b0);
  and and_6 (and_6_out, 1'b0, _74typeflipflop_25_always[2]);
  xor xor_6 (xor_6_out, _74typeflipflop_25_always[2], 1'b0);
  and and_7 (and_7_out, 1'b0, _74typeflipflop_25_always[1]);
  xor xor_7 (xor_7_out, _74typeflipflop_25_always[1], 1'b0);
  and and_8 (and_8_out, 1'b1, _74typeflipflop_25_always[0]);
  xor xor_8 (xor_8_out, _74typeflipflop_25_always[0], 1'b1);
  assign driver_8_out[0] = and_229_out ? OPCODE_read[0] : 1'bz;  // Driver driver_1
  // Or or_1 has open pins: In_1=and_1_out, In_2=and_9_out, out=open
  and and_9 (and_9_out, xor_1_out, or_2_out);
  xor xor_9 (xor_16_out[7], xor_1_out, or_2_out);
  or or_2 (or_2_out, and_2_out, and_10_out);
  and and_10 (and_10_out, xor_2_out, or_3_out);
  xor xor_10 (xor_16_out[6], xor_2_out, or_3_out);
  or or_3 (or_3_out, and_3_out, and_11_out);
  and and_11 (and_11_out, xor_3_out, or_4_out);
  xor xor_11 (xor_16_out[5], xor_3_out, or_4_out);
  or or_4 (or_4_out, and_4_out, and_12_out);
  and and_12 (and_12_out, xor_4_out, or_5_out);
  xor xor_12 (xor_16_out[4], xor_4_out, or_5_out);
  or or_5 (or_5_out, and_5_out, and_13_out);
  or or_6 (or_6_out, and_6_out, and_14_out);
  or or_7 (or_7_out, and_7_out, and_15_out);
  or or_8 (or_8_out, and_8_out, and_16_out);
  assign driver_8_out[1] = and_229_out ? OPCODE_read[1] : 1'bz;  // Driver driver_2
  assign driver_8_out[2] = and_229_out ? OPCODE_read[2] : 1'bz;  // Driver driver_3
  and and_13 (and_13_out, xor_5_out, or_6_out);
  xor xor_13 (xor_16_out[3], xor_5_out, or_6_out);
  and and_14 (and_14_out, xor_6_out, or_7_out);
  xor xor_14 (xor_16_out[2], xor_6_out, or_7_out);
  and and_15 (and_15_out, xor_7_out, or_8_out);
  xor xor_15 (xor_16_out[1], xor_7_out, or_8_out);
  and and_16 (and_16_out, xor_8_out, 1'b0);
  xor xor_16 (xor_16_out[0], xor_8_out, 1'b0);
  assign driver_8_out[3] = and_229_out ? OPCODE_read[3] : 1'bz;  // Driver driver_4
  assign driver_8_out[4] = and_229_out ? OPCODE_read[4] : 1'bz;  // Driver driver_5
  assign driver_8_out[5] = and_229_out ? OPCODE_read[5] : 1'bz;  // Driver driver_6
  assign driver_8_out[6] = and_229_out ? OPCODE_read[6] : 1'bz;  // Driver driver_7
  not not_1 (not_1_out, and_229_out);
  assign driver_8_out[7] = and_229_out ? OPCODE_read[7] : 1'bz;  // Driver driver_8
  assign driver_8_out[0] = not_1_out ? xor_16_out[0] : 1'bz;  // Driver driver_9
  assign driver_8_out[1] = not_1_out ? xor_16_out[1] : 1'bz;  // Driver driver_10
  assign driver_8_out[2] = not_1_out ? xor_16_out[2] : 1'bz;  // Driver driver_11
  assign driver_8_out[3] = not_1_out ? xor_16_out[3] : 1'bz;  // Driver driver_12
  assign driver_8_out[4] = not_1_out ? xor_16_out[4] : 1'bz;  // Driver driver_13
  assign driver_8_out[5] = not_1_out ? xor_16_out[5] : 1'bz;  // Driver driver_14
  and and_17 (and_17_out, not_5_out, not_4_out);
  not not_2 (not_2_out, and_17_out);
  assign driver_8_out[6] = not_1_out ? xor_16_out[6] : 1'bz;  // Driver driver_15
  assign driver_8_out[7] = not_1_out ? xor_16_out[7] : 1'bz;  // Driver driver_16
  not not_3 (not_3_out, _74typeflipflop_1_always);
  _74TypeFlipFlop _74typeflipflop_1 (
    .CLK(or_9_out), .Data(not_3_out), .Load_A(notconnected_1_out), .Load_B(notconnected_2_out),
    .Always(_74typeflipflop_1_always), .Reset(notconnected_3_out));  // open: Loaded_A, Loaded_B
  or or_9 (or_9_out, and_17_out, reset_1_out);
  Reset #(.invertOutput("false")) reset_1 (.out(reset_1_out));
  // NotConnected on notconnected_1_out
  // NotConnected on notconnected_2_out
  // NotConnected on notconnected_3_out
  DipSwitch dipswitch_1 (.out(dipswitch_1_out));
  Reset #(.invertOutput("false")) reset_2 (.out(reset_2_out));
  DipSwitch dipswitch_2 (.out(dipswitch_2_out));
  Reset #(.invertOutput("false")) reset_3 (.out(reset_3_out));
  not not_4 (not_4_out, clk);
  Reset #(.invertOutput("false")) reset_4 (.out(reset_4_out));
  _74TypeFlipFlop _74typeflipflop_2 (
    .CLK(and_17_out), .Data(driver_104_out[7]), .Load_A(not_2_out), .Load_B(dipswitch_1_out),
    .Always(TAR_always_2[7]), .Loaded_A(_74typeflipflop_9_loaded_a[7]), .Loaded_B(TAR_loadB_2[7]),
    .Reset(reset_2_out));
  _74TypeFlipFlop _74typeflipflop_3 (
    .CLK(and_17_out), .Data(driver_104_out[6]), .Load_A(not_2_out), .Load_B(dipswitch_1_out),
    .Always(TAR_always_2[6]), .Loaded_A(_74typeflipflop_9_loaded_a[6]), .Loaded_B(TAR_loadB_2[6]),
    .Reset(reset_2_out));
  _74TypeFlipFlop _74typeflipflop_4 (
    .CLK(and_17_out), .Data(driver_104_out[5]), .Load_A(not_2_out), .Load_B(dipswitch_1_out),
    .Always(TAR_always_2[5]), .Loaded_A(_74typeflipflop_9_loaded_a[5]), .Loaded_B(TAR_loadB_2[5]),
    .Reset(reset_2_out));
  _74TypeFlipFlop _74typeflipflop_5 (
    .CLK(and_17_out), .Data(driver_104_out[4]), .Load_A(not_2_out), .Load_B(dipswitch_1_out),
    .Always(TAR_always_2[4]), .Loaded_A(_74typeflipflop_9_loaded_a[4]), .Loaded_B(TAR_loadB_2[4]),
    .Reset(reset_2_out));
  _74TypeFlipFlop _74typeflipflop_6 (
    .CLK(and_17_out), .Data(driver_104_out[3]), .Load_A(not_2_out), .Load_B(dipswitch_1_out),
    .Always(TAR_always_2[3]), .Loaded_A(_74typeflipflop_9_loaded_a[3]), .Loaded_B(TAR_loadB_2[3]),
    .Reset(reset_2_out));
  _74TypeFlipFlop _74typeflipflop_7 (
    .CLK(and_17_out), .Data(driver_104_out[2]), .Load_A(not_2_out), .Load_B(dipswitch_1_out),
    .Always(TAR_always_2[2]), .Loaded_A(_74typeflipflop_9_loaded_a[2]), .Loaded_B(TAR_loadB_2[2]),
    .Reset(reset_2_out));
  _74TypeFlipFlop _74typeflipflop_8 (
    .CLK(and_17_out), .Data(driver_104_out[1]), .Load_A(not_2_out), .Load_B(dipswitch_1_out),
    .Always(TAR_always_2[1]), .Loaded_A(_74typeflipflop_9_loaded_a[1]), .Loaded_B(TAR_loadB_2[1]),
    .Reset(reset_2_out));
  _74TypeFlipFlop _74typeflipflop_9 (
    .CLK(and_17_out), .Data(driver_104_out[0]), .Load_A(not_2_out), .Load_B(dipswitch_1_out),
    .Always(TAR_always_2[0]), .Loaded_A(_74typeflipflop_9_loaded_a[0]), .Loaded_B(TAR_loadB_2[0]),
    .Reset(reset_2_out));
  _74TypeFlipFlop _74typeflipflop_10 (
    .CLK(and_17_out), .Data(and_42_out[7]), .Load_A(not_2_out), .Load_B(dipswitch_2_out),
    .Always(TAR_always_3[7]), .Loaded_A(_74typeflipflop_17_loaded_a[7]), .Loaded_B(TAR_loadB_3[7]),
    .Reset(reset_3_out));
  _74TypeFlipFlop _74typeflipflop_11 (
    .CLK(and_17_out), .Data(and_42_out[6]), .Load_A(not_2_out), .Load_B(dipswitch_2_out),
    .Always(TAR_always_3[6]), .Loaded_A(_74typeflipflop_17_loaded_a[6]), .Loaded_B(TAR_loadB_3[6]),
    .Reset(reset_3_out));
  _74TypeFlipFlop _74typeflipflop_12 (
    .CLK(and_17_out), .Data(and_42_out[5]), .Load_A(not_2_out), .Load_B(dipswitch_2_out),
    .Always(TAR_always_3[5]), .Loaded_A(_74typeflipflop_17_loaded_a[5]), .Loaded_B(TAR_loadB_3[5]),
    .Reset(reset_3_out));
  _74TypeFlipFlop _74typeflipflop_13 (
    .CLK(and_17_out), .Data(and_42_out[4]), .Load_A(not_2_out), .Load_B(dipswitch_2_out),
    .Always(TAR_always_3[4]), .Loaded_A(_74typeflipflop_17_loaded_a[4]), .Loaded_B(TAR_loadB_3[4]),
    .Reset(reset_3_out));
  _74TypeFlipFlop _74typeflipflop_14 (
    .CLK(and_17_out), .Data(and_42_out[3]), .Load_A(not_2_out), .Load_B(dipswitch_2_out),
    .Always(TAR_always_3[3]), .Loaded_A(_74typeflipflop_17_loaded_a[3]), .Loaded_B(TAR_loadB_3[3]),
    .Reset(reset_3_out));
  _74TypeFlipFlop _74typeflipflop_15 (
    .CLK(and_17_out), .Data(and_42_out[2]), .Load_A(not_2_out), .Load_B(dipswitch_2_out),
    .Always(TAR_always_3[2]), .Loaded_A(_74typeflipflop_17_loaded_a[2]), .Loaded_B(TAR_loadB_3[2]),
    .Reset(reset_3_out));
  _74TypeFlipFlop _74typeflipflop_16 (
    .CLK(and_17_out), .Data(and_42_out[1]), .Load_A(not_2_out), .Load_B(dipswitch_2_out),
    .Always(TAR_always_3[1]), .Loaded_A(_74typeflipflop_17_loaded_a[1]), .Loaded_B(TAR_loadB_3[1]),
    .Reset(reset_3_out));
  _74TypeFlipFlop _74typeflipflop_17 (
    .CLK(and_17_out), .Data(and_42_out[0]), .Load_A(not_2_out), .Load_B(dipswitch_2_out),
    .Always(TAR_always_3[0]), .Loaded_A(_74typeflipflop_17_loaded_a[0]), .Loaded_B(TAR_loadB_3[0]),
    .Reset(reset_3_out));
  _74TypeFlipFlop _74typeflipflop_18 (
    .CLK(clk), .Data(driver_8_out[7]), .Load_A(1'b0), .Load_B(1'b0), .Always(_74typeflipflop_25_always[7]),
    .Loaded_A(_74typeflipflop_18_loaded_a), .Loaded_B(_74typeflipflop_18_loaded_b), .Reset(reset_4_out));
  _74TypeFlipFlop _74typeflipflop_19 (
    .CLK(clk), .Data(driver_8_out[6]), .Load_A(1'b0), .Load_B(1'b0), .Always(_74typeflipflop_25_always[6]),
    .Loaded_A(_74typeflipflop_19_loaded_a), .Loaded_B(_74typeflipflop_19_loaded_b), .Reset(reset_4_out));
  _74TypeFlipFlop _74typeflipflop_20 (
    .CLK(clk), .Data(driver_8_out[5]), .Load_A(1'b0), .Load_B(1'b0), .Always(_74typeflipflop_25_always[5]),
    .Loaded_A(_74typeflipflop_20_loaded_a), .Loaded_B(_74typeflipflop_20_loaded_b), .Reset(reset_4_out));
  _74TypeFlipFlop _74typeflipflop_21 (
    .CLK(clk), .Data(driver_8_out[4]), .Load_A(1'b0), .Load_B(1'b0), .Always(_74typeflipflop_25_always[4]),
    .Loaded_A(_74typeflipflop_21_loaded_a), .Loaded_B(_74typeflipflop_21_loaded_b), .Reset(reset_4_out));
  _74TypeFlipFlop _74typeflipflop_22 (
    .CLK(clk), .Data(driver_8_out[3]), .Load_A(1'b0), .Load_B(1'b0), .Always(_74typeflipflop_25_always[3]),
    .Loaded_A(_74typeflipflop_22_loaded_a), .Loaded_B(_74typeflipflop_22_loaded_b), .Reset(reset_4_out));
  _74TypeFlipFlop _74typeflipflop_23 (
    .CLK(clk), .Data(driver_8_out[2]), .Load_A(1'b0), .Load_B(1'b0), .Always(_74typeflipflop_25_always[2]),
    .Loaded_A(_74typeflipflop_23_loaded_a), .Loaded_B(_74typeflipflop_23_loaded_b), .Reset(reset_4_out));
  _74TypeFlipFlop _74typeflipflop_24 (
    .CLK(clk), .Data(driver_8_out[1]), .Load_A(1'b0), .Load_B(1'b0), .Always(_74typeflipflop_25_always[1]),
    .Loaded_A(_74typeflipflop_24_loaded_a), .Loaded_B(_74typeflipflop_24_loaded_b), .Reset(reset_4_out));
  _74TypeFlipFlop _74typeflipflop_25 (
    .CLK(clk), .Data(driver_8_out[0]), .Load_A(1'b0), .Load_B(1'b0), .Always(_74typeflipflop_25_always[0]),
    .Loaded_A(_74typeflipflop_25_loaded_a), .Loaded_B(_74typeflipflop_25_loaded_b), .Reset(reset_4_out));
  not not_5 (not_5_out, and_229_out);
  not not_6 (not_6_out, OPCODE_read[2]);
  not not_7 (not_7_out, not_6_out);
  and and_18 (and_18_out, and_21_out, not_7_out);
  and and_19 (and_42_out[0], not_13_out, and_18_out);
  and and_20 (and_20_out, not_9_out, OPCODE_read[0]);
  and and_21 (and_21_out, OPCODE_read[0], OPCODE_read[1]);
  and and_22 (and_22_out, and_20_out, not_7_out);
  and and_23 (and_42_out[1], not_13_out, and_22_out);
  ROM #(.AddrBits(8), .isProgramMemory("true"), .Bits(32)) Program_Memory (
    .A(_74typeflipflop_25_always), .sel(1'b1), .D(Program_Memory_d));
  and and_24 (and_24_out, OPCODE_read[1], not_8_out);
  and and_25 (and_25_out, and_24_out, not_7_out);
  and and_26 (and_42_out[2], not_13_out, and_25_out);
  and and_27 (and_27_out, not_9_out, not_8_out);
  and and_28 (and_28_out, and_27_out, not_7_out);
  and and_29 (and_42_out[3], not_13_out, and_28_out);
  assign OPCODE_read = Program_Memory_d & {32{clk}};  // And and_30, 32 bits wide
  not not_8 (not_8_out, OPCODE_read[0]);
  not not_9 (not_9_out, OPCODE_read[1]);
  not not_10 (not_10_out, OPCODE_read[2]);
  and and_31 (and_31_out, OPCODE_read[0], OPCODE_read[1]);
  and and_32 (and_32_out, and_37_out, not_10_out);
  and and_33 (and_33_out, and_31_out, not_10_out);
  and and_34 (and_42_out[5], not_13_out, and_32_out);
  and and_35 (and_42_out[4], not_13_out, and_33_out);
  and and_36 (and_36_out, OPCODE_read[1], not_11_out);
  and and_37 (and_37_out, not_12_out, OPCODE_read[0]);
  and and_38 (and_38_out, and_36_out, not_10_out);
  and and_39 (and_42_out[6], not_13_out, and_38_out);
  and and_40 (and_40_out, not_12_out, not_11_out);
  and and_41 (and_41_out, and_40_out, not_10_out);
  and and_42 (and_42_out[7], not_13_out, and_41_out);
  not not_11 (not_11_out, OPCODE_read[0]);
  not not_12 (not_12_out, OPCODE_read[1]);
  not not_13 (not_13_out, and_229_out);
  not not_14 (not_14_out, OPCODE_read[10]);
  not not_15 (not_15_out, not_14_out);
  and and_43 (and_43_out, OPCODE_read[9], OPCODE_read[8]);
  and and_44 (and_44_out, and_43_out, not_15_out);
  and and_45 (and_45_out, not_23_out, and_44_out);
  and and_46 (and_46_out, not_17_out, OPCODE_read[9]);
  and and_47 (and_47_out, and_46_out, not_15_out);
  and and_48 (and_48_out, not_23_out, and_47_out);
  Delay #(.Bits(8)) delay_1 (.in(_74typeflipflop_17_loaded_a), .out(delay_1_out));
  and and_49 (and_49_out, OPCODE_read[8], not_16_out);
  and and_50 (and_50_out, and_54_out, not_15_out);
  and and_51 (and_51_out, and_49_out, not_15_out);
  and and_52 (and_52_out, not_23_out, and_50_out);
  and and_53 (and_53_out, not_23_out, and_51_out);
  and and_54 (and_54_out, not_17_out, not_16_out);
  not not_16 (not_16_out, OPCODE_read[9]);
  not not_17 (not_17_out, OPCODE_read[8]);
  and and_55 (and_55_out, not_18_out, not_19_out);
  not not_18 (not_18_out, OPCODE_read[29]);
  not not_19 (not_19_out, OPCODE_read[28]);
  and and_56 (and_56_out, not_19_out, OPCODE_read[29]);
  not not_20 (not_20_out, OPCODE_read[10]);
  and and_57 (and_57_out, and_60_out, not_20_out);
  and and_58 (and_58_out, not_23_out, and_57_out);
  and and_59 (and_59_out, not_22_out, OPCODE_read[9]);
  and and_60 (and_60_out, OPCODE_read[9], OPCODE_read[8]);
  and and_61 (and_61_out, and_59_out, not_20_out);
  and and_62 (and_62_out, not_23_out, and_61_out);
  and and_63 (and_63_out, OPCODE_read[8], not_21_out);
  and and_64 (and_64_out, and_63_out, not_20_out);
  and and_65 (and_65_out, not_23_out, and_64_out);
  and and_66 (and_66_out, not_22_out, not_21_out);
  and and_67 (and_67_out, and_66_out, not_20_out);
  and and_68 (and_68_out, not_23_out, and_67_out);
  not not_21 (not_21_out, OPCODE_read[9]);
  not not_22 (not_22_out, OPCODE_read[8]);
  not not_23 (not_23_out, OPCODE_read[30]);
  not not_24 (not_24_out, OPCODE_read[18]);
  not not_25 (not_25_out, not_24_out);
  and and_69 (and_69_out, and_72_out, not_25_out);
  and and_70 (and_70_out, not_31_out, and_69_out);
  and and_71 (and_71_out, not_27_out, OPCODE_read[17]);
  and and_72 (and_72_out, OPCODE_read[17], OPCODE_read[16]);
  and and_73 (and_73_out, and_71_out, not_25_out);
  and and_74 (and_74_out, not_31_out, and_73_out);
  and and_75 (and_75_out, OPCODE_read[16], not_26_out);
  and and_76 (and_76_out, and_75_out, not_25_out);
  and and_77 (and_77_out, not_31_out, and_76_out);
  and and_78 (and_78_out, not_27_out, not_26_out);
  and and_79 (and_79_out, and_78_out, not_25_out);
  and and_80 (and_80_out, not_31_out, and_79_out);
  not not_26 (not_26_out, OPCODE_read[17]);
  not not_27 (not_27_out, OPCODE_read[16]);
  not not_28 (not_28_out, OPCODE_read[18]);
  and and_81 (and_81_out, OPCODE_read[17], OPCODE_read[16]);
  and and_82 (and_82_out, and_87_out, not_28_out);
  and and_83 (and_83_out, and_81_out, not_28_out);
  and and_84 (and_84_out, not_31_out, and_82_out);
  and and_85 (and_85_out, not_31_out, and_83_out);
  and and_86 (and_86_out, OPCODE_read[16], not_29_out);
  and and_87 (and_87_out, not_30_out, OPCODE_read[17]);
  and and_88 (and_88_out, and_86_out, not_28_out);
  and and_89 (and_89_out, not_31_out, and_88_out);
  and and_90 (and_90_out, not_30_out, not_29_out);
  and and_91 (and_91_out, and_90_out, not_28_out);
  and and_92 (and_92_out, not_31_out, and_91_out);
  not not_29 (not_29_out, OPCODE_read[17]);
  not not_30 (not_30_out, OPCODE_read[16]);
  not not_31 (not_31_out, OPCODE_read[31]);
  Reset #(.invertOutput("false")) reset_5 (.out(reset_5_out));
  Reset #(.invertOutput("false")) reset_6 (.out(reset_6_out));
  Reset #(.invertOutput("false")) reset_7 (.out(reset_7_out));
  Reset #(.invertOutput("false")) reset_8 (.out(reset_8_out));
  Reset #(.invertOutput("false")) reset_9 (.out(reset_9_out));
  Reset #(.invertOutput("false")) reset_10 (.out(reset_10_out));
  // NotConnected on notconnected_4_out
  ROM #(.AddrBits(8), .Bits(8)) rom_1 (.A(notconnected_4_out), .sel(1'b1), .D(rom_1_d));
  _74TypeFlipFlop _74typeflipflop_26 (
    .CLK(delay_1_out[0]), .Data(_74typeflipflop_9_loaded_a[7]), .Load_A(and_92_out), .Load_B(and_68_out),
    .Always(_74typeflipflop_33_always[7]), .Loaded_A(_74typeflipflop_33_loaded_a[7]),
    .Loaded_B(_74typeflipflop_26_loaded_b[7]), .Reset(reset_5_out));
  _74TypeFlipFlop _74typeflipflop_27 (
    .CLK(delay_1_out[0]), .Data(_74typeflipflop_9_loaded_a[6]), .Load_A(and_92_out), .Load_B(and_68_out),
    .Always(_74typeflipflop_33_always[6]), .Loaded_A(_74typeflipflop_33_loaded_a[6]),
    .Loaded_B(_74typeflipflop_26_loaded_b[6]), .Reset(reset_5_out));
  _74TypeFlipFlop _74typeflipflop_28 (
    .CLK(delay_1_out[0]), .Data(_74typeflipflop_9_loaded_a[5]), .Load_A(and_92_out), .Load_B(and_68_out),
    .Always(_74typeflipflop_33_always[5]), .Loaded_A(_74typeflipflop_33_loaded_a[5]),
    .Loaded_B(_74typeflipflop_26_loaded_b[5]), .Reset(reset_5_out));
  _74TypeFlipFlop _74typeflipflop_29 (
    .CLK(delay_1_out[0]), .Data(_74typeflipflop_9_loaded_a[4]), .Load_A(and_92_out), .Load_B(and_68_out),
    .Always(_74typeflipflop_33_always[4]), .Loaded_A(_74typeflipflop_33_loaded_a[4]),
    .Loaded_B(_74typeflipflop_26_loaded_b[4]), .Reset(reset_5_out));
  _74TypeFlipFlop _74typeflipflop_30 (
    .CLK(delay_1_out[0]), .Data(_74typeflipflop_9_loaded_a[3]), .Load_A(and_92_out), .Load_B(and_68_out),
    .Always(_74typeflipflop_33_always[3]), .Loaded_A(_74typeflipflop_33_loaded_a[3]),
    .Loaded_B(_74typeflipflop_26_loaded_b[3]), .Reset(reset_5_out));
  _74TypeFlipFlop _74typeflipflop_31 (
    .CLK(delay_1_out[0]), .Data(_74typeflipflop_9_loaded_a[2]), .Load_A(and_92_out), .Load_B(and_68_out),
    .Always(_74typeflipflop_33_always[2]), .Loaded_A(_74typeflipflop_33_loaded_a[2]),
    .Loaded_B(_74typeflipflop_26_loaded_b[2]), .Reset(reset_5_out));
  _74TypeFlipFlop _74typeflipflop_32 (
    .CLK(delay_1_out[0]), .Data(_74typeflipflop_9_loaded_a[1]), .Load_A(and_92_out), .Load_B(and_68_out),
    .Always(_74typeflipflop_33_always[1]), .Loaded_A(_74typeflipflop_33_loaded_a[1]),
    .Loaded_B(_74typeflipflop_26_loaded_b[1]), .Reset(reset_5_out));
  _74TypeFlipFlop _74typeflipflop_33 (
    .CLK(delay_1_out[0]), .Data(_74typeflipflop_9_loaded_a[0]), .Load_A(and_92_out), .Load_B(and_68_out),
    .Always(_74typeflipflop_33_always[0]), .Loaded_A(_74typeflipflop_33_loaded_a[0]),
    .Loaded_B(_74typeflipflop_26_loaded_b[0]), .Reset(reset_5_out));
  _74TypeFlipFlop _74typeflipflop_34 (
    .CLK(delay_1_out[1]), .Data(_74typeflipflop_9_loaded_a[7]), .Load_A(and_89_out), .Load_B(and_65_out),
    .Always(_74typeflipflop_34_always), .Loaded_A(_74typeflipflop_33_loaded_a[7]),
    .Loaded_B(_74typeflipflop_26_loaded_b[7]), .Reset(reset_6_out));
  _74TypeFlipFlop _74typeflipflop_35 (
    .CLK(delay_1_out[1]), .Data(_74typeflipflop_9_loaded_a[6]), .Load_A(and_89_out), .Load_B(and_65_out),
    .Always(_74typeflipflop_35_always), .Loaded_A(_74typeflipflop_33_loaded_a[6]),
    .Loaded_B(_74typeflipflop_26_loaded_b[6]), .Reset(reset_6_out));
  _74TypeFlipFlop _74typeflipflop_36 (
    .CLK(delay_1_out[1]), .Data(_74typeflipflop_9_loaded_a[5]), .Load_A(and_89_out), .Load_B(and_65_out),
    .Always(_74typeflipflop_36_always), .Loaded_A(_74typeflipflop_33_loaded_a[5]),
    .Loaded_B(_74typeflipflop_26_loaded_b[5]), .Reset(reset_6_out));
  _74TypeFlipFlop _74typeflipflop_37 (
    .CLK(delay_1_out[1]), .Data(_74typeflipflop_9_loaded_a[4]), .Load_A(and_89_out), .Load_B(and_65_out),
    .Always(_74typeflipflop_37_always), .Loaded_A(_74typeflipflop_33_loaded_a[4]),
    .Loaded_B(_74typeflipflop_26_loaded_b[4]), .Reset(reset_6_out));
  _74TypeFlipFlop _74typeflipflop_38 (
    .CLK(delay_1_out[1]), .Data(_74typeflipflop_9_loaded_a[3]), .Load_A(and_89_out), .Load_B(and_65_out),
    .Always(_74typeflipflop_38_always), .Loaded_A(_74typeflipflop_33_loaded_a[3]),
    .Loaded_B(_74typeflipflop_26_loaded_b[3]), .Reset(reset_6_out));
  _74TypeFlipFlop _74typeflipflop_39 (
    .CLK(delay_1_out[1]), .Data(_74typeflipflop_9_loaded_a[2]), .Load_A(and_89_out), .Load_B(and_65_out),
    .Always(_74typeflipflop_39_always), .Loaded_A(_74typeflipflop_33_loaded_a[2]),
    .Loaded_B(_74typeflipflop_26_loaded_b[2]), .Reset(reset_6_out));
  _74TypeFlipFlop _74typeflipflop_40 (
    .CLK(delay_1_out[1]), .Data(_74typeflipflop_9_loaded_a[1]), .Load_A(and_89_out), .Load_B(and_65_out),
    .Always(_74typeflipflop_40_always), .Loaded_A(_74typeflipflop_33_loaded_a[1]),
    .Loaded_B(_74typeflipflop_26_loaded_b[1]), .Reset(reset_6_out));
  _74TypeFlipFlop _74typeflipflop_41 (
    .CLK(delay_1_out[1]), .Data(_74typeflipflop_9_loaded_a[0]), .Load_A(and_89_out), .Load_B(and_65_out),
    .Always(_74typeflipflop_41_always), .Loaded_A(_74typeflipflop_33_loaded_a[0]),
    .Loaded_B(_74typeflipflop_26_loaded_b[0]), .Reset(reset_6_out));
  _74TypeFlipFlop _74typeflipflop_42 (
    .CLK(delay_1_out[2]), .Data(_74typeflipflop_9_loaded_a[7]), .Load_A(and_84_out), .Load_B(and_62_out),
    .Always(_74typeflipflop_42_always), .Loaded_A(_74typeflipflop_33_loaded_a[7]),
    .Loaded_B(_74typeflipflop_26_loaded_b[7]), .Reset(reset_7_out));
  _74TypeFlipFlop _74typeflipflop_43 (
    .CLK(delay_1_out[2]), .Data(_74typeflipflop_9_loaded_a[6]), .Load_A(and_84_out), .Load_B(and_62_out),
    .Always(_74typeflipflop_43_always), .Loaded_A(_74typeflipflop_33_loaded_a[6]),
    .Loaded_B(_74typeflipflop_26_loaded_b[6]), .Reset(reset_7_out));
  _74TypeFlipFlop _74typeflipflop_44 (
    .CLK(delay_1_out[2]), .Data(_74typeflipflop_9_loaded_a[5]), .Load_A(and_84_out), .Load_B(and_62_out),
    .Always(_74typeflipflop_44_always), .Loaded_A(_74typeflipflop_33_loaded_a[5]),
    .Loaded_B(_74typeflipflop_26_loaded_b[5]), .Reset(reset_7_out));
  _74TypeFlipFlop _74typeflipflop_45 (
    .CLK(delay_1_out[2]), .Data(_74typeflipflop_9_loaded_a[4]), .Load_A(and_84_out), .Load_B(and_62_out),
    .Always(_74typeflipflop_45_always), .Loaded_A(_74typeflipflop_33_loaded_a[4]),
    .Loaded_B(_74typeflipflop_26_loaded_b[4]), .Reset(reset_7_out));
  _74TypeFlipFlop _74typeflipflop_46 (
    .CLK(delay_1_out[2]), .Data(_74typeflipflop_9_loaded_a[3]), .Load_A(and_84_out), .Load_B(and_62_out),
    .Always(_74typeflipflop_46_always), .Loaded_A(_74typeflipflop_33_loaded_a[3]),
    .Loaded_B(_74typeflipflop_26_loaded_b[3]), .Reset(reset_7_out));
  _74TypeFlipFlop _74typeflipflop_47 (
    .CLK(delay_1_out[2]), .Data(_74typeflipflop_9_loaded_a[2]), .Load_A(and_84_out), .Load_B(and_62_out),
    .Always(_74typeflipflop_47_always), .Loaded_A(_74typeflipflop_33_loaded_a[2]),
    .Loaded_B(_74typeflipflop_26_loaded_b[2]), .Reset(reset_7_out));
  _74TypeFlipFlop _74typeflipflop_48 (
    .CLK(delay_1_out[2]), .Data(_74typeflipflop_9_loaded_a[1]), .Load_A(and_84_out), .Load_B(and_62_out),
    .Always(_74typeflipflop_48_always), .Loaded_A(_74typeflipflop_33_loaded_a[1]),
    .Loaded_B(_74typeflipflop_26_loaded_b[1]), .Reset(reset_7_out));
  _74TypeFlipFlop _74typeflipflop_49 (
    .CLK(delay_1_out[2]), .Data(_74typeflipflop_9_loaded_a[0]), .Load_A(and_84_out), .Load_B(and_62_out),
    .Always(_74typeflipflop_49_always), .Loaded_A(_74typeflipflop_33_loaded_a[0]),
    .Loaded_B(_74typeflipflop_26_loaded_b[0]), .Reset(reset_7_out));
  _74TypeFlipFlop _74typeflipflop_50 (
    .CLK(delay_1_out[3]), .Data(_74typeflipflop_9_loaded_a[7]), .Load_A(and_85_out), .Load_B(and_58_out),
    .Always(_74typeflipflop_50_always), .Loaded_A(_74typeflipflop_33_loaded_a[7]),
    .Loaded_B(_74typeflipflop_26_loaded_b[7]), .Reset(reset_8_out));
  _74TypeFlipFlop _74typeflipflop_51 (
    .CLK(delay_1_out[3]), .Data(_74typeflipflop_9_loaded_a[6]), .Load_A(and_85_out), .Load_B(and_58_out),
    .Always(_74typeflipflop_51_always), .Loaded_A(_74typeflipflop_33_loaded_a[6]),
    .Loaded_B(_74typeflipflop_26_loaded_b[6]), .Reset(reset_8_out));
  _74TypeFlipFlop _74typeflipflop_52 (
    .CLK(delay_1_out[3]), .Data(_74typeflipflop_9_loaded_a[5]), .Load_A(and_85_out), .Load_B(and_58_out),
    .Always(_74typeflipflop_52_always), .Loaded_A(_74typeflipflop_33_loaded_a[5]),
    .Loaded_B(_74typeflipflop_26_loaded_b[5]), .Reset(reset_8_out));
  _74TypeFlipFlop _74typeflipflop_53 (
    .CLK(delay_1_out[3]), .Data(_74typeflipflop_9_loaded_a[4]), .Load_A(and_85_out), .Load_B(and_58_out),
    .Always(_74typeflipflop_53_always), .Loaded_A(_74typeflipflop_33_loaded_a[4]),
    .Loaded_B(_74typeflipflop_26_loaded_b[4]), .Reset(reset_8_out));
  _74TypeFlipFlop _74typeflipflop_54 (
    .CLK(delay_1_out[3]), .Data(_74typeflipflop_9_loaded_a[3]), .Load_A(and_85_out), .Load_B(and_58_out),
    .Always(_74typeflipflop_54_always), .Loaded_A(_74typeflipflop_33_loaded_a[3]),
    .Loaded_B(_74typeflipflop_26_loaded_b[3]), .Reset(reset_8_out));
  _74TypeFlipFlop _74typeflipflop_55 (
    .CLK(delay_1_out[3]), .Data(_74typeflipflop_9_loaded_a[2]), .Load_A(and_85_out), .Load_B(and_58_out),
    .Always(_74typeflipflop_55_always), .Loaded_A(_74typeflipflop_33_loaded_a[2]),
    .Loaded_B(_74typeflipflop_26_loaded_b[2]), .Reset(reset_8_out));
  _74TypeFlipFlop _74typeflipflop_56 (
    .CLK(delay_1_out[3]), .Data(_74typeflipflop_9_loaded_a[1]), .Load_A(and_85_out), .Load_B(and_58_out),
    .Always(_74typeflipflop_56_always), .Loaded_A(_74typeflipflop_33_loaded_a[1]),
    .Loaded_B(_74typeflipflop_26_loaded_b[1]), .Reset(reset_8_out));
  _74TypeFlipFlop _74typeflipflop_57 (
    .CLK(delay_1_out[3]), .Data(_74typeflipflop_9_loaded_a[0]), .Load_A(and_85_out), .Load_B(and_58_out),
    .Always(_74typeflipflop_57_always), .Loaded_A(_74typeflipflop_33_loaded_a[0]),
    .Loaded_B(_74typeflipflop_26_loaded_b[0]), .Reset(reset_8_out));
  _74TypeFlipFlop _74typeflipflop_58 (
    .CLK(delay_1_out[4]), .Data(_74typeflipflop_9_loaded_a[7]), .Load_A(and_80_out), .Load_B(and_52_out),
    .Always(_74typeflipflop_58_always), .Loaded_A(_74typeflipflop_33_loaded_a[7]),
    .Loaded_B(_74typeflipflop_26_loaded_b[7]), .Reset(reset_9_out));
  _74TypeFlipFlop _74typeflipflop_59 (
    .CLK(delay_1_out[4]), .Data(_74typeflipflop_9_loaded_a[6]), .Load_A(and_80_out), .Load_B(and_52_out),
    .Always(_74typeflipflop_59_always), .Loaded_A(_74typeflipflop_33_loaded_a[6]),
    .Loaded_B(_74typeflipflop_26_loaded_b[6]), .Reset(reset_9_out));
  _74TypeFlipFlop _74typeflipflop_60 (
    .CLK(delay_1_out[4]), .Data(_74typeflipflop_9_loaded_a[5]), .Load_A(and_80_out), .Load_B(and_52_out),
    .Always(_74typeflipflop_60_always), .Loaded_A(_74typeflipflop_33_loaded_a[5]),
    .Loaded_B(_74typeflipflop_26_loaded_b[5]), .Reset(reset_9_out));
  _74TypeFlipFlop _74typeflipflop_61 (
    .CLK(delay_1_out[4]), .Data(_74typeflipflop_9_loaded_a[4]), .Load_A(and_80_out), .Load_B(and_52_out),
    .Always(_74typeflipflop_61_always), .Loaded_A(_74typeflipflop_33_loaded_a[4]),
    .Loaded_B(_74typeflipflop_26_loaded_b[4]), .Reset(reset_9_out));
  _74TypeFlipFlop _74typeflipflop_62 (
    .CLK(delay_1_out[4]), .Data(_74typeflipflop_9_loaded_a[3]), .Load_A(and_80_out), .Load_B(and_52_out),
    .Always(_74typeflipflop_62_always), .Loaded_A(_74typeflipflop_33_loaded_a[3]),
    .Loaded_B(_74typeflipflop_26_loaded_b[3]), .Reset(reset_9_out));
  _74TypeFlipFlop _74typeflipflop_63 (
    .CLK(delay_1_out[4]), .Data(_74typeflipflop_9_loaded_a[2]), .Load_A(and_80_out), .Load_B(and_52_out),
    .Always(_74typeflipflop_63_always), .Loaded_A(_74typeflipflop_33_loaded_a[2]),
    .Loaded_B(_74typeflipflop_26_loaded_b[2]), .Reset(reset_9_out));
  _74TypeFlipFlop _74typeflipflop_64 (
    .CLK(delay_1_out[4]), .Data(_74typeflipflop_9_loaded_a[1]), .Load_A(and_80_out), .Load_B(and_52_out),
    .Always(_74typeflipflop_64_always), .Loaded_A(_74typeflipflop_33_loaded_a[1]),
    .Loaded_B(_74typeflipflop_26_loaded_b[1]), .Reset(reset_9_out));
  _74TypeFlipFlop _74typeflipflop_65 (
    .CLK(delay_1_out[4]), .Data(_74typeflipflop_9_loaded_a[0]), .Load_A(and_80_out), .Load_B(and_52_out),
    .Always(_74typeflipflop_65_always), .Loaded_A(_74typeflipflop_33_loaded_a[0]),
    .Loaded_B(_74typeflipflop_26_loaded_b[0]), .Reset(reset_9_out));
  _74TypeFlipFlop _74typeflipflop_66 (
    .CLK(delay_1_out[5]), .Data(_74typeflipflop_9_loaded_a[7]), .Load_A(and_77_out), .Load_B(and_53_out),
    .Always(_74typeflipflop_66_always), .Loaded_A(_74typeflipflop_33_loaded_a[7]),
    .Loaded_B(_74typeflipflop_26_loaded_b[7]), .Reset(reset_10_out));
  _74TypeFlipFlop _74typeflipflop_67 (
    .CLK(delay_1_out[5]), .Data(_74typeflipflop_9_loaded_a[6]), .Load_A(and_77_out), .Load_B(and_53_out),
    .Always(_74typeflipflop_67_always), .Loaded_A(_74typeflipflop_33_loaded_a[6]),
    .Loaded_B(_74typeflipflop_26_loaded_b[6]), .Reset(reset_10_out));
  _74TypeFlipFlop _74typeflipflop_68 (
    .CLK(delay_1_out[5]), .Data(_74typeflipflop_9_loaded_a[5]), .Load_A(and_77_out), .Load_B(and_53_out),
    .Always(_74typeflipflop_68_always), .Loaded_A(_74typeflipflop_33_loaded_a[5]),
    .Loaded_B(_74typeflipflop_26_loaded_b[5]), .Reset(reset_10_out));
  _74TypeFlipFlop _74typeflipflop_69 (
    .CLK(delay_1_out[5]), .Data(_74typeflipflop_9_loaded_a[4]), .Load_A(and_77_out), .Load_B(and_53_out),
    .Always(_74typeflipflop_69_always), .Loaded_A(_74typeflipflop_33_loaded_a[4]),
    .Loaded_B(_74typeflipflop_26_loaded_b[4]), .Reset(reset_10_out));
  _74TypeFlipFlop _74typeflipflop_70 (
    .CLK(delay_1_out[5]), .Data(_74typeflipflop_9_loaded_a[3]), .Load_A(and_77_out), .Load_B(and_53_out),
    .Always(_74typeflipflop_70_always), .Loaded_A(_74typeflipflop_33_loaded_a[3]),
    .Loaded_B(_74typeflipflop_26_loaded_b[3]), .Reset(reset_10_out));
  _74TypeFlipFlop _74typeflipflop_71 (
    .CLK(delay_1_out[5]), .Data(_74typeflipflop_9_loaded_a[2]), .Load_A(and_77_out), .Load_B(and_53_out),
    .Always(_74typeflipflop_71_always), .Loaded_A(_74typeflipflop_33_loaded_a[2]),
    .Loaded_B(_74typeflipflop_26_loaded_b[2]), .Reset(reset_10_out));
  _74TypeFlipFlop _74typeflipflop_72 (
    .CLK(delay_1_out[5]), .Data(_74typeflipflop_9_loaded_a[1]), .Load_A(and_77_out), .Load_B(and_53_out),
    .Always(_74typeflipflop_72_always), .Loaded_A(_74typeflipflop_33_loaded_a[1]),
    .Loaded_B(_74typeflipflop_26_loaded_b[1]), .Reset(reset_10_out));
  _74TypeFlipFlop _74typeflipflop_73 (
    .CLK(delay_1_out[5]), .Data(_74typeflipflop_9_loaded_a[0]), .Load_A(and_77_out), .Load_B(and_53_out),
    .Always(_74typeflipflop_73_always), .Loaded_A(_74typeflipflop_33_loaded_a[0]),
    .Loaded_B(_74typeflipflop_26_loaded_b[0]), .Reset(reset_10_out));
  assign _74typeflipflop_26_loaded_b[0] = OPCODE_read[30] ? OPCODE_read[8] : 1'bz;  // Driver driver_17
  assign _74typeflipflop_26_loaded_b[1] = OPCODE_read[30] ? OPCODE_read[9] : 1'bz;  // Driver driver_18
  assign _74typeflipflop_33_loaded_a[0] = OPCODE_read[31] ? OPCODE_read[16] : 1'bz;  // Driver driver_19
  assign _74typeflipflop_33_loaded_a[1] = OPCODE_read[31] ? OPCODE_read[17] : 1'bz;  // Driver driver_20
  assign _74typeflipflop_26_loaded_b[0] = and_48_out ? rom_1_d[0] : 1'bz;  // Driver driver_21
  assign _74typeflipflop_33_loaded_a[0] = and_74_out ? rom_1_d[0] : 1'bz;  // Driver driver_22
  assign _74typeflipflop_26_loaded_b[2] = OPCODE_read[30] ? OPCODE_read[10] : 1'bz;  // Driver driver_23
  assign _74typeflipflop_26_loaded_b[3] = OPCODE_read[30] ? OPCODE_read[11] : 1'bz;  // Driver driver_24
  assign _74typeflipflop_33_loaded_a[2] = OPCODE_read[31] ? OPCODE_read[18] : 1'bz;  // Driver driver_25
  assign _74typeflipflop_33_loaded_a[3] = OPCODE_read[31] ? OPCODE_read[19] : 1'bz;  // Driver driver_26
  assign _74typeflipflop_26_loaded_b[1] = and_48_out ? rom_1_d[1] : 1'bz;  // Driver driver_27
  assign _74typeflipflop_26_loaded_b[2] = and_48_out ? rom_1_d[2] : 1'bz;  // Driver driver_28
  assign _74typeflipflop_33_loaded_a[1] = and_74_out ? rom_1_d[1] : 1'bz;  // Driver driver_29
  assign _74typeflipflop_33_loaded_a[2] = and_74_out ? rom_1_d[2] : 1'bz;  // Driver driver_30
  assign _74typeflipflop_26_loaded_b[4] = OPCODE_read[30] ? OPCODE_read[12] : 1'bz;  // Driver driver_31
  assign _74typeflipflop_26_loaded_b[5] = OPCODE_read[30] ? OPCODE_read[13] : 1'bz;  // Driver driver_32
  assign _74typeflipflop_33_loaded_a[4] = OPCODE_read[31] ? OPCODE_read[20] : 1'bz;  // Driver driver_33
  assign _74typeflipflop_33_loaded_a[5] = OPCODE_read[31] ? OPCODE_read[21] : 1'bz;  // Driver driver_34
  assign _74typeflipflop_26_loaded_b[3] = and_48_out ? rom_1_d[3] : 1'bz;  // Driver driver_35
  assign _74typeflipflop_26_loaded_b[4] = and_48_out ? rom_1_d[4] : 1'bz;  // Driver driver_36
  assign _74typeflipflop_33_loaded_a[3] = and_74_out ? rom_1_d[3] : 1'bz;  // Driver driver_37
  assign _74typeflipflop_33_loaded_a[4] = and_74_out ? rom_1_d[4] : 1'bz;  // Driver driver_38
  assign _74typeflipflop_26_loaded_b[6] = OPCODE_read[30] ? OPCODE_read[14] : 1'bz;  // Driver driver_39
  assign _74typeflipflop_26_loaded_b[7] = OPCODE_read[30] ? OPCODE_read[15] : 1'bz;  // Driver driver_40
  assign _74typeflipflop_33_loaded_a[6] = OPCODE_read[31] ? OPCODE_read[22] : 1'bz;  // Driver driver_41
  assign _74typeflipflop_33_loaded_a[7] = OPCODE_read[31] ? OPCODE_read[23] : 1'bz;  // Driver driver_42
  assign _74typeflipflop_26_loaded_b[5] = and_48_out ? rom_1_d[5] : 1'bz;  // Driver driver_43
  assign _74typeflipflop_26_loaded_b[6] = and_48_out ? rom_1_d[6] : 1'bz;  // Driver driver_44
  assign _74typeflipflop_33_loaded_a[5] = and_74_out ? rom_1_d[5] : 1'bz;  // Driver driver_45
  assign _74typeflipflop_33_loaded_a[6] = and_74_out ? rom_1_d[6] : 1'bz;  // Driver driver_46
  assign _74typeflipflop_26_loaded_b[7] = and_48_out ? rom_1_d[7] : 1'bz;  // Driver driver_47
  assign _74typeflipflop_33_loaded_a[7] = and_74_out ? rom_1_d[7] : 1'bz;  // Driver driver_48
  LED led_1 (.in(_74typeflipflop_33_always[2]));
  LED led_2 (.in(_74typeflipflop_33_always[3]));
  LED led_3 (.in(_74typeflipflop_33_always[6]));
  LED led_4 (.in(_74typeflipflop_33_always[7]));
  LED led_5 (.in(_74typeflipflop_33_always[0]));
  LED led_6 (.in(_74typeflipflop_33_always[1]));
  LED led_7 (.in(_74typeflipflop_33_always[4]));
  LED led_8 (.in(_74typeflipflop_33_always[5]));
  // NotConnected on nothing
  xor xor_17 (xor_17_out, _74typeflipflop_26_loaded_b[7], 1'b1);
  xor xor_18 (xor_18_out, _74typeflipflop_26_loaded_b[6], 1'b1);
  xor xor_19 (xor_19_out, _74typeflipflop_26_loaded_b[5], 1'b1);
  xor xor_20 (xor_20_out, 1'b1, _74typeflipflop_26_loaded_b[4]);
  xor xor_21 (xor_21_out, 1'b1, _74typeflipflop_26_loaded_b[3]);
  xor xor_22 (xor_22_out, 1'b1, _74typeflipflop_26_loaded_b[2]);
  xor xor_23 (xor_23_out, 1'b1, _74typeflipflop_26_loaded_b[1]);
  xor xor_24 (xor_24_out, 1'b1, _74typeflipflop_26_loaded_b[0]);
  and and_93 (and_93_out, xor_17_out, _74typeflipflop_33_loaded_a[7]);
  xor xor_25 (xor_25_out, xor_17_out, _74typeflipflop_33_loaded_a[7]);
  and and_94 (and_94_out, xor_18_out, _74typeflipflop_33_loaded_a[6]);
  xor xor_26 (xor_26_out, xor_18_out, _74typeflipflop_33_loaded_a[6]);
  and and_95 (and_95_out, xor_19_out, _74typeflipflop_33_loaded_a[5]);
  xor xor_27 (xor_27_out, xor_19_out, _74typeflipflop_33_loaded_a[5]);
  and and_96 (and_96_out, xor_20_out, _74typeflipflop_33_loaded_a[4]);
  xor xor_28 (xor_28_out, xor_20_out, _74typeflipflop_33_loaded_a[4]);
  and and_97 (and_97_out, xor_21_out, _74typeflipflop_33_loaded_a[3]);
  xor xor_29 (xor_29_out, xor_21_out, _74typeflipflop_33_loaded_a[3]);
  and and_98 (and_98_out, xor_22_out, _74typeflipflop_33_loaded_a[2]);
  xor xor_30 (xor_30_out, xor_22_out, _74typeflipflop_33_loaded_a[2]);
  and and_99 (and_99_out, xor_23_out, _74typeflipflop_33_loaded_a[1]);
  xor xor_31 (xor_31_out, xor_23_out, _74typeflipflop_33_loaded_a[1]);
  and and_100 (and_100_out, xor_24_out, _74typeflipflop_33_loaded_a[0]);
  xor xor_32 (xor_32_out, xor_24_out, _74typeflipflop_33_loaded_a[0]);
  xor xor_33 (xor_33_out, _74typeflipflop_26_loaded_b[7], and_222_out);
  xor xor_34 (xor_34_out, _74typeflipflop_26_loaded_b[6], and_222_out);
  xor xor_35 (xor_35_out, _74typeflipflop_26_loaded_b[5], and_222_out);
  xor xor_36 (xor_36_out, and_222_out, _74typeflipflop_26_loaded_b[4]);
  xor xor_37 (xor_37_out, and_222_out, _74typeflipflop_26_loaded_b[3]);
  xor xor_38 (xor_38_out, and_222_out, _74typeflipflop_26_loaded_b[2]);
  xor xor_39 (xor_39_out, and_222_out, _74typeflipflop_26_loaded_b[1]);
  xor xor_40 (xor_40_out, and_222_out, _74typeflipflop_26_loaded_b[0]);
  and and_101 (and_156_out[0], _74typeflipflop_26_loaded_b[0], _74typeflipflop_33_loaded_a[0]);
  and and_102 (and_156_out[1], _74typeflipflop_26_loaded_b[1], _74typeflipflop_33_loaded_a[1]);
  nand nand_1 (nand_8_out[0], _74typeflipflop_26_loaded_b[0], _74typeflipflop_33_loaded_a[0]);
  nand nand_2 (nand_8_out[1], _74typeflipflop_26_loaded_b[1], _74typeflipflop_33_loaded_a[1]);
  or or_10 (or_21_out[0], _74typeflipflop_26_loaded_b[0], _74typeflipflop_33_loaded_a[0]);
  or or_11 (or_21_out[1], _74typeflipflop_26_loaded_b[1], _74typeflipflop_33_loaded_a[1]);
  nor nor_1 (nor_8_out[0], _74typeflipflop_26_loaded_b[0], _74typeflipflop_33_loaded_a[0]);
  nor nor_2 (nor_8_out[1], _74typeflipflop_26_loaded_b[1], _74typeflipflop_33_loaded_a[1]);
  xor xor_41 (xor_56_out[0], _74typeflipflop_26_loaded_b[0], _74typeflipflop_33_loaded_a[0]);
  xor xor_42 (xor_56_out[1], _74typeflipflop_26_loaded_b[1], _74typeflipflop_33_loaded_a[1]);
  and and_103 (and_103_out, xor_33_out, _74typeflipflop_33_loaded_a[7]);
  xor xor_43 (xor_43_out, xor_33_out, _74typeflipflop_33_loaded_a[7]);
  and and_104 (and_104_out, xor_34_out, _74typeflipflop_33_loaded_a[6]);
  xor xor_44 (xor_44_out, xor_34_out, _74typeflipflop_33_loaded_a[6]);
  and and_105 (and_105_out, xor_35_out, _74typeflipflop_33_loaded_a[5]);
  xor xor_45 (xor_45_out, xor_35_out, _74typeflipflop_33_loaded_a[5]);
  and and_106 (and_106_out, xor_36_out, _74typeflipflop_33_loaded_a[4]);
  xor xor_46 (xor_46_out, xor_36_out, _74typeflipflop_33_loaded_a[4]);
  and and_107 (and_107_out, xor_37_out, _74typeflipflop_33_loaded_a[3]);
  xor xor_47 (xor_47_out, xor_37_out, _74typeflipflop_33_loaded_a[3]);
  and and_108 (and_108_out, xor_38_out, _74typeflipflop_33_loaded_a[2]);
  xor xor_48 (xor_48_out, xor_38_out, _74typeflipflop_33_loaded_a[2]);
  and and_109 (and_109_out, xor_39_out, _74typeflipflop_33_loaded_a[1]);
  xor xor_49 (xor_49_out, xor_39_out, _74typeflipflop_33_loaded_a[1]);
  and and_110 (and_110_out, xor_40_out, _74typeflipflop_33_loaded_a[0]);
  xor xor_50 (xor_50_out, xor_40_out, _74typeflipflop_33_loaded_a[0]);
  and and_111 (and_156_out[2], _74typeflipflop_26_loaded_b[2], _74typeflipflop_33_loaded_a[2]);
  nand nand_3 (nand_8_out[2], _74typeflipflop_26_loaded_b[2], _74typeflipflop_33_loaded_a[2]);
  or or_12 (or_21_out[2], _74typeflipflop_26_loaded_b[2], _74typeflipflop_33_loaded_a[2]);
  nor nor_3 (nor_8_out[2], _74typeflipflop_26_loaded_b[2], _74typeflipflop_33_loaded_a[2]);
  xor xor_51 (xor_56_out[2], _74typeflipflop_26_loaded_b[2], _74typeflipflop_33_loaded_a[2]);
  and and_112 (and_112_out, or_31_out, xor_28_out);
  and and_113 (and_113_out, xor_27_out, xor_26_out);
  and and_114 (and_114_out, and_95_out, xor_27_out);
  and and_115 (and_115_out, xor_26_out, xor_25_out);
  and and_116 (and_116_out, xor_25_out, xor_26_out);
  and and_117 (and_117_out, and_94_out, xor_25_out);
  and and_118 (and_118_out, xor_26_out, xor_27_out);
  and and_119 (and_119_out, xor_28_out, or_31_out);
  and and_120 (and_120_out, xor_27_out, xor_26_out);
  and and_121 (and_121_out, and_95_out, xor_26_out);
  and and_122 (and_122_out, xor_28_out, xor_27_out);
  and and_123 (and_123_out, xor_27_out, and_96_out);
  and and_124 (and_124_out, xor_28_out, or_31_out);
  and and_125 (and_125_out, 1'b1, xor_32_out);
  and and_126 (and_126_out, xor_31_out, xor_30_out);
  and and_127 (and_127_out, and_99_out, xor_31_out);
  and and_128 (and_128_out, xor_30_out, xor_29_out);
  and and_129 (and_129_out, xor_29_out, xor_30_out);
  and and_130 (and_130_out, and_98_out, xor_29_out);
  and and_131 (and_131_out, xor_30_out, xor_31_out);
  and and_132 (and_132_out, xor_32_out, 1'b1);
  and and_133 (and_133_out, xor_31_out, xor_30_out);
  and and_134 (and_134_out, and_99_out, xor_30_out);
  and and_135 (and_135_out, xor_32_out, xor_31_out);
  and and_136 (and_136_out, xor_31_out, and_100_out);
  and and_137 (and_137_out, xor_32_out, 1'b1);
  and and_138 (and_156_out[3], _74typeflipflop_26_loaded_b[3], _74typeflipflop_33_loaded_a[3]);
  nand nand_4 (nand_8_out[3], _74typeflipflop_26_loaded_b[3], _74typeflipflop_33_loaded_a[3]);
  or or_13 (or_21_out[3], _74typeflipflop_26_loaded_b[3], _74typeflipflop_33_loaded_a[3]);
  nor nor_4 (nor_8_out[3], _74typeflipflop_26_loaded_b[3], _74typeflipflop_33_loaded_a[3]);
  xor xor_52 (xor_56_out[3], _74typeflipflop_26_loaded_b[3], _74typeflipflop_33_loaded_a[3]);
  and and_139 (and_139_out, and_112_out, and_113_out);
  and and_140 (and_140_out, and_114_out, and_115_out);
  and and_141 (and_141_out, and_116_out, and_95_out);
  and and_142 (and_142_out, and_118_out, and_119_out);
  and and_143 (and_143_out, and_120_out, and_96_out);
  and and_144 (and_144_out, and_122_out, or_31_out);
  and and_145 (and_145_out, and_125_out, and_126_out);
  and and_146 (and_146_out, and_127_out, and_128_out);
  and and_147 (and_147_out, and_129_out, and_99_out);
  and and_148 (and_148_out, and_131_out, and_132_out);
  and and_149 (and_149_out, and_133_out, and_100_out);
  and and_150 (and_150_out, and_135_out, 1'b1);
  and and_151 (and_156_out[4], _74typeflipflop_26_loaded_b[4], _74typeflipflop_33_loaded_a[4]);
  and and_152 (and_156_out[5], _74typeflipflop_26_loaded_b[5], _74typeflipflop_33_loaded_a[5]);
  nand nand_5 (nand_8_out[4], _74typeflipflop_26_loaded_b[4], _74typeflipflop_33_loaded_a[4]);
  nand nand_6 (nand_8_out[5], _74typeflipflop_26_loaded_b[5], _74typeflipflop_33_loaded_a[5]);
  or or_14 (or_21_out[4], _74typeflipflop_26_loaded_b[4], _74typeflipflop_33_loaded_a[4]);
  or or_15 (or_21_out[5], _74typeflipflop_26_loaded_b[5], _74typeflipflop_33_loaded_a[5]);
  nor nor_5 (nor_8_out[4], _74typeflipflop_26_loaded_b[4], _74typeflipflop_33_loaded_a[4]);
  nor nor_6 (nor_8_out[5], _74typeflipflop_26_loaded_b[5], _74typeflipflop_33_loaded_a[5]);
  xor xor_53 (xor_56_out[4], _74typeflipflop_26_loaded_b[4], _74typeflipflop_33_loaded_a[4]);
  xor xor_54 (xor_56_out[5], _74typeflipflop_26_loaded_b[5], _74typeflipflop_33_loaded_a[5]);
  or or_16 (or_16_out, and_124_out, and_96_out);
  or or_17 (or_17_out, and_137_out, and_100_out);
  and and_153 (and_156_out[6], _74typeflipflop_26_loaded_b[6], _74typeflipflop_33_loaded_a[6]);
  nand nand_7 (nand_8_out[6], _74typeflipflop_26_loaded_b[6], _74typeflipflop_33_loaded_a[6]);
  or or_18 (or_21_out[6], _74typeflipflop_26_loaded_b[6], _74typeflipflop_33_loaded_a[6]);
  nor nor_7 (nor_8_out[6], _74typeflipflop_26_loaded_b[6], _74typeflipflop_33_loaded_a[6]);
  xor xor_55 (xor_56_out[6], _74typeflipflop_26_loaded_b[6], _74typeflipflop_33_loaded_a[6]);
  and and_154 (and_154_out, and_139_out, xor_25_out);
  or or_19 (or_19_out, and_144_out, and_123_out);
  and and_155 (and_155_out, and_145_out, xor_29_out);
  or or_20 (or_20_out, and_150_out, and_136_out);
  and and_156 (and_156_out[7], _74typeflipflop_26_loaded_b[7], _74typeflipflop_33_loaded_a[7]);
  nand nand_8 (nand_8_out[7], _74typeflipflop_26_loaded_b[7], _74typeflipflop_33_loaded_a[7]);
  or or_21 (or_21_out[7], _74typeflipflop_26_loaded_b[7], _74typeflipflop_33_loaded_a[7]);
  nor nor_8 (nor_8_out[7], _74typeflipflop_26_loaded_b[7], _74typeflipflop_33_loaded_a[7]);
  xor xor_56 (xor_56_out[7], _74typeflipflop_26_loaded_b[7], _74typeflipflop_33_loaded_a[7]);
  or or_22 (or_22_out, and_142_out, and_143_out);
  or or_23 (or_23_out, and_121_out, and_94_out);
  or or_24 (or_24_out, and_148_out, and_149_out);
  or or_25 (or_25_out, and_134_out, and_98_out);
  or or_26 (or_26_out, and_141_out, and_117_out);
  or or_27 (or_27_out, or_35_out, and_93_out);
  or or_28 (or_28_out, or_22_out, or_23_out);
  or or_29 (or_29_out, or_19_out, and_95_out);
  or or_30 (or_30_out, and_147_out, and_130_out);
  or or_31 (or_31_out, or_37_out, and_97_out);
  or or_32 (or_32_out, or_24_out, or_25_out);
  or or_33 (or_33_out, or_20_out, and_99_out);
  assign driver_80_out[0] = and_223_out ? and_156_out[0] : 1'bz;  // Driver driver_49
  assign driver_80_out[1] = and_223_out ? and_156_out[1] : 1'bz;  // Driver driver_50
  assign driver_80_out[0] = and_224_out ? nand_8_out[0] : 1'bz;  // Driver driver_51
  assign driver_80_out[1] = and_224_out ? nand_8_out[1] : 1'bz;  // Driver driver_52
  assign driver_80_out[0] = and_225_out ? or_21_out[0] : 1'bz;  // Driver driver_53
  assign driver_80_out[1] = and_225_out ? or_21_out[1] : 1'bz;  // Driver driver_54
  assign driver_80_out[0] = and_226_out ? nor_8_out[0] : 1'bz;  // Driver driver_55
  assign driver_80_out[1] = and_226_out ? nor_8_out[1] : 1'bz;  // Driver driver_56
  assign driver_80_out[0] = and_227_out ? xor_56_out[0] : 1'bz;  // Driver driver_57
  assign driver_80_out[1] = and_227_out ? xor_56_out[1] : 1'bz;  // Driver driver_58
  or or_34 (or_34_out, and_154_out, and_140_out);
  or or_35 (or_35_out, or_34_out, or_26_out);
  or or_36 (or_36_out, and_155_out, and_146_out);
  or or_37 (or_37_out, or_36_out, or_30_out);
  assign driver_80_out[2] = and_223_out ? and_156_out[2] : 1'bz;  // Driver driver_59
  assign driver_80_out[3] = and_223_out ? and_156_out[3] : 1'bz;  // Driver driver_60
  assign driver_80_out[2] = and_224_out ? nand_8_out[2] : 1'bz;  // Driver driver_61
  assign driver_80_out[3] = and_224_out ? nand_8_out[3] : 1'bz;  // Driver driver_62
  assign driver_80_out[2] = and_225_out ? or_21_out[2] : 1'bz;  // Driver driver_63
  assign driver_80_out[3] = and_225_out ? or_21_out[3] : 1'bz;  // Driver driver_64
  assign driver_80_out[2] = and_226_out ? nor_8_out[2] : 1'bz;  // Driver driver_65
  assign driver_80_out[3] = and_226_out ? nor_8_out[3] : 1'bz;  // Driver driver_66
  assign driver_80_out[2] = and_227_out ? xor_56_out[2] : 1'bz;  // Driver driver_67
  assign driver_80_out[3] = and_227_out ? xor_56_out[3] : 1'bz;  // Driver driver_68
  xor xor_57 (xor_57_out[7], xor_25_out, or_28_out);
  xor xor_58 (xor_57_out[6], xor_26_out, or_29_out);
  xor xor_59 (xor_57_out[5], xor_27_out, or_16_out);
  xor xor_60 (xor_57_out[4], or_31_out, xor_28_out);
  xor xor_61 (xor_57_out[3], xor_29_out, or_32_out);
  xor xor_62 (xor_57_out[2], xor_30_out, or_33_out);
  xor xor_63 (xor_57_out[1], xor_31_out, or_17_out);
  xor xor_64 (xor_57_out[0], 1'b1, xor_32_out);
  and and_157 (and_157_out, or_48_out, xor_46_out);
  and and_158 (and_158_out, xor_45_out, xor_44_out);
  and and_159 (and_159_out, and_105_out, xor_45_out);
  and and_160 (and_160_out, xor_44_out, xor_43_out);
  and and_161 (and_161_out, xor_43_out, xor_44_out);
  and and_162 (and_162_out, and_104_out, xor_43_out);
  and and_163 (and_163_out, xor_44_out, xor_45_out);
  and and_164 (and_164_out, xor_46_out, or_48_out);
  and and_165 (and_165_out, xor_45_out, xor_44_out);
  and and_166 (and_166_out, and_105_out, xor_44_out);
  and and_167 (and_167_out, xor_46_out, xor_45_out);
  and and_168 (and_168_out, xor_45_out, and_106_out);
  and and_169 (and_169_out, xor_46_out, or_48_out);
  and and_170 (and_170_out, and_222_out, xor_50_out);
  and and_171 (and_171_out, xor_49_out, xor_48_out);
  and and_172 (and_172_out, and_109_out, xor_49_out);
  and and_173 (and_173_out, xor_48_out, xor_47_out);
  and and_174 (and_174_out, xor_47_out, xor_48_out);
  and and_175 (and_175_out, and_108_out, xor_47_out);
  and and_176 (and_176_out, xor_48_out, xor_49_out);
  and and_177 (and_177_out, xor_50_out, and_222_out);
  and and_178 (and_178_out, xor_49_out, xor_48_out);
  and and_179 (and_179_out, and_109_out, xor_48_out);
  and and_180 (and_180_out, xor_50_out, xor_49_out);
  and and_181 (and_181_out, xor_49_out, and_110_out);
  and and_182 (and_182_out, xor_50_out, and_222_out);
  assign driver_80_out[4] = and_223_out ? and_156_out[4] : 1'bz;  // Driver driver_69
  assign driver_80_out[5] = and_223_out ? and_156_out[5] : 1'bz;  // Driver driver_70
  assign driver_80_out[4] = and_224_out ? nand_8_out[4] : 1'bz;  // Driver driver_71
  assign driver_80_out[5] = and_224_out ? nand_8_out[5] : 1'bz;  // Driver driver_72
  assign driver_80_out[4] = and_225_out ? or_21_out[4] : 1'bz;  // Driver driver_73
  assign driver_80_out[5] = and_225_out ? or_21_out[5] : 1'bz;  // Driver driver_74
  assign driver_80_out[4] = and_226_out ? nor_8_out[4] : 1'bz;  // Driver driver_75
  assign driver_80_out[5] = and_226_out ? nor_8_out[5] : 1'bz;  // Driver driver_76
  assign driver_80_out[4] = and_227_out ? xor_56_out[4] : 1'bz;  // Driver driver_77
  assign driver_80_out[5] = and_227_out ? xor_56_out[5] : 1'bz;  // Driver driver_78
  assign driver_80_out[6] = and_223_out ? and_156_out[6] : 1'bz;  // Driver driver_79
  assign driver_80_out[7] = and_223_out ? and_156_out[7] : 1'bz;  // Driver driver_80
  assign driver_80_out[6] = and_224_out ? nand_8_out[6] : 1'bz;  // Driver driver_81
  assign driver_80_out[7] = and_224_out ? nand_8_out[7] : 1'bz;  // Driver driver_82
  assign driver_80_out[6] = and_225_out ? or_21_out[6] : 1'bz;  // Driver driver_83
  assign driver_80_out[7] = and_225_out ? or_21_out[7] : 1'bz;  // Driver driver_84
  assign driver_80_out[6] = and_226_out ? nor_8_out[6] : 1'bz;  // Driver driver_85
  assign driver_80_out[7] = and_226_out ? nor_8_out[7] : 1'bz;  // Driver driver_86
  assign driver_80_out[6] = and_227_out ? xor_56_out[6] : 1'bz;  // Driver driver_87
  assign driver_80_out[7] = and_227_out ? xor_56_out[7] : 1'bz;  // Driver driver_88
  and and_183 (and_183_out, and_157_out, and_158_out);
  and and_184 (and_184_out, and_159_out, and_160_out);
  and and_185 (and_185_out, and_161_out, and_105_out);
  and and_186 (and_186_out, and_163_out, and_164_out);
  and and_187 (and_187_out, and_165_out, and_106_out);
  and and_188 (and_188_out, and_167_out, or_48_out);
  or or_38 (or_38_out, and_169_out, and_106_out);
  and and_189 (and_189_out, and_170_out, and_171_out);
  and and_190 (and_190_out, and_172_out, and_173_out);
  and and_191 (and_191_out, and_174_out, and_109_out);
  and and_192 (and_192_out, and_176_out, and_177_out);
  and and_193 (and_193_out, and_178_out, and_110_out);
  and and_194 (and_194_out, and_180_out, and_222_out);
  or or_39 (or_39_out, and_182_out, and_110_out);
  and and_195 (and_195_out, and_183_out, xor_43_out);
  and and_196 (and_196_out, and_189_out, xor_47_out);
  or or_40 (or_40_out, and_186_out, and_187_out);
  or or_41 (or_41_out, and_166_out, and_104_out);
  or or_42 (or_42_out, and_188_out, and_168_out);
  or or_43 (or_43_out, and_192_out, and_193_out);
  or or_44 (or_44_out, and_179_out, and_108_out);
  or or_45 (or_45_out, and_194_out, and_181_out);
  or or_46 (or_46_out, or_51_out, and_103_out);
  or or_47 (or_47_out, or_42_out, and_105_out);
  or or_48 (or_48_out, or_54_out, and_107_out);
  or or_49 (or_49_out, or_45_out, and_109_out);
  or or_50 (or_50_out, and_185_out, and_162_out);
  or or_51 (or_51_out, or_56_out, or_50_out);
  or or_52 (or_52_out, or_40_out, or_41_out);
  or or_53 (or_53_out, and_191_out, and_175_out);
  or or_54 (or_54_out, or_57_out, or_53_out);
  or or_55 (or_55_out, or_43_out, or_44_out);
  or or_56 (or_56_out, and_195_out, and_184_out);
  xor xor_65 (xor_69_out[7], xor_43_out, or_52_out);
  xor xor_66 (xor_69_out[6], xor_44_out, or_47_out);
  xor xor_67 (xor_69_out[5], xor_45_out, or_38_out);
  xor xor_68 (xor_69_out[4], or_48_out, xor_46_out);
  or or_57 (or_57_out, and_196_out, and_190_out);
  xor xor_69 (xor_69_out[3], xor_47_out, or_55_out);
  xor xor_70 (xor_69_out[2], xor_48_out, or_49_out);
  xor xor_71 (xor_69_out[1], xor_49_out, or_39_out);
  xor xor_72 (xor_69_out[0], and_222_out, xor_50_out);
  not not_32 (not_32_out, OPCODE_read[26]);
  not not_33 (not_33_out, OPCODE_read[25]);
  not not_34 (not_34_out, OPCODE_read[25]);
  not not_35 (not_35_out, OPCODE_read[24]);
  and and_197 (and_197_out, not_35_out, not_33_out);
  and and_198 (and_198_out, OPCODE_read[24], not_33_out);
  and and_199 (and_199_out, not_35_out, OPCODE_read[25]);
  and and_200 (and_200_out, OPCODE_read[25], OPCODE_read[24]);
  not not_36 (not_36_out, OPCODE_read[26]);
  not not_37 (not_37_out, OPCODE_read[24]);
  and and_201 (and_201_out, not_37_out, not_34_out);
  and and_202 (and_202_out, OPCODE_read[24], not_34_out);
  and and_203 (and_203_out, not_37_out, OPCODE_read[25]);
  and and_204 (and_204_out, OPCODE_read[25], OPCODE_read[24]);
  not not_38 (not_38_out, not_32_out);
  and and_205 (and_205_out, and_197_out, not_36_out);
  and and_206 (and_206_out, and_198_out, not_36_out);
  and and_207 (and_207_out, and_199_out, not_36_out);
  and and_208 (and_208_out, and_200_out, not_36_out);
  and and_209 (and_209_out, and_201_out, not_38_out);
  and and_210 (and_210_out, and_202_out, not_38_out);
  and and_211 (and_211_out, and_203_out, not_38_out);
  // And and_212 has open pins: In_1=and_204_out, In_2=not_38_out, out=open
  or or_58 (or_58_out, xor_57_out[7], xor_57_out[6]);
  or or_59 (or_59_out, xor_57_out[5], xor_57_out[4]);
  or or_60 (or_60_out, xor_57_out[3], xor_57_out[2]);
  or or_61 (or_61_out, xor_57_out[1], xor_57_out[0]);
  not not_39 (not_39_out, OPCODE_read[26]);
  assign driver_80_out[0] = or_73_out ? xor_69_out[0] : 1'bz;  // Driver driver_89
  assign driver_80_out[1] = or_73_out ? xor_69_out[1] : 1'bz;  // Driver driver_90
  or or_62 (or_62_out, or_58_out, or_59_out);
  or or_63 (or_63_out, or_62_out, or_64_out);
  or or_64 (or_64_out, or_60_out, or_61_out);
  not not_40 (not_40_out, OPCODE_read[25]);
  not not_41 (not_41_out, OPCODE_read[24]);
  not not_42 (not_42_out, OPCODE_read[26]);
  not not_43 (not_43_out, OPCODE_read[25]);
  not not_44 (not_44_out, OPCODE_read[24]);
  not not_45 (not_45_out, not_39_out);
  assign driver_80_out[2] = or_73_out ? xor_69_out[2] : 1'bz;  // Driver driver_91
  assign driver_80_out[3] = or_73_out ? xor_69_out[3] : 1'bz;  // Driver driver_92
  and and_213 (and_213_out, not_41_out, not_40_out);
  and and_214 (and_214_out, OPCODE_read[24], not_40_out);
  and and_215 (and_215_out, not_41_out, OPCODE_read[25]);
  and and_216 (and_216_out, OPCODE_read[25], OPCODE_read[24]);
  and and_217 (and_217_out, not_44_out, not_43_out);
  and and_218 (and_218_out, OPCODE_read[24], not_43_out);
  and and_219 (and_219_out, not_44_out, OPCODE_read[25]);
  and and_220 (and_220_out, OPCODE_read[25], OPCODE_read[24]);
  assign driver_80_out[4] = or_73_out ? xor_69_out[4] : 1'bz;  // Driver driver_93
  assign driver_80_out[5] = or_73_out ? xor_69_out[5] : 1'bz;  // Driver driver_94
  and and_221 (and_221_out, and_213_out, not_42_out);
  and and_222 (and_222_out, and_214_out, not_42_out);
  and and_223 (and_223_out, and_215_out, not_42_out);
  and and_224 (and_224_out, and_216_out, not_42_out);
  and and_225 (and_225_out, and_217_out, not_45_out);
  and and_226 (and_226_out, and_218_out, not_45_out);
  and and_227 (and_227_out, and_219_out, not_45_out);
  // And and_228 has open pins: In_1=and_220_out, In_2=not_45_out, out=open
  assign driver_80_out[6] = or_73_out ? xor_69_out[6] : 1'bz;  // Driver driver_95
  assign driver_80_out[7] = or_73_out ? xor_69_out[7] : 1'bz;  // Driver driver_96
  or or_65 (or_65_out, and_210_out, or_66_out);
  or or_66 (or_66_out, and_209_out, and_205_out);
  or or_67 (or_67_out, and_207_out, and_209_out);
  or or_68 (or_68_out, and_208_out, and_210_out);
  or or_69 (or_69_out, or_71_out, and_211_out);
  or or_70 (or_70_out, or_72_out, or_69_out);
  or or_71 (or_71_out, and_231_out, and_232_out);
  and and_229 (and_229_out, and_56_out, or_70_out);
  and and_230 (and_230_out, or_65_out, not_46_out);
  not not_46 (not_46_out, or_63_out);
  and and_231 (and_231_out, or_63_out, and_206_out);
  and and_232 (and_232_out, or_67_out, not_47_out);
  not not_47 (not_47_out, xor_57_out[7]);
  and and_233 (and_233_out, xor_57_out[7], or_68_out);
  or or_72 (or_72_out, and_230_out, and_233_out);
  or or_73 (or_73_out, and_221_out, and_222_out);
  assign driver_104_out[0] = and_55_out ? driver_80_out[0] : 1'bz;  // Driver driver_97
  assign driver_104_out[1] = and_55_out ? driver_80_out[1] : 1'bz;  // Driver driver_98
  assign driver_104_out[2] = and_55_out ? driver_80_out[2] : 1'bz;  // Driver driver_99
  assign driver_104_out[3] = and_55_out ? driver_80_out[3] : 1'bz;  // Driver driver_100
  assign driver_104_out[4] = and_55_out ? driver_80_out[4] : 1'bz;  // Driver driver_101
  assign driver_104_out[5] = and_55_out ? driver_80_out[5] : 1'bz;  // Driver driver_102
  assign driver_104_out[6] = and_55_out ? driver_80_out[6] : 1'bz;  // Driver driver_103
  assign driver_104_out[7] = and_55_out ? driver_80_out[7] : 1'bz;  // Driver driver_104
  DipSwitch dipswitch_3 (.out(dipswitch_3_out));
  DipSwitch dipswitch_4 (.out(dipswitch_4_out));
  DipSwitch dipswitch_5 (.out(dipswitch_5_out));
  DipSwitch dipswitch_6 (.out(dipswitch_6_out));
  DipSwitch dipswitch_7 (.out(dipswitch_7_out));
  DipSwitch dipswitch_8 (.out(dipswitch_8_out));
  DipSwitch dipswitch_9 (.out(dipswitch_9_out));
  DipSwitch dipswitch_10 (.out(dipswitch_10_out));
  and and_234 (and_234_out, dipswitch_4_out, dipswitch_3_out);
  xor xor_73 (xor_73_out, dipswitch_3_out, dipswitch_4_out);
  and and_235 (and_235_out, dipswitch_6_out, dipswitch_5_out);
  xor xor_74 (xor_74_out, dipswitch_5_out, dipswitch_6_out);
  and and_236 (and_236_out, dipswitch_8_out, dipswitch_7_out);
  xor xor_75 (xor_75_out, dipswitch_7_out, dipswitch_8_out);
  and and_237 (and_237_out, dipswitch_10_out, dipswitch_9_out);
  xor xor_76 (xor_76_out, dipswitch_9_out, dipswitch_10_out);
  // Or or_74 has open pins: In_1=and_234_out, In_2=and_238_out, out=open
  and and_238 (and_238_out, xor_73_out, or_75_out);
  xor xor_77 (xor_77_out, xor_73_out, or_75_out);
  or or_75 (or_75_out, and_235_out, and_239_out);
  and and_239 (and_239_out, xor_74_out, or_76_out);
  xor xor_78 (xor_78_out, xor_74_out, or_76_out);
  or or_76 (or_76_out, and_236_out, and_240_out);
  and and_240 (and_240_out, xor_75_out, or_77_out);
  xor xor_79 (xor_79_out, xor_75_out, or_77_out);
  or or_77 (or_77_out, and_237_out, and_241_out);
  and and_241 (and_241_out, xor_76_out, 1'b0);
  xor xor_80 (xor_80_out, xor_76_out, 1'b0);
  // NotConnected on notconnected_6_out
  // NotConnected on notconnected_7_out
  // NotConnected on notconnected_8_out
  xor xor_81 (xor_81_out, notconnected_6_out[7], notconnected_7_out);
  xor xor_82 (xor_82_out, notconnected_6_out[6], notconnected_7_out);
  xor xor_83 (xor_83_out, notconnected_6_out[5], notconnected_7_out);
  xor xor_84 (xor_84_out, notconnected_7_out, notconnected_6_out[4]);
  xor xor_85 (xor_85_out, notconnected_7_out, notconnected_6_out[3]);
  xor xor_86 (xor_86_out, notconnected_7_out, notconnected_6_out[2]);
  xor xor_87 (xor_87_out, notconnected_7_out, notconnected_6_out[1]);
  xor xor_88 (xor_88_out, notconnected_7_out, notconnected_6_out[0]);
  and and_242 (and_242_out, xor_81_out, notconnected_8_out[7]);
  xor xor_89 (xor_89_out, xor_81_out, notconnected_8_out[7]);
  and and_243 (and_243_out, xor_82_out, notconnected_8_out[6]);
  xor xor_90 (xor_90_out, xor_82_out, notconnected_8_out[6]);
  and and_244 (and_244_out, xor_83_out, notconnected_8_out[5]);
  xor xor_91 (xor_91_out, xor_83_out, notconnected_8_out[5]);
  and and_245 (and_245_out, xor_84_out, notconnected_8_out[4]);
  xor xor_92 (xor_92_out, xor_84_out, notconnected_8_out[4]);
  and and_246 (and_246_out, xor_85_out, notconnected_8_out[3]);
  xor xor_93 (xor_93_out, xor_85_out, notconnected_8_out[3]);
  and and_247 (and_247_out, xor_86_out, notconnected_8_out[2]);
  xor xor_94 (xor_94_out, xor_86_out, notconnected_8_out[2]);
  and and_248 (and_248_out, xor_87_out, notconnected_8_out[1]);
  xor xor_95 (xor_95_out, xor_87_out, notconnected_8_out[1]);
  and and_249 (and_249_out, xor_88_out, notconnected_8_out[0]);
  xor xor_96 (xor_96_out, xor_88_out, notconnected_8_out[0]);
  xor xor_97 (xor_97_out, B_0[7], and_323_out);
  xor xor_98 (xor_98_out, B_0[6], and_323_out);
  xor xor_99 (xor_99_out, B_0[5], and_323_out);
  xor xor_100 (xor_100_out, B_0[4], and_323_out);
  xor xor_101 (xor_101_out, B_0[3], and_323_out);
  xor xor_102 (xor_102_out, B_0[2], and_323_out);
  xor xor_103 (xor_103_out, B_0[1], and_323_out);
  xor xor_104 (xor_104_out, B_0[0], and_323_out);
  and and_250 (and_309_out[0], B_0[0], A_0[0]);
  nand nand_9 (nand_16_out[0], B_0[0], A_0[0]);
  or or_78 (or_95_out[0], B_0[0], A_0[0]);
  nor nor_9 (nor_16_out[0], B_0[0], A_0[0]);
  xor xor_105 (xor_124_out[0], B_0[0], A_0[0]);
  and and_251 (and_309_out[1], B_0[1], A_0[1]);
  nand nand_10 (nand_16_out[1], B_0[1], A_0[1]);
  or or_79 (or_95_out[1], B_0[1], A_0[1]);
  nor nor_10 (nor_16_out[1], B_0[1], A_0[1]);
  xor xor_106 (xor_124_out[1], B_0[1], A_0[1]);
  and and_252 (and_309_out[2], B_0[2], A_0[2]);
  nand nand_11 (nand_16_out[2], B_0[2], A_0[2]);
  or or_80 (or_95_out[2], B_0[2], A_0[2]);
  nor nor_11 (nor_16_out[2], B_0[2], A_0[2]);
  xor xor_107 (xor_124_out[2], B_0[2], A_0[2]);
  and and_253 (and_253_out, or_104_out, xor_92_out);
  and and_254 (and_254_out, xor_91_out, xor_90_out);
  and and_255 (and_255_out, and_244_out, xor_91_out);
  and and_256 (and_256_out, xor_90_out, xor_89_out);
  and and_257 (and_257_out, xor_89_out, xor_90_out);
  and and_258 (and_258_out, and_243_out, xor_89_out);
  and and_259 (and_259_out, xor_90_out, xor_91_out);
  and and_260 (and_260_out, xor_92_out, or_104_out);
  and and_261 (and_261_out, xor_91_out, xor_90_out);
  and and_262 (and_262_out, and_244_out, xor_90_out);
  and and_263 (and_263_out, xor_92_out, xor_91_out);
  and and_264 (and_264_out, xor_91_out, and_245_out);
  and and_265 (and_265_out, xor_92_out, or_104_out);
  and and_266 (and_266_out, notconnected_7_out, xor_96_out);
  and and_267 (and_267_out, xor_95_out, xor_94_out);
  and and_268 (and_268_out, and_248_out, xor_95_out);
  and and_269 (and_269_out, xor_94_out, xor_93_out);
  and and_270 (and_270_out, xor_93_out, xor_94_out);
  and and_271 (and_271_out, and_247_out, xor_93_out);
  and and_272 (and_272_out, xor_94_out, xor_95_out);
  and and_273 (and_273_out, xor_96_out, notconnected_7_out);
  and and_274 (and_274_out, xor_95_out, xor_94_out);
  and and_275 (and_275_out, and_248_out, xor_94_out);
  and and_276 (and_276_out, xor_96_out, xor_95_out);
  and and_277 (and_277_out, xor_95_out, and_249_out);
  and and_278 (and_278_out, xor_96_out, notconnected_7_out);
  and and_279 (and_309_out[3], B_0[3], A_0[3]);
  and and_280 (and_309_out[4], B_0[4], A_0[4]);
  nand nand_12 (nand_16_out[3], B_0[3], A_0[3]);
  nand nand_13 (nand_16_out[4], B_0[4], A_0[4]);
  or or_81 (or_95_out[3], B_0[3], A_0[3]);
  or or_82 (or_95_out[4], B_0[4], A_0[4]);
  nor nor_12 (nor_16_out[3], B_0[3], A_0[3]);
  nor nor_13 (nor_16_out[4], B_0[4], A_0[4]);
  xor xor_108 (xor_124_out[3], B_0[3], A_0[3]);
  xor xor_109 (xor_124_out[4], B_0[4], A_0[4]);
  and and_281 (and_309_out[5], B_0[5], A_0[5]);
  nand nand_14 (nand_16_out[5], B_0[5], A_0[5]);
  or or_83 (or_95_out[5], B_0[5], A_0[5]);
  nor nor_14 (nor_16_out[5], B_0[5], A_0[5]);
  xor xor_110 (xor_124_out[5], B_0[5], A_0[5]);
  and and_282 (and_282_out, and_253_out, and_254_out);
  and and_283 (and_283_out, and_255_out, and_256_out);
  and and_284 (and_284_out, and_257_out, and_244_out);
  and and_285 (and_285_out, and_259_out, and_260_out);
  and and_286 (and_286_out, and_261_out, and_245_out);
  and and_287 (and_287_out, and_263_out, or_104_out);
  or or_84 (or_84_out, and_265_out, and_245_out);
  and and_288 (and_288_out, and_266_out, and_267_out);
  and and_289 (and_289_out, and_268_out, and_269_out);
  and and_290 (and_290_out, and_270_out, and_248_out);
  and and_291 (and_291_out, and_272_out, and_273_out);
  and and_292 (and_292_out, and_274_out, and_249_out);
  and and_293 (and_293_out, and_276_out, notconnected_7_out);
  or or_85 (or_85_out, and_278_out, and_249_out);
  and and_294 (and_294_out, xor_97_out, A_0[7]);
  xor xor_111 (xor_111_out, A_0[7], xor_97_out);
  and and_295 (and_295_out, xor_98_out, A_0[6]);
  xor xor_112 (xor_112_out, A_0[6], xor_98_out);
  and and_296 (and_296_out, xor_99_out, A_0[5]);
  xor xor_113 (xor_113_out, A_0[5], xor_99_out);
  and and_297 (and_297_out, xor_100_out, A_0[4]);
  xor xor_114 (xor_114_out, A_0[4], xor_100_out);
  and and_298 (and_298_out, xor_101_out, A_0[3]);
  xor xor_115 (xor_115_out, A_0[3], xor_101_out);
  and and_299 (and_299_out, xor_102_out, A_0[2]);
  xor xor_116 (xor_116_out, A_0[2], xor_102_out);
  and and_300 (and_300_out, xor_103_out, A_0[1]);
  xor xor_117 (xor_117_out, A_0[1], xor_103_out);
  and and_301 (and_301_out, xor_104_out, A_0[0]);
  xor xor_118 (xor_118_out, A_0[0], xor_104_out);
  and and_302 (and_309_out[6], B_0[6], A_0[6]);
  nand nand_15 (nand_16_out[6], B_0[6], A_0[6]);
  or or_86 (or_95_out[6], B_0[6], A_0[6]);
  nor nor_15 (nor_16_out[6], B_0[6], A_0[6]);
  xor xor_119 (xor_124_out[6], B_0[6], A_0[6]);
  and and_303 (and_303_out, and_282_out, xor_89_out);
  and and_304 (and_304_out, and_288_out, xor_93_out);
  or or_87 (or_87_out, and_294_out, and_305_out);
  and and_305 (and_305_out, xor_111_out, or_88_out);
  xor xor_120 (xor_128_out[7], xor_111_out, or_88_out);
  or or_88 (or_88_out, and_295_out, and_306_out);
  and and_306 (and_306_out, xor_112_out, or_89_out);
  xor xor_121 (xor_128_out[6], xor_112_out, or_89_out);
  or or_89 (or_89_out, and_296_out, and_307_out);
  and and_307 (and_307_out, xor_113_out, or_90_out);
  xor xor_122 (xor_128_out[5], xor_113_out, or_90_out);
  or or_90 (or_90_out, and_297_out, and_308_out);
  and and_308 (and_308_out, xor_114_out, or_91_out);
  xor xor_123 (xor_128_out[4], xor_114_out, or_91_out);
  or or_91 (or_91_out, and_298_out, and_310_out);
  or or_92 (or_92_out, and_299_out, and_311_out);
  or or_93 (or_93_out, and_300_out, and_312_out);
  or or_94 (or_94_out, and_301_out, and_313_out);
  and and_309 (and_309_out[7], B_0[7], A_0[7]);
  nand nand_16 (nand_16_out[7], B_0[7], A_0[7]);
  or or_95 (or_95_out[7], B_0[7], A_0[7]);
  nor nor_16 (nor_16_out[7], B_0[7], A_0[7]);
  xor xor_124 (xor_124_out[7], B_0[7], A_0[7]);
  or or_96 (or_96_out, and_285_out, and_286_out);
  or or_97 (or_97_out, and_262_out, and_243_out);
  or or_98 (or_98_out, and_287_out, and_264_out);
  or or_99 (or_99_out, and_291_out, and_292_out);
  or or_100 (or_100_out, and_275_out, and_247_out);
  or or_101 (or_101_out, and_293_out, and_277_out);
  and and_310 (and_310_out, xor_115_out, or_92_out);
  xor xor_125 (xor_128_out[3], xor_115_out, or_92_out);
  and and_311 (and_311_out, xor_116_out, or_93_out);
  xor xor_126 (xor_128_out[2], xor_116_out, or_93_out);
  and and_312 (and_312_out, xor_117_out, or_94_out);
  xor xor_127 (xor_128_out[1], xor_117_out, or_94_out);
  and and_313 (and_313_out, xor_118_out, and_323_out);
  xor xor_128 (xor_128_out[0], xor_118_out, and_323_out);
  or or_102 (or_102_out, or_107_out, and_242_out);
  or or_103 (or_103_out, or_98_out, and_244_out);
  or or_104 (or_104_out, or_110_out, and_246_out);
  or or_105 (or_105_out, or_101_out, and_248_out);
  assign C_Arith[0] = and_324_out ? and_309_out[0] : 1'bz;  // Driver driver_105
  assign C_Arith[1] = and_324_out ? and_309_out[1] : 1'bz;  // Driver driver_106
  assign C_Arith[0] = and_325_out ? nand_16_out[0] : 1'bz;  // Driver driver_107
  assign C_Arith[1] = and_325_out ? nand_16_out[1] : 1'bz;  // Driver driver_108
  assign C_Arith[0] = and_326_out ? or_95_out[0] : 1'bz;  // Driver driver_109
  assign C_Arith[1] = and_326_out ? or_95_out[1] : 1'bz;  // Driver driver_110
  assign C_Arith[0] = and_327_out ? nor_16_out[0] : 1'bz;  // Driver driver_111
  assign C_Arith[1] = and_327_out ? nor_16_out[1] : 1'bz;  // Driver driver_112
  assign C_Arith[0] = and_328_out ? xor_124_out[0] : 1'bz;  // Driver driver_113
  assign C_Arith[1] = and_328_out ? xor_124_out[1] : 1'bz;  // Driver driver_114
  or or_106 (or_106_out, and_284_out, and_258_out);
  or or_107 (or_107_out, or_112_out, or_106_out);
  or or_108 (or_108_out, or_96_out, or_97_out);
  or or_109 (or_109_out, and_290_out, and_271_out);
  or or_110 (or_110_out, or_113_out, or_109_out);
  or or_111 (or_111_out, or_99_out, or_100_out);
  assign C_Arith[2] = and_324_out ? and_309_out[2] : 1'bz;  // Driver driver_115
  assign C_Arith[3] = and_324_out ? and_309_out[3] : 1'bz;  // Driver driver_116
  assign C_Arith[2] = and_325_out ? nand_16_out[2] : 1'bz;  // Driver driver_117
  assign C_Arith[3] = and_325_out ? nand_16_out[3] : 1'bz;  // Driver driver_118
  assign C_Arith[2] = and_326_out ? or_95_out[2] : 1'bz;  // Driver driver_119
  assign C_Arith[3] = and_326_out ? or_95_out[3] : 1'bz;  // Driver driver_120
  assign C_Arith[2] = and_327_out ? nor_16_out[2] : 1'bz;  // Driver driver_121
  assign C_Arith[3] = and_327_out ? nor_16_out[3] : 1'bz;  // Driver driver_122
  assign C_Arith[2] = and_328_out ? xor_124_out[2] : 1'bz;  // Driver driver_123
  assign C_Arith[3] = and_328_out ? xor_124_out[3] : 1'bz;  // Driver driver_124
  or or_112 (or_112_out, and_303_out, and_283_out);
  xor xor_129 (xor_129_out, xor_89_out, or_108_out);
  xor xor_130 (xor_130_out, xor_90_out, or_103_out);
  xor xor_131 (xor_131_out, xor_91_out, or_84_out);
  xor xor_132 (xor_132_out, or_104_out, xor_92_out);
  or or_113 (or_113_out, and_304_out, and_289_out);
  xor xor_133 (xor_133_out, xor_93_out, or_111_out);
  xor xor_134 (xor_134_out, xor_94_out, or_105_out);
  xor xor_135 (xor_135_out, xor_95_out, or_85_out);
  xor xor_136 (xor_136_out, notconnected_7_out, xor_96_out);
  assign C_Arith[4] = and_324_out ? and_309_out[4] : 1'bz;  // Driver driver_125
  assign C_Arith[5] = and_324_out ? and_309_out[5] : 1'bz;  // Driver driver_126
  assign C_Arith[4] = and_325_out ? nand_16_out[4] : 1'bz;  // Driver driver_127
  assign C_Arith[5] = and_325_out ? nand_16_out[5] : 1'bz;  // Driver driver_128
  assign C_Arith[4] = and_326_out ? or_95_out[4] : 1'bz;  // Driver driver_129
  assign C_Arith[5] = and_326_out ? or_95_out[5] : 1'bz;  // Driver driver_130
  assign C_Arith[4] = and_327_out ? nor_16_out[4] : 1'bz;  // Driver driver_131
  assign C_Arith[5] = and_327_out ? nor_16_out[5] : 1'bz;  // Driver driver_132
  assign C_Arith[4] = and_328_out ? xor_124_out[4] : 1'bz;  // Driver driver_133
  assign C_Arith[5] = and_328_out ? xor_124_out[5] : 1'bz;  // Driver driver_134
  assign C_Arith[6] = and_324_out ? and_309_out[6] : 1'bz;  // Driver driver_135
  assign C_Arith[7] = and_324_out ? and_309_out[7] : 1'bz;  // Driver driver_136
  assign C_Arith[6] = and_325_out ? nand_16_out[6] : 1'bz;  // Driver driver_137
  assign C_Arith[7] = and_325_out ? nand_16_out[7] : 1'bz;  // Driver driver_138
  assign C_Arith[6] = and_326_out ? or_95_out[6] : 1'bz;  // Driver driver_139
  assign C_Arith[7] = and_326_out ? or_95_out[7] : 1'bz;  // Driver driver_140
  assign C_Arith[6] = and_327_out ? nor_16_out[6] : 1'bz;  // Driver driver_141
  assign C_Arith[7] = and_327_out ? nor_16_out[7] : 1'bz;  // Driver driver_142
  assign C_Arith[6] = and_328_out ? xor_124_out[6] : 1'bz;  // Driver driver_143
  assign C_Arith[7] = and_328_out ? xor_124_out[7] : 1'bz;  // Driver driver_144
  not not_48 (not_48_out, C_2);
  assign C_Arith[0] = or_114_out ? xor_128_out[0] : 1'bz;  // Driver driver_145
  not not_49 (not_49_out, C_1);
  not not_50 (not_50_out, C_1);
  assign C_Arith[1] = or_114_out ? xor_128_out[1] : 1'bz;  // Driver driver_146
  assign C_Arith[2] = or_114_out ? xor_128_out[2] : 1'bz;  // Driver driver_147
  not not_51 (not_51_out, C_0);
  and and_314 (and_314_out, not_51_out, not_49_out);
  and and_315 (and_315_out, C_0, not_49_out);
  and and_316 (and_316_out, not_51_out, C_1);
  and and_317 (and_317_out, C_1, C_0);
  not not_52 (not_52_out, C_2);
  not not_53 (not_53_out, C_0);
  and and_318 (and_318_out, not_53_out, not_50_out);
  and and_319 (and_319_out, C_0, not_50_out);
  and and_320 (and_320_out, not_53_out, C_1);
  and and_321 (and_321_out, C_1, C_0);
  not not_54 (not_54_out, not_48_out);
  assign C_Arith[3] = or_114_out ? xor_128_out[3] : 1'bz;  // Driver driver_148
  assign C_Arith[4] = or_114_out ? xor_128_out[4] : 1'bz;  // Driver driver_149
  assign C_Arith[5] = or_114_out ? xor_128_out[5] : 1'bz;  // Driver driver_150
  assign C_Arith[6] = or_114_out ? xor_128_out[6] : 1'bz;  // Driver driver_151
  and and_322 (and_322_out, and_314_out, not_52_out);
  and and_323 (and_323_out, and_315_out, not_52_out);
  and and_324 (and_324_out, and_316_out, not_52_out);
  and and_325 (and_325_out, and_317_out, not_52_out);
  and and_326 (and_326_out, and_318_out, not_54_out);
  and and_327 (and_327_out, and_319_out, not_54_out);
  and and_328 (and_328_out, and_320_out, not_54_out);
  // And and_329 has open pins: In_1=and_321_out, In_2=not_54_out, out=open
  assign C_Arith[7] = or_114_out ? xor_128_out[7] : 1'bz;  // Driver driver_152
  or or_114 (or_114_out, and_322_out, and_323_out);
  // NotConnected on notconnected_9_out
  // NotConnected on notconnected_10_out
  // NotConnected on notconnected_11_out
  // NotConnected on notconnected_12_out
  DipSwitch dipswitch_11 (.out(dipswitch_11_out));
  DipSwitch dipswitch_12 (.out(dipswitch_12_out));
  DipSwitch dipswitch_13 (.out(dipswitch_13_out));
  // NotConnected on notconnected_13_out
  nand nand_17 (nand_17_out, nand_20_out, nand_18_out);
  nand nand_18 (nand_18_out, nand_17_out, dipswitch_11_out);
  nand nand_19 (nand_19_out, nand_18_out, dipswitch_11_out, nand_20_out);
  nand nand_20 (nand_20_out, nand_19_out, NormalRegTest[6]);
  nand nand_21 (nand_21_out, nand_24_out, nand_22_out);
  nand nand_22 (nand_22_out, nand_21_out, dipswitch_11_out);
  nand nand_23 (nand_23_out, nand_22_out, dipswitch_11_out, nand_24_out);
  nand nand_24 (nand_24_out, nand_23_out, NormalRegTest[4]);
  nand nand_25 (nand_25_out, nand_28_out, nand_26_out);
  nand nand_26 (nand_26_out, nand_25_out, dipswitch_11_out);
  nand nand_27 (nand_27_out, nand_26_out, dipswitch_11_out, nand_28_out);
  nand nand_28 (nand_28_out, nand_27_out, NormalRegTest[2]);
  nand nand_29 (nand_29_out, nand_32_out, nand_30_out);
  nand nand_30 (nand_30_out, nand_29_out, dipswitch_11_out);
  nand nand_31 (nand_31_out, nand_30_out, dipswitch_11_out, nand_32_out);
  nand nand_32 (nand_32_out, nand_31_out, NormalRegTest[0]);
  DipSwitch dipswitch_14 (.out(dipswitch_14_out));
  DipSwitch dipswitch_15 (.out(dipswitch_15_out));
  DipSwitch dipswitch_16 (.out(dipswitch_16_out));
  not not_55 (not_55_out, notconnected_11_out[7]);
  and and_330 (and_330_out, notconnected_9_out, notconnected_11_out[7]);
  not not_56 (not_56_out, notconnected_11_out[6]);
  and and_331 (and_331_out, notconnected_9_out, notconnected_11_out[6]);
  not not_57 (not_57_out, notconnected_11_out[5]);
  and and_332 (and_332_out, notconnected_9_out, notconnected_11_out[5]);
  not not_58 (not_58_out, notconnected_11_out[4]);
  and and_333 (and_333_out, notconnected_9_out, notconnected_11_out[4]);
  not not_59 (not_59_out, notconnected_11_out[3]);
  and and_334 (and_334_out, notconnected_9_out, notconnected_11_out[3]);
  not not_60 (not_60_out, notconnected_11_out[2]);
  and and_335 (and_335_out, notconnected_9_out, notconnected_11_out[2]);
  not not_61 (not_61_out, notconnected_11_out[1]);
  and and_336 (and_336_out, notconnected_9_out, notconnected_11_out[1]);
  not not_62 (not_62_out, notconnected_11_out[0]);
  and and_337 (and_337_out, notconnected_9_out, notconnected_11_out[0]);
  and and_338 (and_338_out, not_63_out, dipswitch_15_out);
  not not_63 (not_63_out, dipswitch_16_out);
  and and_339 (and_339_out, dipswitch_15_out, dipswitch_16_out);
  and and_340 (and_340_out, not_55_out, notconnected_9_out);
  and and_341 (and_341_out, not_56_out, notconnected_9_out);
  and and_342 (and_342_out, not_57_out, notconnected_9_out);
  and and_343 (and_343_out, not_58_out, notconnected_9_out);
  and and_344 (and_344_out, not_59_out, notconnected_9_out);
  and and_345 (and_345_out, not_60_out, notconnected_9_out);
  and and_346 (and_346_out, not_61_out, notconnected_9_out);
  and and_347 (and_347_out, not_62_out, notconnected_9_out);
  nand nand_33 (nand_33_out, nand_18_out, nand_34_out);
  nand nand_34 (nand_34_out, nand_33_out, nand_19_out);
  nand nand_35 (nand_35_out, nand_22_out, nand_36_out);
  nand nand_36 (nand_36_out, nand_35_out, nand_23_out);
  nand nand_37 (nand_37_out, nand_26_out, nand_38_out);
  nand nand_38 (nand_38_out, nand_37_out, nand_27_out);
  nand nand_39 (nand_39_out, nand_30_out, nand_40_out);
  nand nand_40 (nand_40_out, nand_39_out, nand_31_out);
  nor nor_17 (nor_17_out, and_340_out, nor_18_out);
  nor nor_18 (nor_18_out, nor_17_out, and_330_out);
  nor nor_19 (nor_19_out, and_341_out, nor_20_out);
  nor nor_20 (nor_20_out, nor_19_out, and_331_out);
  nor nor_21 (nor_21_out, and_342_out, nor_22_out);
  nor nor_22 (nor_22_out, nor_21_out, and_332_out);
  nor nor_23 (nor_23_out, and_343_out, nor_24_out);
  nor nor_24 (nor_24_out, nor_23_out, and_333_out);
  nor nor_25 (nor_25_out, and_344_out, nor_26_out);
  nor nor_26 (nor_26_out, nor_25_out, and_334_out);
  nor nor_27 (nor_27_out, and_345_out, nor_28_out);
  nor nor_28 (nor_28_out, nor_27_out, and_335_out);
  nor nor_29 (nor_29_out, and_346_out, nor_30_out);
  nor nor_30 (nor_30_out, nor_29_out, and_336_out);
  nor nor_31 (nor_31_out, and_347_out, nor_32_out);
  nor nor_32 (nor_32_out, nor_31_out, and_337_out);
  assign driver_153_out = dipswitch_12_out ? nand_33_out : 1'bz;  // Driver driver_153
  assign driver_154_out = dipswitch_13_out ? nand_33_out : 1'bz;  // Driver driver_154
  assign driver_155_out = dipswitch_12_out ? nand_35_out : 1'bz;  // Driver driver_155
  assign driver_156_out = dipswitch_13_out ? nand_35_out : 1'bz;  // Driver driver_156
  assign driver_157_out = dipswitch_12_out ? nand_37_out : 1'bz;  // Driver driver_157
  assign driver_158_out = dipswitch_13_out ? nand_37_out : 1'bz;  // Driver driver_158
  assign driver_159_out = dipswitch_12_out ? nand_39_out : 1'bz;  // Driver driver_159
  assign driver_160_out = dipswitch_13_out ? nand_39_out : 1'bz;  // Driver driver_160
  and and_348 (and_348_out, notconnected_12_out[7], notconnected_13_out[7]);
  xor xor_137 (xor_137_out, notconnected_13_out[7], notconnected_12_out[7]);
  and and_349 (and_349_out, notconnected_12_out[6], notconnected_13_out[6]);
  xor xor_138 (xor_138_out, notconnected_13_out[6], notconnected_12_out[6]);
  and and_350 (and_350_out, notconnected_12_out[5], notconnected_13_out[5]);
  xor xor_139 (xor_139_out, notconnected_13_out[5], notconnected_12_out[5]);
  and and_351 (and_351_out, notconnected_12_out[4], notconnected_13_out[4]);
  xor xor_140 (xor_140_out, notconnected_13_out[4], notconnected_12_out[4]);
  and and_352 (and_352_out, notconnected_12_out[3], notconnected_13_out[3]);
  xor xor_141 (xor_141_out, notconnected_13_out[3], notconnected_12_out[3]);
  and and_353 (and_353_out, notconnected_12_out[2], notconnected_13_out[2]);
  xor xor_142 (xor_142_out, notconnected_13_out[2], notconnected_12_out[2]);
  and and_354 (and_354_out, notconnected_12_out[1], notconnected_13_out[1]);
  xor xor_143 (xor_143_out, notconnected_13_out[1], notconnected_12_out[1]);
  and and_355 (and_355_out, notconnected_12_out[0], notconnected_13_out[0]);
  xor xor_144 (xor_144_out, notconnected_13_out[0], notconnected_12_out[0]);
  nor nor_33 (nor_33_out, and_338_out, nor_34_out);
  nor nor_34 (nor_34_out, nor_33_out, and_339_out);
  or or_115 (or_115_out, and_348_out, and_356_out);
  and and_356 (and_356_out, xor_137_out, or_116_out);
  xor xor_145 (xor_145_out, xor_137_out, or_116_out);
  or or_116 (or_116_out, and_349_out, and_357_out);
  and and_357 (and_357_out, xor_138_out, or_117_out);
  xor xor_146 (xor_146_out, xor_138_out, or_117_out);
  or or_117 (or_117_out, and_350_out, and_358_out);
  and and_358 (and_358_out, xor_139_out, or_118_out);
  xor xor_147 (xor_147_out, xor_139_out, or_118_out);
  or or_118 (or_118_out, and_351_out, and_359_out);
  and and_359 (and_359_out, xor_140_out, or_119_out);
  xor xor_148 (xor_148_out, xor_140_out, or_119_out);
  or or_119 (or_119_out, and_352_out, and_368_out);
  or or_120 (or_120_out, and_353_out, and_369_out);
  or or_121 (or_121_out, and_354_out, and_370_out);
  or or_122 (or_122_out, and_355_out, and_371_out);
  // NotConnected on notconnected_14_out
  Reset reset_11 ();  // open: out
  Reset reset_12 ();  // open: out
  and and_360 (and_360_out, nor_17_out, notconnected_10_out);
  Reset reset_13 ();  // open: out
  and and_361 (and_361_out, nor_19_out, notconnected_10_out);
  Reset reset_14 ();  // open: out
  and and_362 (and_362_out, nor_21_out, notconnected_10_out);
  Reset reset_15 ();  // open: out
  and and_363 (and_363_out, nor_23_out, notconnected_10_out);
  Reset reset_16 ();  // open: out
  and and_364 (and_364_out, nor_25_out, notconnected_10_out);
  Reset reset_17 ();  // open: out
  and and_365 (and_365_out, nor_27_out, notconnected_10_out);
  Reset reset_18 ();  // open: out
  and and_366 (and_366_out, nor_29_out, notconnected_10_out);
  Reset reset_19 ();  // open: out
  and and_367 (and_367_out, nor_31_out, notconnected_10_out);
  and and_368 (and_368_out, xor_141_out, or_120_out);
  xor xor_149 (xor_149_out, xor_141_out, or_120_out);
  and and_369 (and_369_out, xor_142_out, or_121_out);
  xor xor_150 (xor_150_out, xor_142_out, or_121_out);
  and and_370 (and_370_out, xor_143_out, or_122_out);
  xor xor_151 (xor_151_out, xor_143_out, or_122_out);
  and and_371 (and_371_out, xor_144_out, notconnected_14_out);
  xor xor_152 (xor_152_out, xor_144_out, notconnected_14_out);
  and and_372 (and_372_out, nor_33_out, dipswitch_14_out);
  nand nand_41 (nand_41_out, nand_44_out, nand_42_out);
  nand nand_42 (nand_42_out, nand_41_out, dipswitch_11_out);
  nand nand_43 (nand_43_out, nand_42_out, dipswitch_11_out, nand_44_out);
  nand nand_44 (nand_44_out, nand_43_out, NormalRegTest[7]);
  nand nand_45 (nand_45_out, nand_48_out, nand_46_out);
  nand nand_46 (nand_46_out, nand_45_out, dipswitch_11_out);
  nand nand_47 (nand_47_out, nand_46_out, dipswitch_11_out, nand_48_out);
  nand nand_48 (nand_48_out, nand_47_out, NormalRegTest[5]);
  nand nand_49 (nand_49_out, nand_52_out, nand_50_out);
  nand nand_50 (nand_50_out, nand_49_out, dipswitch_11_out);
  nand nand_51 (nand_51_out, nand_50_out, dipswitch_11_out, nand_52_out);
  nand nand_52 (nand_52_out, nand_51_out, NormalRegTest[3]);
  nand nand_53 (nand_53_out, nand_56_out, nand_54_out);
  nand nand_54 (nand_54_out, nand_53_out, dipswitch_11_out);
  nand nand_55 (nand_55_out, nand_54_out, dipswitch_11_out, nand_56_out);
  nand nand_56 (nand_56_out, nand_55_out, NormalRegTest[1]);
  nand nand_57 (nand_57_out, nand_42_out, nand_58_out);
  nand nand_58 (nand_58_out, nand_57_out, nand_43_out);
  nand nand_59 (nand_59_out, nand_46_out, nand_60_out);
  nand nand_60 (nand_60_out, nand_59_out, nand_47_out);
  nand nand_61 (nand_61_out, nand_50_out, nand_62_out);
  nand nand_62 (nand_62_out, nand_61_out, nand_51_out);
  nand nand_63 (nand_63_out, nand_54_out, nand_64_out);
  nand nand_64 (nand_64_out, nand_63_out, nand_55_out);
  assign driver_161_out = dipswitch_12_out ? nand_57_out : 1'bz;  // Driver driver_161
  assign driver_162_out = dipswitch_13_out ? nand_57_out : 1'bz;  // Driver driver_162
  assign driver_163_out = dipswitch_12_out ? nand_59_out : 1'bz;  // Driver driver_163
  assign driver_164_out = dipswitch_13_out ? nand_59_out : 1'bz;  // Driver driver_164
  assign driver_165_out = dipswitch_12_out ? nand_61_out : 1'bz;  // Driver driver_165
  assign driver_166_out = dipswitch_13_out ? nand_61_out : 1'bz;  // Driver driver_166
  assign driver_167_out = dipswitch_12_out ? nand_63_out : 1'bz;  // Driver driver_167
  assign driver_168_out = dipswitch_13_out ? nand_63_out : 1'bz;  // Driver driver_168
  // NotConnected on notconnected_15_out
  // NotConnected on notconnected_16_out
  // NotConnected on notconnected_17_out
  // NotConnected on notconnected_18_out
  and and_373 (and_373_out, notconnected_16_out[0], notconnected_16_out[0]);
  or or_123 (or_123_out, notconnected_17_out[0], notconnected_17_out[0]);
  xor xor_153 (xor_153_out, notconnected_18_out[0], notconnected_18_out[0]);
  and and_374 (and_374_out, notconnected_16_out[1], notconnected_16_out[1]);
  or or_124 (or_124_out, notconnected_17_out[1], notconnected_17_out[1]);
  xor xor_154 (xor_154_out, notconnected_18_out[1], notconnected_18_out[1]);
  not not_64 (not_64_out, notconnected_19_out);
  // NotConnected on notconnected_19_out
  and and_375 (and_375_out, notconnected_16_out[2], notconnected_16_out[2]);
  and and_376 (and_376_out, notconnected_16_out[3], notconnected_16_out[3]);
  or or_125 (or_125_out, notconnected_17_out[2], notconnected_17_out[2]);
  or or_126 (or_126_out, notconnected_17_out[3], notconnected_17_out[3]);
  xor xor_155 (xor_155_out, notconnected_18_out[2], notconnected_18_out[2]);
  xor xor_156 (xor_156_out, notconnected_18_out[3], notconnected_18_out[3]);
  // And and_377 has open pins: In_1=and_378_out, In_2=notconnected_15_out[7], out=open
  xor xor_157 (xor_157_out, notconnected_15_out[7], and_378_out);
  and and_378 (and_378_out, and_379_out, notconnected_15_out[6]);
  xor xor_158 (xor_158_out, notconnected_15_out[6], and_379_out);
  and and_379 (and_379_out, and_380_out, notconnected_15_out[5]);
  xor xor_159 (xor_159_out, notconnected_15_out[5], and_380_out);
  and and_380 (and_380_out, and_381_out, notconnected_15_out[4]);
  xor xor_160 (xor_160_out, notconnected_15_out[4], and_381_out);
  and and_381 (and_381_out, and_382_out, notconnected_15_out[3]);
  xor xor_161 (xor_161_out, notconnected_15_out[3], and_382_out);
  and and_382 (and_382_out, and_383_out, notconnected_15_out[2]);
  xor xor_162 (xor_162_out, notconnected_15_out[2], and_383_out);
  and and_383 (and_383_out, and_384_out, notconnected_15_out[1]);
  xor xor_163 (xor_163_out, notconnected_15_out[1], and_384_out);
  and and_384 (and_384_out, not_64_out, notconnected_15_out[0]);
  xor xor_164 (xor_164_out, notconnected_15_out[0], not_64_out);
  and and_385 (and_385_out, notconnected_16_out[4], notconnected_16_out[4]);
  or or_127 (or_127_out, notconnected_17_out[4], notconnected_17_out[4]);
  xor xor_165 (xor_165_out, notconnected_18_out[4], notconnected_18_out[4]);
  and and_386 (and_386_out, notconnected_16_out[5], notconnected_16_out[5]);
  or or_128 (or_128_out, notconnected_17_out[5], notconnected_17_out[5]);
  xor xor_166 (xor_166_out, notconnected_18_out[5], notconnected_18_out[5]);
  and and_387 (and_387_out, notconnected_16_out[6], notconnected_16_out[6]);
  and and_388 (and_388_out, notconnected_16_out[7], notconnected_16_out[7]);
  or or_129 (or_129_out, notconnected_17_out[6], notconnected_17_out[6]);
  or or_130 (or_130_out, notconnected_17_out[7], notconnected_17_out[7]);
  xor xor_167 (xor_167_out, notconnected_18_out[6], notconnected_18_out[6]);
  xor xor_168 (xor_168_out, notconnected_18_out[7], notconnected_18_out[7]);
  // NotConnected on notconnected_20_out
  // NotConnected on notconnected_21_out
  // NotConnected on notconnected_22_out
  // NotConnected on notconnected_23_out
  // NotConnected on notconnected_24_out
  // NotConnected on notconnected_25_out
  Button button_1 (.out(button_1_out));
  DipSwitch dipswitch_17 (.out(dipswitch_17_out));
  DipSwitch dipswitch_18 (.out(dipswitch_18_out));
  Reset #(.invertOutput("false")) reset_20 (.out(reset_20_out));
  and and_389 (and_389_out, notconnected_26_out, notconnected_20_out[0]);
  nand nand_65 (nand_65_out, notconnected_21_out[0], notconnected_21_out[0]);
  nor nor_35 (nor_35_out, notconnected_22_out[0], notconnected_22_out[0]);
  not not_65 (not_65_out, notconnected_25_out);
  and and_390 (and_390_out, notconnected_26_out, notconnected_20_out[1]);
  and and_391 (and_391_out, notconnected_26_out, notconnected_20_out[2]);
  nand nand_66 (nand_66_out, notconnected_21_out[1], notconnected_21_out[1]);
  nand nand_67 (nand_67_out, notconnected_21_out[2], notconnected_21_out[2]);
  nor nor_36 (nor_36_out, notconnected_22_out[1], notconnected_22_out[1]);
  nor nor_37 (nor_37_out, notconnected_22_out[2], notconnected_22_out[2]);
  not not_66 (not_66_out, notconnected_24_out);
  not not_67 (not_67_out, notconnected_23_out);
  not not_68 (not_68_out, notconnected_25_out);
  not not_69 (not_69_out, notconnected_24_out);
  not not_70 (not_70_out, notconnected_23_out);
  not not_71 (not_71_out, not_65_out);
  // NotConnected on notconnected_26_out
  and and_392 (and_392_out, notconnected_26_out, notconnected_20_out[3]);
  nand nand_68 (nand_68_out, notconnected_21_out[3], notconnected_21_out[3]);
  nor nor_38 (nor_38_out, notconnected_22_out[3], notconnected_22_out[3]);
  and and_393 (and_393_out, not_67_out, not_66_out);
  and and_394 (and_394_out, notconnected_23_out, not_66_out);
  and and_395 (and_395_out, not_67_out, notconnected_24_out);
  and and_396 (and_396_out, notconnected_24_out, notconnected_23_out);
  and and_397 (and_397_out, not_70_out, not_69_out);
  and and_398 (and_398_out, notconnected_23_out, not_69_out);
  and and_399 (and_399_out, not_70_out, notconnected_24_out);
  and and_400 (and_400_out, notconnected_24_out, notconnected_23_out);
  _74TypeFlipFlop _74typeflipflop_74 (
    .CLK(button_1_out), .Data(TestAdvRegister[7]), .Load_A(dipswitch_17_out), .Load_B(dipswitch_18_out),
    .Always(TAR_always[7]), .Loaded_A(TAR_loadA[7]), .Loaded_B(TAR_loadB[7]), .Reset(reset_20_out));
  _74TypeFlipFlop _74typeflipflop_75 (
    .CLK(button_1_out), .Data(TestAdvRegister[6]), .Load_A(dipswitch_17_out), .Load_B(dipswitch_18_out),
    .Always(TAR_always[6]), .Loaded_A(TAR_loadA[6]), .Loaded_B(TAR_loadB[6]), .Reset(reset_20_out));
  _74TypeFlipFlop _74typeflipflop_76 (
    .CLK(button_1_out), .Data(TestAdvRegister[5]), .Load_A(dipswitch_17_out), .Load_B(dipswitch_18_out),
    .Always(TAR_always[5]), .Loaded_A(TAR_loadA[5]), .Loaded_B(TAR_loadB[5]), .Reset(reset_20_out));
  _74TypeFlipFlop _74typeflipflop_77 (
    .CLK(button_1_out), .Data(TestAdvRegister[4]), .Load_A(dipswitch_17_out), .Load_B(dipswitch_18_out),
    .Always(TAR_always[4]), .Loaded_A(TAR_loadA[4]), .Loaded_B(TAR_loadB[4]), .Reset(reset_20_out));
  _74TypeFlipFlop _74typeflipflop_78 (
    .CLK(button_1_out), .Data(TestAdvRegister[3]), .Load_A(dipswitch_17_out), .Load_B(dipswitch_18_out),
    .Always(TAR_always[3]), .Loaded_A(TAR_loadA[3]), .Loaded_B(TAR_loadB[3]), .Reset(reset_20_out));
  _74TypeFlipFlop _74typeflipflop_79 (
    .CLK(button_1_out), .Data(TestAdvRegister[2]), .Load_A(dipswitch_17_out), .Load_B(dipswitch_18_out),
    .Always(TAR_always[2]), .Loaded_A(TAR_loadA[2]), .Loaded_B(TAR_loadB[2]), .Reset(reset_20_out));
  _74TypeFlipFlop _74typeflipflop_80 (
    .CLK(button_1_out), .Data(TestAdvRegister[1]), .Load_A(dipswitch_17_out), .Load_B(dipswitch_18_out),
    .Always(TAR_always[1]), .Loaded_A(TAR_loadA[1]), .Loaded_B(TAR_loadB[1]), .Reset(reset_20_out));
  _74TypeFlipFlop _74typeflipflop_81 (
    .CLK(button_1_out), .Data(TestAdvRegister[0]), .Load_A(dipswitch_17_out), .Load_B(dipswitch_18_out),
    .Always(TAR_always[0]), .Loaded_A(TAR_loadA[0]), .Loaded_B(TAR_loadB[0]), .Reset(reset_20_out));
  and and_401 (and_401_out, notconnected_26_out, notconnected_20_out[4]);
  nand nand_69 (nand_69_out, notconnected_21_out[4], notconnected_21_out[4]);
  nor nor_39 (nor_39_out, notconnected_22_out[4], notconnected_22_out[4]);
  and and_402 (and_402_out, and_393_out, not_68_out);
  and and_403 (and_403_out, and_394_out, not_68_out);
  and and_404 (and_404_out, and_395_out, not_68_out);
  and and_405 (and_405_out, and_396_out, not_68_out);
  and and_406 (and_406_out, and_397_out, not_71_out);
  and and_407 (and_407_out, and_398_out, not_71_out);
  and and_408 (and_408_out, and_399_out, not_71_out);
  and and_409 (and_409_out, and_400_out, not_71_out);
  and and_410 (and_410_out, notconnected_26_out, notconnected_20_out[5]);
  and and_411 (and_411_out, notconnected_26_out, notconnected_20_out[6]);
  nand nand_70 (nand_70_out, notconnected_21_out[5], notconnected_21_out[5]);
  nand nand_71 (nand_71_out, notconnected_21_out[6], notconnected_21_out[6]);
  nor nor_40 (nor_40_out, notconnected_22_out[5], notconnected_22_out[5]);
  nor nor_41 (nor_41_out, notconnected_22_out[6], notconnected_22_out[6]);
  and and_412 (and_412_out, notconnected_26_out, notconnected_20_out[7]);
  nand nand_72 (nand_72_out, notconnected_21_out[7], notconnected_21_out[7]);
  nor nor_42 (nor_42_out, notconnected_22_out[7], notconnected_22_out[7]);
  // NotConnected on notconnected_27_out
  assign driver_169_out = notconnected_28_out ? notconnected_27_out[0] : 1'bz;  // Driver driver_169
  assign driver_170_out = notconnected_28_out ? notconnected_27_out[1] : 1'bz;  // Driver driver_170
  assign driver_171_out = notconnected_28_out ? notconnected_27_out[2] : 1'bz;  // Driver driver_171
  assign driver_172_out = notconnected_28_out ? notconnected_27_out[3] : 1'bz;  // Driver driver_172
  assign driver_173_out = notconnected_28_out ? notconnected_27_out[4] : 1'bz;  // Driver driver_173
  assign driver_174_out = notconnected_28_out ? notconnected_27_out[5] : 1'bz;  // Driver driver_174
  assign driver_175_out = notconnected_28_out ? notconnected_27_out[6] : 1'bz;  // Driver driver_175
  // NotConnected on notconnected_28_out
  assign driver_176_out = notconnected_28_out ? notconnected_27_out[7] : 1'bz;  // Driver driver_176

  // Notes on the sheet:
  //   Overwrite Value
  //   Overwrite
  //   Step
  //   COUNTER
  //   B
  //   Select
  //   MUX
  //   A
  //   .
  //   Z SWITCH
  //   Register Saving
  //   Register Saving Sys Active Toggle
  //   Data
  //   Clock
  //   Load_A
  //   Load_B
  //   Reset
  //   SaveValue
  //   SaveLocation
  //   Advanced Edge Flop
  //   Always
  //   Loaded_A
  //   Loaded_B
  //   DESTINATION sel
  //   Disable
  //   A_1
  //   A_0
  //   2x4 Demux
  //   Operation Decode
  //   Add
  //   Sub
  //   AND
  //   NAND
  //   OR
  //   NOR
  //   XOR
  //   Unused
  //   A3
  //   Immediate Arg 1
  //   Immediate Arg 2
  //   Arithmetic/Compare
  //   RAM
  //   Argument
  //   Arithmetic arguments
  //   A1
  //   A2
  //   3x8 Demux
  //   Arguments are listsed in order in decimal value
  //   Is0
  //   IsNot0
  //   More
  //   Less
  //   MoreOrEqual
  //   LessOrEqual
  //   Never
  //   Compare arguments
  //   ARG2 sel
  //   Many components are designed to
  //   take OPCODEs in and only use the
  //   last 3 argument bits.
  //   Arithmetic
  //   Compare
  //   Ram
  //   Main OPCODE Line
  //   Replace delay with system that saves values on the next tick. A register will hold the to save register and value. Then, it will save on that +1 tick to a register, ensuring it arrives before the clock. Selected operands should check if that register is about to be updated, and if so take the new data instead of old.
  //   Argument is another term for Operand
  //   Delay to make sure CLK signal does not arrive before Data is updated, otherwwise registers will never save. Update according to slowest result bus path that involves registers.
  //   ARG1 sel
  //   Immediates
  //   ARG2
  //   Immediate 2 Enable
  //   ARG1
  //   Immediate 1 Enable
  //   Immediate's Disable the corresponding argument sel
  //   Register
  //   Input
  //   SUBBER
  //   ALU
  //   Generate
  //   Propogate
  //   ADDER/SUBBER
  //   P_3
  //   G_3
  //   P_2
  //   G_2
  //   P_1
  //   G_1
  //   P_0
  //   G_0
  //   C_0
  //   4-bit Carry Look-ahead
  //   5Inp
  //   4Inp
  //   3Inp
  //   C_1
  //   C_4
  //   C_3
  //   C_2
  //   0's Conditional Unit
  //   Is less than 0 Unit
  //   Is!0 Unit
  //   ADDER
  //   COMPONENTS
  //   Register - outdated
  //   Edge Register
  //   Save
  //   Load
  //   Save Value
  //   Clk
  //   Load A
  //   Load B
  //   D
  //   Edge Flop
  //   Latch
  //   1 Bit mem
  //   SaveVal
  //   Write
  //   Loaded
  //   Always OUT
  //   OUT
  //   Always On Out
  //   Out
  //   INCRMNT
  //   Advanced Edge Register
  //   SWITCH FAKE
endmodule

/* Test case:
C_2 C_1 C_0 A_0 B_0 C_Arith
0 0 0 9 6 15 #addition and subtraction
0 0 1 9 6 3
0 0 0 6 7 13
0 0 1 111 67 44
0 0 0 32 59 91
0 1 0 51 60 48  #and
0 1 0 3 2 2
0 1 0 5 3 1
0 1 0 12 25 8
0 1 0 4 8 0
1 0 0 5 3 7 #or
1 0 0 2 8 10
1 0 0 12 25 29
1 0 0 0 7 7
0 1 1 1 1 254 #nand
0 1 1 2 4 255
0 1 1 15 3 252
1 0 1 1 0 254 #nor
1 0 1 3 5 248
1 0 1 128 64 63
1 1 0 5 3 6 #xor
1 1 0 10 10 0
1 1 0 85 170 255
1 1 0 14 1 15
*/

/* Test case:
In_3 In_2 In_1 Num_1 Out_0
0 0 0 4 0
0 0 1 5 1
0 0 0 210 0
0 0 1 253 1
0 1 1 65 0
0 1 0 102 1
0 1 1 237 1
0 1 0 179 0
1 0 0 102 1
1 0 0 0 1
1 0 0 252 0
1 0 1 179 1
1 0 1 0 1
1 0 1 112 0
1 1 0 0 1
1 1 0 243 1
1 1 0 123 1
1 1 1 0 0
1 1 1 243 0
1 1 1 123 0
*/

/* Test case:
D C L ALWAYS LOADED
# 1. Randomized Startup: Register state is unknown (X). LOADED is 0 because L=0.
0x00 0 0 X 0x00

# 2. Load 0xAA: ALWAYS updates to 0xAA. LOADED shows it because L=1.
0xAA C 1 0xAA 0xAA

# 3. Transparent Check: ALWAYS stays 0xAA. LOADED drops to 0x00 because L=0.
0x55 0 0 0xAA 0x00
0x21 C 0 0x21 0x00

# 5. Load 0x00: Register becomes 0. Both pins show 0.
0x00 C 1 0x00 0x00

# 6. Edge-Triggering: Data 0xEE only moves to ALWAYS on the rising edge.
0xEE 0 1 0x00 0x00  # L=1, but no clock yet; LOADED is 0 because reg is 0
0xEE 1 1 0xEE 0xEE  # Clock goes high; Reg becomes 0xEE. LOADED now shows it.
0xDD 0 1 0xEE 0xEE  # Clock falls; Reg stays 0xEE.

# 7. High-Clock Stability Test
0xAA 0 1 0xEE 0xEE  # Prepare data 0xAA, but clock is 0. ALWAYS stays 0xEE.
0xAA 1 1 0xAA 0xAA  # Clock goes High. Register captures 0xAA.
0xFF 1 1 0xAA 0xAA  # DATA CHANGES TO 0xFF WHILE CLOCK IS STILL HIGH.
                    # ALWAYS MUST STAY 0xAA. If it changes to 0xFF, it's a latch!
*/
