// Digital circuit overture.dig as structural Verilog
module overture (
  input  C_0,
  input  C_1,
  input  C_2,
  input  [7:0] A_0,
  input  [7:0] B_0,
  input  clk,
  input  [7:0] Num_1,
  input  In_3,
  input  In_2,
  input  In_1,
  output [7:0] O_0,
  output Out_0
);

  wire and_1_out, and_2_out, and_3_out, and_4_out, and_5_out, and_6_out, and_7_out, and_8_out, and_9_out,
       and_10_out, and_11_out, and_12_out, and_13_out, and_14_out, and_15_out, and_16_out, and_17_out,
       and_18_out, and_19_out, and_20_out, and_21_out, and_22_out, and_23_out, and_24_out, and_25_out,
       and_26_out, and_27_out, and_28_out, and_29_out, and_30_out, and_31_out, and_32_out, and_33_out,
       and_34_out, and_35_out, and_36_out, and_37_out, and_38_out, and_39_out, and_40_out, and_41_out,
       and_42_out, and_43_out, and_44_out, and_45_out, and_46_out, and_47_out, and_48_out, and_49_out,
       and_50_out, and_51_out, and_52_out, and_53_out, and_54_out, and_55_out, and_56_out, and_57_out,
       and_58_out, and_59_out, and_60_out, and_61_out, and_62_out, and_63_out, and_64_out, and_65_out,
       and_66_out, and_67_out, and_68_out, and_69_out, and_70_out, and_71_out, and_72_out, and_73_out,
       and_74_out, and_75_out, and_76_out, and_77_out, and_78_out, and_79_out, and_80_out, and_85_out,
       and_86_out, and_87_out, and_88_out, and_89_out, and_90_out, and_91_out, and_105_out, and_106_out,
       and_107_out, and_108_out, and_109_out, and_110_out, and_111_out, and_112_out, and_113_out,
       and_114_out, and_115_out, and_116_out, and_117_out, and_118_out, and_119_out, and_120_out,
       and_121_out, and_122_out, and_123_out, and_124_out, and_125_out, and_126_out, and_127_out,
       and_129_out, and_130_out, and_131_out, and_132_out, and_139_out, and_140_out, and_141_out,
       and_142_out, and_143_out, and_144_out, and_145_out, and_146_out, and_148_out, and_149_out,
       and_150_out, and_151_out, and_153_out, and_154_out, and_155_out, and_156_out, and_199_out,
       and_200_out, and_201_out, and_202_out, and_203_out, and_204_out, and_205_out, and_206_out,
       and_211_out, and_212_out, and_213_out, and_214_out, and_215_out, and_216_out, and_217_out,
       and_221_out, and_222_out, and_223_out, and_224_out, and_225_out, and_226_out, and_227_out,
       and_228_out, and_229_out, and_230_out, and_231_out, and_232_out, and_233_out, and_234_out,
       and_235_out, and_236_out, and_237_out, and_238_out, and_239_out, and_240_out, and_241_out,
       and_242_out, and_243_out, and_244_out, and_245_out, and_246_out, and_247_out, and_248_out,
       and_249_out, and_250_out, and_251_out, and_252_out, and_253_out, and_254_out, and_255_out,
       and_256_out, and_257_out, and_258_out, and_259_out, and_260_out, and_261_out, and_262_out,
       and_263_out, and_264_out, and_265_out, and_266_out, and_267_out, and_268_out, and_269_out,
       and_270_out, and_271_out, and_272_out, and_273_out, and_274_out, and_275_out, and_277_out,
       and_278_out, and_279_out, and_280_out, and_281_out, and_282_out, and_283_out, and_284_out,
       and_285_out, and_286_out, and_287_out, and_288_out, and_289_out, and_290_out, and_291_out,
       and_292_out, and_293_out, and_294_out, and_295_out, and_296_out, and_297_out, and_298_out,
       and_299_out, and_300_out, and_301_out, and_302_out, and_303_out, and_304_out, and_305_out,
       and_306_out, and_307_out, and_308_out, and_309_out, and_310_out, and_311_out, dipswitch_1_out,
       dipswitch_2_out, dipswitch_3_out, dipswitch_4_out, nand_1_out, nand_2_out, nand_3_out, nand_4_out,
       nand_5_out, nand_6_out, nand_7_out, nand_8_out, nand_9_out, nand_10_out, nand_11_out, nand_12_out,
       nand_13_out, nand_14_out, nand_15_out, nand_16_out, nand_17_out, nand_18_out, nand_19_out,
       nand_20_out, nand_21_out, nand_22_out, nand_23_out, nand_24_out, nand_25_out, nand_26_out,
       nand_27_out, nand_28_out, nand_29_out, nand_30_out, nand_31_out, nand_32_out, nand_33_out,
       nand_34_out, nand_35_out, nand_36_out, nand_37_out, nand_38_out, nand_39_out, nand_40_out,
       nand_41_out, nand_42_out, nand_43_out, nand_44_out, nand_45_out, nand_46_out, nand_47_out,
       nand_48_out, nand_49_out, nand_50_out, nand_51_out, nand_52_out, nand_53_out, nand_54_out,
       nand_55_out, nand_56_out, nand_57_out, nand_58_out, nand_59_out, nand_60_out, nand_61_out,
       nand_62_out, nand_63_out, nand_64_out, nand_65_out, nand_66_out, nand_67_out, nand_68_out,
       nand_69_out, nand_70_out, nand_71_out, nand_72_out, nand_73_out, nand_74_out, nand_75_out,
       nand_76_out, nand_77_out, nand_78_out, nand_79_out, nand_80_out, nand_81_out, nand_82_out,
       nand_83_out, nand_84_out, nand_85_out, nand_86_out, nand_87_out, nand_88_out, nand_89_out,
       nand_90_out, nand_91_out, nand_92_out, nand_93_out, nand_94_out, nand_95_out, nand_96_out,
       nand_97_out, nand_98_out, nand_99_out, nand_100_out, nand_101_out, nand_102_out, nand_103_out,
       nand_104_out, nand_105_out, nand_106_out, nand_107_out, nand_108_out, nand_109_out, nand_110_out,
       nand_111_out, nand_112_out, nand_113_out, nand_114_out, nand_115_out, nand_116_out, nand_117_out,
       nand_118_out, nand_119_out, nand_120_out, nand_121_out, nand_122_out, nand_123_out, nand_124_out,
       nand_125_out, nand_126_out, nand_127_out, nand_128_out, nand_129_out, nand_130_out, nand_131_out,
       nand_132_out, nand_133_out, nand_134_out, nand_135_out, nand_136_out, nand_137_out, nand_138_out,
       nand_139_out, nand_140_out, nand_141_out, nand_142_out, nand_143_out, nand_144_out, nand_145_out,
       nand_146_out, nand_147_out, nand_148_out, nand_149_out, nand_150_out, nand_151_out, nand_152_out,
       nand_153_out, nand_154_out, nand_155_out, nand_156_out, nand_157_out, nand_158_out, nand_159_out,
       nand_160_out, nand_161_out, nand_162_out, nand_163_out, nand_164_out, nand_165_out, nand_166_out,
       nand_167_out, nand_168_out, nand_169_out, nand_170_out, nand_171_out, nand_172_out, nand_173_out,
       nand_174_out, nand_175_out, nand_176_out, nand_177_out, nand_178_out, nand_179_out, nand_180_out,
       nand_181_out, nand_182_out, nand_183_out, nand_184_out, nand_185_out, nand_186_out, nand_187_out,
       nand_188_out, nand_189_out, nand_190_out, nand_191_out, nand_192_out, nand_193_out, nand_194_out,
       nand_195_out, nand_196_out, nand_197_out, nand_198_out, nand_199_out, nand_200_out, nand_201_out,
       nand_202_out, nand_203_out, nand_204_out, nand_205_out, nand_206_out, nand_207_out, nand_208_out,
       nand_209_out, nand_210_out, nand_211_out, nand_212_out, nand_213_out, nand_214_out, nand_215_out,
       nand_216_out, nand_217_out, nand_218_out, nand_219_out, nand_220_out, nand_221_out, nand_222_out,
       nand_223_out, nand_224_out, nand_225_out, nand_226_out, nand_227_out, nand_228_out, nand_229_out,
       nand_230_out, nand_231_out, nand_232_out, nand_233_out, nand_234_out, nand_235_out, nand_236_out,
       nand_237_out, nand_238_out, nand_239_out, nand_240_out, nand_241_out, nand_242_out, nand_243_out,
       nand_244_out, nand_245_out, nand_246_out, nand_247_out, nand_248_out, nand_249_out, nand_250_out,
       nand_251_out, nand_252_out, nand_253_out, nand_254_out, nand_255_out, nand_256_out, nand_257_out,
       nand_258_out, nand_259_out, nand_260_out, nand_261_out, nand_262_out, nand_263_out, nand_264_out,
       nand_265_out, nand_266_out, nand_267_out, nand_268_out, nand_269_out, nand_270_out, nand_271_out,
       nand_272_out, nand_273_out, nand_274_out, nand_275_out, nand_276_out, nand_277_out, nand_278_out,
       nand_279_out, nand_280_out, nand_281_out, nand_282_out, nand_283_out, nand_284_out, nand_285_out,
       nand_286_out, nand_287_out, nand_288_out, nand_289_out, nand_290_out, nand_291_out, nand_292_out,
       nand_293_out, nand_294_out, nand_295_out, nand_296_out, nand_297_out, nand_298_out, nand_299_out,
       nand_300_out, nand_301_out, nand_302_out, nand_303_out, nand_304_out, nand_306_out, nand_308_out,
       nand_310_out, nand_312_out, nand_313_out, nand_314_out, nand_315_out, nand_316_out, nand_317_out,
       nand_318_out, nand_319_out, nand_320_out, nand_321_out, nand_322_out, nand_323_out, nand_324_out,
       nand_325_out, nand_326_out, nand_327_out, nand_328_out, nand_330_out, nand_332_out, nand_334_out,
       nand_336_out, nand_345_out, nand_346_out, nand_347_out, nand_348_out, nand_349_out, nand_350_out,
       nand_351_out, nand_352_out, nand_353_out, nand_354_out, nand_355_out, nand_356_out, nand_357_out,
       nand_358_out, nand_359_out, nand_360_out, nand_361_out, nand_362_out, nand_363_out, nand_364_out,
       nand_365_out, nand_366_out, nand_367_out, nand_368_out, nand_369_out, nand_370_out, nand_371_out,
       nand_372_out, nand_373_out, nand_374_out, nand_375_out, nand_376_out, nand_377_out, nand_378_out,
       nand_379_out, nand_380_out, nand_381_out, nand_382_out, nand_383_out, nand_384_out, nand_385_out,
       nand_386_out, nand_387_out, nand_388_out, nand_389_out, nand_390_out, nand_391_out, nand_392_out,
       nand_393_out, nand_394_out, nand_395_out, nand_396_out, nand_397_out, nand_398_out, nand_399_out,
       nand_400_out, nor_9_out, nor_10_out, nor_11_out, nor_12_out, nor_13_out, nor_14_out, nor_15_out,
       nor_16_out, nor_17_out, nor_18_out, nor_19_out, nor_20_out, nor_21_out, nor_22_out, nor_23_out,
       nor_24_out, nor_25_out, nor_26_out, nor_27_out, nor_28_out, nor_29_out, nor_30_out, nor_31_out,
       nor_32_out, nor_33_out, nor_34_out, not_1_out, not_2_out, not_3_out, not_4_out, not_5_out, not_6_out,
       not_7_out, not_8_out, not_9_out, not_10_out, not_11_out, not_12_out, not_13_out, not_14_out,
       not_15_out, not_16_out, not_17_out, not_18_out, not_19_out, not_20_out, not_21_out, not_22_out,
       not_23_out, not_24_out, not_25_out, not_26_out, not_27_out, not_28_out, not_29_out, not_30_out,
       not_31_out, not_32_out, not_33_out, not_34_out, not_35_out, not_36_out, not_37_out, not_38_out,
       not_39_out, not_40_out, not_41_out, not_42_out, not_43_out, not_44_out, not_45_out, not_46_out,
       not_47_out, not_48_out, notconnected_1_out, notconnected_2_out, notconnected_3_out,
       notconnected_4_out, notconnected_5_out, notconnected_6_out, notconnected_8_out, notconnected_9_out,
       notconnected_11_out, notconnected_12_out, notconnected_14_out, notconnected_15_out,
       notconnected_17_out, notconnected_18_out, notconnected_20_out, notconnected_21_out,
       notconnected_23_out, notconnected_24_out, notconnected_26_out, notconnected_27_out,
       notconnected_28_out, notconnected_29_out, notconnected_33_out, notconnected_38_out,
       notconnected_42_out, notconnected_43_out, notconnected_44_out, notconnected_45_out, or_9_out,
       or_10_out, or_11_out, or_12_out, or_13_out, or_14_out, or_15_out, or_16_out, or_17_out, or_18_out,
       or_19_out, or_20_out, or_21_out, or_22_out, or_23_out, or_25_out, or_26_out, or_34_out, or_35_out,
       or_36_out, or_37_out, or_38_out, or_39_out, or_40_out, or_41_out, or_43_out, or_84_out, or_85_out,
       or_86_out, or_87_out, or_88_out, or_89_out, or_90_out, or_91_out, or_92_out, or_93_out, or_94_out,
       or_95_out, or_96_out, or_97_out, or_98_out, or_99_out, xor_9_out, xor_10_out, xor_11_out, xor_12_out,
       xor_13_out, xor_14_out, xor_15_out, xor_16_out, xor_23_out, xor_24_out, xor_25_out, xor_26_out,
       xor_27_out, xor_28_out, xor_29_out, xor_30_out, xor_41_out, xor_42_out, xor_43_out, xor_44_out,
       xor_45_out, xor_46_out, xor_47_out, xor_48_out, xor_49_out, xor_50_out, xor_51_out, xor_52_out,
       xor_53_out, xor_54_out, xor_55_out, xor_56_out, xor_57_out, xor_58_out, xor_59_out, xor_60_out,
       xor_61_out, xor_62_out, xor_63_out, xor_64_out, xor_65_out, xor_66_out, xor_67_out, xor_68_out,
       xor_69_out, xor_70_out, xor_71_out, xor_72_out;
  wire [7:0] and_96_out, and_104_out, and_152_out, and_192_out, and_193_out, and_194_out, and_195_out,
       and_196_out, and_220_out, nand_335_out, nand_344_out, nor_8_out, notconnected_7_out,
       notconnected_10_out, notconnected_13_out, notconnected_16_out, notconnected_19_out,
       notconnected_22_out, notconnected_25_out, notconnected_30_out, notconnected_31_out,
       notconnected_32_out, notconnected_34_out, notconnected_35_out, notconnected_36_out,
       notconnected_37_out, notconnected_39_out, notconnected_40_out, notconnected_41_out, or_8_out,
       or_42_out, or_80_out, or_81_out, or_82_out, or_83_out, xor_8_out, xor_36_out, xor_40_out;

  not not_1 (not_1_out, notconnected_1_out);
  not not_2 (not_2_out, not_1_out);
  and and_1 (and_1_out, and_3_out, not_2_out);
  and and_2 (and_2_out, not_4_out, notconnected_3_out);
  and and_3 (and_3_out, notconnected_3_out, notconnected_2_out);
  and and_4 (and_4_out, and_2_out, not_2_out);
  and and_5 (and_5_out, notconnected_2_out, not_3_out);
  and and_6 (and_6_out, and_5_out, not_2_out);
  and and_7 (and_7_out, not_4_out, not_3_out);
  and and_8 (and_8_out, and_7_out, not_2_out);
  not not_3 (not_3_out, notconnected_3_out);
  not not_4 (not_4_out, notconnected_2_out);
  not not_5 (not_5_out, notconnected_1_out);
  and and_9 (and_9_out, notconnected_3_out, notconnected_2_out);
  and and_10 (and_10_out, and_13_out, not_5_out);
  and and_11 (and_11_out, and_9_out, not_5_out);
  and and_12 (and_12_out, notconnected_2_out, not_6_out);
  and and_13 (and_13_out, not_7_out, notconnected_3_out);
  and and_14 (and_14_out, and_12_out, not_5_out);
  and and_15 (and_15_out, not_7_out, not_6_out);
  and and_16 (and_16_out, and_15_out, not_5_out);
  // NotConnected on notconnected_1_out
  not not_6 (not_6_out, notconnected_3_out);
  not not_7 (not_7_out, notconnected_2_out);
  // NotConnected on notconnected_2_out
  // NotConnected on notconnected_3_out
  not not_8 (not_8_out, notconnected_4_out);
  not not_9 (not_9_out, not_8_out);
  and and_17 (and_17_out, and_19_out, not_9_out);
  and and_18 (and_18_out, not_11_out, notconnected_6_out);
  and and_19 (and_19_out, notconnected_6_out, notconnected_5_out);
  and and_20 (and_20_out, and_18_out, not_9_out);
  and and_21 (and_21_out, notconnected_5_out, not_10_out);
  and and_22 (and_22_out, and_21_out, not_9_out);
  and and_23 (and_23_out, not_11_out, not_10_out);
  and and_24 (and_24_out, and_23_out, not_9_out);
  not not_10 (not_10_out, notconnected_6_out);
  not not_11 (not_11_out, notconnected_5_out);
  not not_12 (not_12_out, notconnected_4_out);
  and and_25 (and_25_out, notconnected_6_out, notconnected_5_out);
  and and_26 (and_26_out, and_29_out, not_12_out);
  and and_27 (and_27_out, and_25_out, not_12_out);
  and and_28 (and_28_out, notconnected_5_out, not_13_out);
  and and_29 (and_29_out, not_14_out, notconnected_6_out);
  and and_30 (and_30_out, and_28_out, not_12_out);
  and and_31 (and_31_out, not_14_out, not_13_out);
  and and_32 (and_32_out, and_31_out, not_12_out);
  // NotConnected on notconnected_4_out
  not not_13 (not_13_out, notconnected_6_out);
  not not_14 (not_14_out, notconnected_5_out);
  // NotConnected on notconnected_5_out
  // NotConnected on notconnected_6_out
  // NotConnected on notconnected_7_out
  // NotConnected on notconnected_8_out
  // NotConnected on notconnected_9_out
  // NotConnected on notconnected_10_out
  // NotConnected on notconnected_11_out
  // NotConnected on notconnected_12_out
  // NotConnected on notconnected_13_out
  // NotConnected on notconnected_14_out
  // NotConnected on notconnected_15_out
  // NotConnected on notconnected_16_out
  // NotConnected on notconnected_17_out
  // NotConnected on notconnected_18_out
  // NotConnected on notconnected_19_out
  // NotConnected on notconnected_20_out
  // NotConnected on notconnected_21_out
  // NotConnected on notconnected_22_out
  // NotConnected on notconnected_23_out
  // NotConnected on notconnected_24_out
  nand nand_1 (nand_1_out, nand_4_out, nand_2_out);
  nand nand_2 (nand_2_out, nand_1_out, notconnected_8_out);
  nand nand_3 (nand_3_out, nand_2_out, notconnected_8_out, nand_4_out);
  nand nand_4 (nand_4_out, nand_3_out, notconnected_7_out[6]);
  nand nand_5 (nand_5_out, nand_8_out, nand_6_out);
  nand nand_6 (nand_6_out, nand_5_out, notconnected_8_out);
  nand nand_7 (nand_7_out, nand_6_out, notconnected_8_out, nand_8_out);
  nand nand_8 (nand_8_out, nand_7_out, notconnected_7_out[4]);
  nand nand_9 (nand_9_out, nand_12_out, nand_10_out);
  nand nand_10 (nand_10_out, nand_9_out, notconnected_8_out);
  nand nand_11 (nand_11_out, nand_10_out, notconnected_8_out, nand_12_out);
  nand nand_12 (nand_12_out, nand_11_out, notconnected_7_out[2]);
  nand nand_13 (nand_13_out, nand_16_out, nand_14_out);
  nand nand_14 (nand_14_out, nand_13_out, notconnected_8_out);
  nand nand_15 (nand_15_out, nand_14_out, notconnected_8_out, nand_16_out);
  nand nand_16 (nand_16_out, nand_15_out, notconnected_7_out[0]);
  nand nand_17 (nand_17_out, nand_20_out, nand_18_out);
  nand nand_18 (nand_18_out, nand_17_out, notconnected_11_out);
  nand nand_19 (nand_19_out, nand_18_out, notconnected_11_out, nand_20_out);
  nand nand_20 (nand_20_out, nand_19_out, notconnected_10_out[6]);
  nand nand_21 (nand_21_out, nand_24_out, nand_22_out);
  nand nand_22 (nand_22_out, nand_21_out, notconnected_11_out);
  nand nand_23 (nand_23_out, nand_22_out, notconnected_11_out, nand_24_out);
  nand nand_24 (nand_24_out, nand_23_out, notconnected_10_out[4]);
  nand nand_25 (nand_25_out, nand_28_out, nand_26_out);
  nand nand_26 (nand_26_out, nand_25_out, notconnected_11_out);
  nand nand_27 (nand_27_out, nand_26_out, notconnected_11_out, nand_28_out);
  nand nand_28 (nand_28_out, nand_27_out, notconnected_10_out[2]);
  nand nand_29 (nand_29_out, nand_32_out, nand_30_out);
  nand nand_30 (nand_30_out, nand_29_out, notconnected_11_out);
  nand nand_31 (nand_31_out, nand_30_out, notconnected_11_out, nand_32_out);
  nand nand_32 (nand_32_out, nand_31_out, notconnected_10_out[0]);
  nand nand_33 (nand_33_out, nand_36_out, nand_34_out);
  nand nand_34 (nand_34_out, nand_33_out, notconnected_14_out);
  nand nand_35 (nand_35_out, nand_34_out, notconnected_14_out, nand_36_out);
  nand nand_36 (nand_36_out, nand_35_out, notconnected_13_out[6]);
  nand nand_37 (nand_37_out, nand_40_out, nand_38_out);
  nand nand_38 (nand_38_out, nand_37_out, notconnected_14_out);
  nand nand_39 (nand_39_out, nand_38_out, notconnected_14_out, nand_40_out);
  nand nand_40 (nand_40_out, nand_39_out, notconnected_13_out[4]);
  nand nand_41 (nand_41_out, nand_44_out, nand_42_out);
  nand nand_42 (nand_42_out, nand_41_out, notconnected_14_out);
  nand nand_43 (nand_43_out, nand_42_out, notconnected_14_out, nand_44_out);
  nand nand_44 (nand_44_out, nand_43_out, notconnected_13_out[2]);
  nand nand_45 (nand_45_out, nand_48_out, nand_46_out);
  nand nand_46 (nand_46_out, nand_45_out, notconnected_14_out);
  nand nand_47 (nand_47_out, nand_46_out, notconnected_14_out, nand_48_out);
  nand nand_48 (nand_48_out, nand_47_out, notconnected_13_out[0]);
  nand nand_49 (nand_49_out, nand_52_out, nand_50_out);
  nand nand_50 (nand_50_out, nand_49_out, notconnected_17_out);
  nand nand_51 (nand_51_out, nand_50_out, notconnected_17_out, nand_52_out);
  nand nand_52 (nand_52_out, nand_51_out, notconnected_16_out[6]);
  nand nand_53 (nand_53_out, nand_56_out, nand_54_out);
  nand nand_54 (nand_54_out, nand_53_out, notconnected_17_out);
  nand nand_55 (nand_55_out, nand_54_out, notconnected_17_out, nand_56_out);
  nand nand_56 (nand_56_out, nand_55_out, notconnected_16_out[4]);
  nand nand_57 (nand_57_out, nand_60_out, nand_58_out);
  nand nand_58 (nand_58_out, nand_57_out, notconnected_17_out);
  nand nand_59 (nand_59_out, nand_58_out, notconnected_17_out, nand_60_out);
  nand nand_60 (nand_60_out, nand_59_out, notconnected_16_out[2]);
  nand nand_61 (nand_61_out, nand_64_out, nand_62_out);
  nand nand_62 (nand_62_out, nand_61_out, notconnected_17_out);
  nand nand_63 (nand_63_out, nand_62_out, notconnected_17_out, nand_64_out);
  nand nand_64 (nand_64_out, nand_63_out, notconnected_16_out[0]);
  nand nand_65 (nand_65_out, nand_68_out, nand_66_out);
  nand nand_66 (nand_66_out, nand_65_out, notconnected_20_out);
  nand nand_67 (nand_67_out, nand_66_out, notconnected_20_out, nand_68_out);
  nand nand_68 (nand_68_out, nand_67_out, notconnected_19_out[6]);
  nand nand_69 (nand_69_out, nand_72_out, nand_70_out);
  nand nand_70 (nand_70_out, nand_69_out, notconnected_20_out);
  nand nand_71 (nand_71_out, nand_70_out, notconnected_20_out, nand_72_out);
  nand nand_72 (nand_72_out, nand_71_out, notconnected_19_out[4]);
  nand nand_73 (nand_73_out, nand_76_out, nand_74_out);
  nand nand_74 (nand_74_out, nand_73_out, notconnected_20_out);
  nand nand_75 (nand_75_out, nand_74_out, notconnected_20_out, nand_76_out);
  nand nand_76 (nand_76_out, nand_75_out, notconnected_19_out[2]);
  nand nand_77 (nand_77_out, nand_80_out, nand_78_out);
  nand nand_78 (nand_78_out, nand_77_out, notconnected_20_out);
  nand nand_79 (nand_79_out, nand_78_out, notconnected_20_out, nand_80_out);
  nand nand_80 (nand_80_out, nand_79_out, notconnected_19_out[0]);
  nand nand_81 (nand_81_out, nand_84_out, nand_82_out);
  nand nand_82 (nand_82_out, nand_81_out, notconnected_23_out);
  nand nand_83 (nand_83_out, nand_82_out, notconnected_23_out, nand_84_out);
  nand nand_84 (nand_84_out, nand_83_out, notconnected_22_out[6]);
  nand nand_85 (nand_85_out, nand_88_out, nand_86_out);
  nand nand_86 (nand_86_out, nand_85_out, notconnected_23_out);
  nand nand_87 (nand_87_out, nand_86_out, notconnected_23_out, nand_88_out);
  nand nand_88 (nand_88_out, nand_87_out, notconnected_22_out[4]);
  nand nand_89 (nand_89_out, nand_92_out, nand_90_out);
  nand nand_90 (nand_90_out, nand_89_out, notconnected_23_out);
  nand nand_91 (nand_91_out, nand_90_out, notconnected_23_out, nand_92_out);
  nand nand_92 (nand_92_out, nand_91_out, notconnected_22_out[2]);
  nand nand_93 (nand_93_out, nand_96_out, nand_94_out);
  nand nand_94 (nand_94_out, nand_93_out, notconnected_23_out);
  nand nand_95 (nand_95_out, nand_94_out, notconnected_23_out, nand_96_out);
  nand nand_96 (nand_96_out, nand_95_out, notconnected_22_out[0]);
  nand nand_97 (nand_97_out, nand_2_out, nand_98_out);
  nand nand_98 (nand_98_out, nand_97_out, nand_3_out);
  and and_33 (and_33_out, nand_97_out, notconnected_9_out);
  nand nand_99 (nand_99_out, nand_6_out, nand_100_out);
  nand nand_100 (nand_100_out, nand_99_out, nand_7_out);
  and and_34 (and_34_out, nand_99_out, notconnected_9_out);
  nand nand_101 (nand_101_out, nand_10_out, nand_102_out);
  nand nand_102 (nand_102_out, nand_101_out, nand_11_out);
  and and_35 (and_35_out, nand_101_out, notconnected_9_out);
  nand nand_103 (nand_103_out, nand_14_out, nand_104_out);
  nand nand_104 (nand_104_out, nand_103_out, nand_15_out);
  and and_36 (and_36_out, nand_103_out, notconnected_9_out);
  nand nand_105 (nand_105_out, nand_18_out, nand_106_out);
  nand nand_106 (nand_106_out, nand_105_out, nand_19_out);
  and and_37 (and_37_out, nand_105_out, notconnected_12_out);
  nand nand_107 (nand_107_out, nand_22_out, nand_108_out);
  nand nand_108 (nand_108_out, nand_107_out, nand_23_out);
  and and_38 (and_38_out, nand_107_out, notconnected_12_out);
  nand nand_109 (nand_109_out, nand_26_out, nand_110_out);
  nand nand_110 (nand_110_out, nand_109_out, nand_27_out);
  and and_39 (and_39_out, nand_109_out, notconnected_12_out);
  nand nand_111 (nand_111_out, nand_30_out, nand_112_out);
  nand nand_112 (nand_112_out, nand_111_out, nand_31_out);
  and and_40 (and_40_out, nand_111_out, notconnected_12_out);
  nand nand_113 (nand_113_out, nand_34_out, nand_114_out);
  nand nand_114 (nand_114_out, nand_113_out, nand_35_out);
  and and_41 (and_41_out, nand_113_out, notconnected_15_out);
  nand nand_115 (nand_115_out, nand_38_out, nand_116_out);
  nand nand_116 (nand_116_out, nand_115_out, nand_39_out);
  and and_42 (and_42_out, nand_115_out, notconnected_15_out);
  nand nand_117 (nand_117_out, nand_42_out, nand_118_out);
  nand nand_118 (nand_118_out, nand_117_out, nand_43_out);
  and and_43 (and_43_out, nand_117_out, notconnected_15_out);
  nand nand_119 (nand_119_out, nand_46_out, nand_120_out);
  nand nand_120 (nand_120_out, nand_119_out, nand_47_out);
  and and_44 (and_44_out, nand_119_out, notconnected_15_out);
  nand nand_121 (nand_121_out, nand_50_out, nand_122_out);
  nand nand_122 (nand_122_out, nand_121_out, nand_51_out);
  and and_45 (and_45_out, nand_121_out, notconnected_18_out);
  nand nand_123 (nand_123_out, nand_54_out, nand_124_out);
  nand nand_124 (nand_124_out, nand_123_out, nand_55_out);
  and and_46 (and_46_out, nand_123_out, notconnected_18_out);
  nand nand_125 (nand_125_out, nand_58_out, nand_126_out);
  nand nand_126 (nand_126_out, nand_125_out, nand_59_out);
  and and_47 (and_47_out, nand_125_out, notconnected_18_out);
  nand nand_127 (nand_127_out, nand_62_out, nand_128_out);
  nand nand_128 (nand_128_out, nand_127_out, nand_63_out);
  and and_48 (and_48_out, nand_127_out, notconnected_18_out);
  nand nand_129 (nand_129_out, nand_66_out, nand_130_out);
  nand nand_130 (nand_130_out, nand_129_out, nand_67_out);
  and and_49 (and_49_out, nand_129_out, notconnected_21_out);
  nand nand_131 (nand_131_out, nand_70_out, nand_132_out);
  nand nand_132 (nand_132_out, nand_131_out, nand_71_out);
  and and_50 (and_50_out, nand_131_out, notconnected_21_out);
  nand nand_133 (nand_133_out, nand_74_out, nand_134_out);
  nand nand_134 (nand_134_out, nand_133_out, nand_75_out);
  and and_51 (and_51_out, nand_133_out, notconnected_21_out);
  nand nand_135 (nand_135_out, nand_78_out, nand_136_out);
  nand nand_136 (nand_136_out, nand_135_out, nand_79_out);
  and and_52 (and_52_out, nand_135_out, notconnected_21_out);
  nand nand_137 (nand_137_out, nand_82_out, nand_138_out);
  nand nand_138 (nand_138_out, nand_137_out, nand_83_out);
  and and_53 (and_53_out, nand_137_out, notconnected_24_out);
  nand nand_139 (nand_139_out, nand_86_out, nand_140_out);
  nand nand_140 (nand_140_out, nand_139_out, nand_87_out);
  and and_54 (and_54_out, nand_139_out, notconnected_24_out);
  nand nand_141 (nand_141_out, nand_90_out, nand_142_out);
  nand nand_142 (nand_142_out, nand_141_out, nand_91_out);
  and and_55 (and_55_out, nand_141_out, notconnected_24_out);
  nand nand_143 (nand_143_out, nand_94_out, nand_144_out);
  nand nand_144 (nand_144_out, nand_143_out, nand_95_out);
  and and_56 (and_56_out, nand_143_out, notconnected_24_out);
  nand nand_145 (nand_145_out, nand_148_out, nand_146_out);
  nand nand_146 (nand_146_out, nand_145_out, notconnected_8_out);
  nand nand_147 (nand_147_out, nand_146_out, notconnected_8_out, nand_148_out);
  nand nand_148 (nand_148_out, nand_147_out, notconnected_7_out[7]);
  nand nand_149 (nand_149_out, nand_152_out, nand_150_out);
  nand nand_150 (nand_150_out, nand_149_out, notconnected_8_out);
  nand nand_151 (nand_151_out, nand_150_out, notconnected_8_out, nand_152_out);
  nand nand_152 (nand_152_out, nand_151_out, notconnected_7_out[5]);
  nand nand_153 (nand_153_out, nand_156_out, nand_154_out);
  nand nand_154 (nand_154_out, nand_153_out, notconnected_8_out);
  nand nand_155 (nand_155_out, nand_154_out, notconnected_8_out, nand_156_out);
  nand nand_156 (nand_156_out, nand_155_out, notconnected_7_out[3]);
  nand nand_157 (nand_157_out, nand_160_out, nand_158_out);
  nand nand_158 (nand_158_out, nand_157_out, notconnected_8_out);
  nand nand_159 (nand_159_out, nand_158_out, notconnected_8_out, nand_160_out);
  nand nand_160 (nand_160_out, nand_159_out, notconnected_7_out[1]);
  nand nand_161 (nand_161_out, nand_164_out, nand_162_out);
  nand nand_162 (nand_162_out, nand_161_out, notconnected_11_out);
  nand nand_163 (nand_163_out, nand_162_out, notconnected_11_out, nand_164_out);
  nand nand_164 (nand_164_out, nand_163_out, notconnected_10_out[7]);
  nand nand_165 (nand_165_out, nand_168_out, nand_166_out);
  nand nand_166 (nand_166_out, nand_165_out, notconnected_11_out);
  nand nand_167 (nand_167_out, nand_166_out, notconnected_11_out, nand_168_out);
  nand nand_168 (nand_168_out, nand_167_out, notconnected_10_out[5]);
  nand nand_169 (nand_169_out, nand_172_out, nand_170_out);
  nand nand_170 (nand_170_out, nand_169_out, notconnected_11_out);
  nand nand_171 (nand_171_out, nand_170_out, notconnected_11_out, nand_172_out);
  nand nand_172 (nand_172_out, nand_171_out, notconnected_10_out[3]);
  nand nand_173 (nand_173_out, nand_176_out, nand_174_out);
  nand nand_174 (nand_174_out, nand_173_out, notconnected_11_out);
  nand nand_175 (nand_175_out, nand_174_out, notconnected_11_out, nand_176_out);
  nand nand_176 (nand_176_out, nand_175_out, notconnected_10_out[1]);
  nand nand_177 (nand_177_out, nand_180_out, nand_178_out);
  nand nand_178 (nand_178_out, nand_177_out, notconnected_14_out);
  nand nand_179 (nand_179_out, nand_178_out, notconnected_14_out, nand_180_out);
  nand nand_180 (nand_180_out, nand_179_out, notconnected_13_out[7]);
  nand nand_181 (nand_181_out, nand_184_out, nand_182_out);
  nand nand_182 (nand_182_out, nand_181_out, notconnected_14_out);
  nand nand_183 (nand_183_out, nand_182_out, notconnected_14_out, nand_184_out);
  nand nand_184 (nand_184_out, nand_183_out, notconnected_13_out[5]);
  nand nand_185 (nand_185_out, nand_188_out, nand_186_out);
  nand nand_186 (nand_186_out, nand_185_out, notconnected_14_out);
  nand nand_187 (nand_187_out, nand_186_out, notconnected_14_out, nand_188_out);
  nand nand_188 (nand_188_out, nand_187_out, notconnected_13_out[3]);
  nand nand_189 (nand_189_out, nand_192_out, nand_190_out);
  nand nand_190 (nand_190_out, nand_189_out, notconnected_14_out);
  nand nand_191 (nand_191_out, nand_190_out, notconnected_14_out, nand_192_out);
  nand nand_192 (nand_192_out, nand_191_out, notconnected_13_out[1]);
  nand nand_193 (nand_193_out, nand_196_out, nand_194_out);
  nand nand_194 (nand_194_out, nand_193_out, notconnected_17_out);
  nand nand_195 (nand_195_out, nand_194_out, notconnected_17_out, nand_196_out);
  nand nand_196 (nand_196_out, nand_195_out, notconnected_16_out[7]);
  nand nand_197 (nand_197_out, nand_200_out, nand_198_out);
  nand nand_198 (nand_198_out, nand_197_out, notconnected_17_out);
  nand nand_199 (nand_199_out, nand_198_out, notconnected_17_out, nand_200_out);
  nand nand_200 (nand_200_out, nand_199_out, notconnected_16_out[5]);
  nand nand_201 (nand_201_out, nand_204_out, nand_202_out);
  nand nand_202 (nand_202_out, nand_201_out, notconnected_17_out);
  nand nand_203 (nand_203_out, nand_202_out, notconnected_17_out, nand_204_out);
  nand nand_204 (nand_204_out, nand_203_out, notconnected_16_out[3]);
  nand nand_205 (nand_205_out, nand_208_out, nand_206_out);
  nand nand_206 (nand_206_out, nand_205_out, notconnected_17_out);
  nand nand_207 (nand_207_out, nand_206_out, notconnected_17_out, nand_208_out);
  nand nand_208 (nand_208_out, nand_207_out, notconnected_16_out[1]);
  nand nand_209 (nand_209_out, nand_212_out, nand_210_out);
  nand nand_210 (nand_210_out, nand_209_out, notconnected_20_out);
  nand nand_211 (nand_211_out, nand_210_out, notconnected_20_out, nand_212_out);
  nand nand_212 (nand_212_out, nand_211_out, notconnected_19_out[7]);
  nand nand_213 (nand_213_out, nand_216_out, nand_214_out);
  nand nand_214 (nand_214_out, nand_213_out, notconnected_20_out);
  nand nand_215 (nand_215_out, nand_214_out, notconnected_20_out, nand_216_out);
  nand nand_216 (nand_216_out, nand_215_out, notconnected_19_out[5]);
  nand nand_217 (nand_217_out, nand_220_out, nand_218_out);
  nand nand_218 (nand_218_out, nand_217_out, notconnected_20_out);
  nand nand_219 (nand_219_out, nand_218_out, notconnected_20_out, nand_220_out);
  nand nand_220 (nand_220_out, nand_219_out, notconnected_19_out[3]);
  nand nand_221 (nand_221_out, nand_224_out, nand_222_out);
  nand nand_222 (nand_222_out, nand_221_out, notconnected_20_out);
  nand nand_223 (nand_223_out, nand_222_out, notconnected_20_out, nand_224_out);
  nand nand_224 (nand_224_out, nand_223_out, notconnected_19_out[1]);
  nand nand_225 (nand_225_out, nand_228_out, nand_226_out);
  nand nand_226 (nand_226_out, nand_225_out, notconnected_23_out);
  nand nand_227 (nand_227_out, nand_226_out, notconnected_23_out, nand_228_out);
  nand nand_228 (nand_228_out, nand_227_out, notconnected_22_out[7]);
  nand nand_229 (nand_229_out, nand_232_out, nand_230_out);
  nand nand_230 (nand_230_out, nand_229_out, notconnected_23_out);
  nand nand_231 (nand_231_out, nand_230_out, notconnected_23_out, nand_232_out);
  nand nand_232 (nand_232_out, nand_231_out, notconnected_22_out[5]);
  nand nand_233 (nand_233_out, nand_236_out, nand_234_out);
  nand nand_234 (nand_234_out, nand_233_out, notconnected_23_out);
  nand nand_235 (nand_235_out, nand_234_out, notconnected_23_out, nand_236_out);
  nand nand_236 (nand_236_out, nand_235_out, notconnected_22_out[3]);
  nand nand_237 (nand_237_out, nand_240_out, nand_238_out);
  nand nand_238 (nand_238_out, nand_237_out, notconnected_23_out);
  nand nand_239 (nand_239_out, nand_238_out, notconnected_23_out, nand_240_out);
  nand nand_240 (nand_240_out, nand_239_out, notconnected_22_out[1]);
  nand nand_241 (nand_241_out, nand_146_out, nand_242_out);
  nand nand_242 (nand_242_out, nand_241_out, nand_147_out);
  and and_57 (and_57_out, nand_241_out, notconnected_9_out);
  nand nand_243 (nand_243_out, nand_150_out, nand_244_out);
  nand nand_244 (nand_244_out, nand_243_out, nand_151_out);
  and and_58 (and_58_out, nand_243_out, notconnected_9_out);
  nand nand_245 (nand_245_out, nand_154_out, nand_246_out);
  nand nand_246 (nand_246_out, nand_245_out, nand_155_out);
  and and_59 (and_59_out, nand_245_out, notconnected_9_out);
  nand nand_247 (nand_247_out, nand_158_out, nand_248_out);
  nand nand_248 (nand_248_out, nand_247_out, nand_159_out);
  and and_60 (and_60_out, nand_247_out, notconnected_9_out);
  nand nand_249 (nand_249_out, nand_162_out, nand_250_out);
  nand nand_250 (nand_250_out, nand_249_out, nand_163_out);
  and and_61 (and_61_out, nand_249_out, notconnected_12_out);
  nand nand_251 (nand_251_out, nand_166_out, nand_252_out);
  nand nand_252 (nand_252_out, nand_251_out, nand_167_out);
  and and_62 (and_62_out, nand_251_out, notconnected_12_out);
  nand nand_253 (nand_253_out, nand_170_out, nand_254_out);
  nand nand_254 (nand_254_out, nand_253_out, nand_171_out);
  and and_63 (and_63_out, nand_253_out, notconnected_12_out);
  nand nand_255 (nand_255_out, nand_174_out, nand_256_out);
  nand nand_256 (nand_256_out, nand_255_out, nand_175_out);
  and and_64 (and_64_out, nand_255_out, notconnected_12_out);
  nand nand_257 (nand_257_out, nand_178_out, nand_258_out);
  nand nand_258 (nand_258_out, nand_257_out, nand_179_out);
  and and_65 (and_65_out, nand_257_out, notconnected_15_out);
  nand nand_259 (nand_259_out, nand_182_out, nand_260_out);
  nand nand_260 (nand_260_out, nand_259_out, nand_183_out);
  and and_66 (and_66_out, nand_259_out, notconnected_15_out);
  nand nand_261 (nand_261_out, nand_186_out, nand_262_out);
  nand nand_262 (nand_262_out, nand_261_out, nand_187_out);
  and and_67 (and_67_out, nand_261_out, notconnected_15_out);
  nand nand_263 (nand_263_out, nand_190_out, nand_264_out);
  nand nand_264 (nand_264_out, nand_263_out, nand_191_out);
  and and_68 (and_68_out, nand_263_out, notconnected_15_out);
  nand nand_265 (nand_265_out, nand_194_out, nand_266_out);
  nand nand_266 (nand_266_out, nand_265_out, nand_195_out);
  and and_69 (and_69_out, nand_265_out, notconnected_18_out);
  nand nand_267 (nand_267_out, nand_198_out, nand_268_out);
  nand nand_268 (nand_268_out, nand_267_out, nand_199_out);
  and and_70 (and_70_out, nand_267_out, notconnected_18_out);
  nand nand_269 (nand_269_out, nand_202_out, nand_270_out);
  nand nand_270 (nand_270_out, nand_269_out, nand_203_out);
  and and_71 (and_71_out, nand_269_out, notconnected_18_out);
  nand nand_271 (nand_271_out, nand_206_out, nand_272_out);
  nand nand_272 (nand_272_out, nand_271_out, nand_207_out);
  and and_72 (and_72_out, nand_271_out, notconnected_18_out);
  nand nand_273 (nand_273_out, nand_210_out, nand_274_out);
  nand nand_274 (nand_274_out, nand_273_out, nand_211_out);
  and and_73 (and_73_out, nand_273_out, notconnected_21_out);
  nand nand_275 (nand_275_out, nand_214_out, nand_276_out);
  nand nand_276 (nand_276_out, nand_275_out, nand_215_out);
  and and_74 (and_74_out, nand_275_out, notconnected_21_out);
  nand nand_277 (nand_277_out, nand_218_out, nand_278_out);
  nand nand_278 (nand_278_out, nand_277_out, nand_219_out);
  and and_75 (and_75_out, nand_277_out, notconnected_21_out);
  nand nand_279 (nand_279_out, nand_222_out, nand_280_out);
  nand nand_280 (nand_280_out, nand_279_out, nand_223_out);
  and and_76 (and_76_out, nand_279_out, notconnected_21_out);
  nand nand_281 (nand_281_out, nand_226_out, nand_282_out);
  nand nand_282 (nand_282_out, nand_281_out, nand_227_out);
  and and_77 (and_77_out, nand_281_out, notconnected_24_out);
  nand nand_283 (nand_283_out, nand_230_out, nand_284_out);
  nand nand_284 (nand_284_out, nand_283_out, nand_231_out);
  and and_78 (and_78_out, nand_283_out, notconnected_24_out);
  nand nand_285 (nand_285_out, nand_234_out, nand_286_out);
  nand nand_286 (nand_286_out, nand_285_out, nand_235_out);
  and and_79 (and_79_out, nand_285_out, notconnected_24_out);
  nand nand_287 (nand_287_out, nand_238_out, nand_288_out);
  nand nand_288 (nand_288_out, nand_287_out, nand_239_out);
  and and_80 (and_80_out, nand_287_out, notconnected_24_out);
  DipSwitch dipswitch_1 (.out(dipswitch_1_out));
  and and_81 (and_96_out[0], dipswitch_1_out, 1'b0);
  and and_82 (and_96_out[1], dipswitch_1_out, 1'b0);
  and and_83 (and_96_out[2], dipswitch_1_out, 1'b0);
  // And and_84 has open pins: In_1=and_85_out, In_2=nand_335_out[7], out=open
  xor xor_1 (xor_8_out[7], nand_335_out[7], and_85_out);
  and and_85 (and_85_out, and_86_out, nand_335_out[6]);
  xor xor_2 (xor_8_out[6], nand_335_out[6], and_86_out);
  and and_86 (and_86_out, and_87_out, nand_335_out[5]);
  xor xor_3 (xor_8_out[5], nand_335_out[5], and_87_out);
  and and_87 (and_87_out, and_88_out, nand_335_out[4]);
  xor xor_4 (xor_8_out[4], nand_335_out[4], and_88_out);
  and and_88 (and_88_out, and_89_out, nand_335_out[3]);
  xor xor_5 (xor_8_out[3], nand_335_out[3], and_89_out);
  and and_89 (and_89_out, and_90_out, nand_335_out[2]);
  xor xor_6 (xor_8_out[2], nand_335_out[2], and_90_out);
  and and_90 (and_90_out, and_91_out, nand_335_out[1]);
  xor xor_7 (xor_8_out[1], nand_335_out[1], and_91_out);
  and and_91 (and_91_out, 1'b1, nand_335_out[0]);
  xor xor_8 (xor_8_out[0], nand_335_out[0], 1'b1);
  and and_92 (and_96_out[3], dipswitch_1_out, 1'b0);
  and and_93 (and_96_out[4], dipswitch_1_out, 1'b0);
  and and_94 (and_96_out[5], dipswitch_1_out, 1'b0);
  and and_95 (and_96_out[6], dipswitch_1_out, 1'b0);
  not not_15 (not_15_out, dipswitch_1_out);
  and and_96 (and_96_out[7], dipswitch_1_out, 1'b0);
  or or_1 (or_8_out[0], and_104_out[0], and_96_out[0]);
  or or_2 (or_8_out[1], and_104_out[1], and_96_out[1]);
  or or_3 (or_8_out[2], and_104_out[2], and_96_out[2]);
  and and_97 (and_104_out[0], not_15_out, xor_8_out[0]);
  and and_98 (and_104_out[1], not_15_out, xor_8_out[1]);
  and and_99 (and_104_out[2], not_15_out, xor_8_out[2]);
  and and_100 (and_104_out[3], not_15_out, xor_8_out[3]);
  and and_101 (and_104_out[4], not_15_out, xor_8_out[4]);
  and and_102 (and_104_out[5], not_15_out, xor_8_out[5]);
  and and_103 (and_104_out[6], not_15_out, xor_8_out[6]);
  and and_104 (and_104_out[7], not_15_out, xor_8_out[7]);
  or or_4 (or_8_out[3], and_104_out[3], and_96_out[3]);
  or or_5 (or_8_out[4], and_104_out[4], and_96_out[4]);
  or or_6 (or_8_out[5], and_104_out[5], and_96_out[5]);
  or or_7 (or_8_out[6], and_104_out[6], and_96_out[6]);
  or or_8 (or_8_out[7], and_104_out[7], and_96_out[7]);
  nand nand_289 (nand_289_out, nand_292_out, nand_290_out);
  nand nand_290 (nand_290_out, nand_289_out, clk);
  nand nand_291 (nand_291_out, nand_290_out, clk, nand_292_out);
  nand nand_292 (nand_292_out, nand_291_out, or_8_out[6]);
  nand nand_293 (nand_293_out, nand_296_out, nand_294_out);
  nand nand_294 (nand_294_out, nand_293_out, clk);
  nand nand_295 (nand_295_out, nand_294_out, clk, nand_296_out);
  nand nand_296 (nand_296_out, nand_295_out, or_8_out[4]);
  nand nand_297 (nand_297_out, nand_300_out, nand_298_out);
  nand nand_298 (nand_298_out, nand_297_out, clk);
  nand nand_299 (nand_299_out, nand_298_out, clk, nand_300_out);
  nand nand_300 (nand_300_out, nand_299_out, or_8_out[2]);
  nand nand_301 (nand_301_out, nand_304_out, nand_302_out);
  nand nand_302 (nand_302_out, nand_301_out, clk);
  nand nand_303 (nand_303_out, nand_302_out, clk, nand_304_out);
  nand nand_304 (nand_304_out, nand_303_out, or_8_out[0]);
  nand nand_305 (nand_335_out[6], nand_290_out, nand_306_out);
  nand nand_306 (nand_306_out, nand_335_out[6], nand_291_out);
  nand nand_307 (nand_335_out[4], nand_294_out, nand_308_out);
  nand nand_308 (nand_308_out, nand_335_out[4], nand_295_out);
  nand nand_309 (nand_335_out[2], nand_298_out, nand_310_out);
  nand nand_310 (nand_310_out, nand_335_out[2], nand_299_out);
  nand nand_311 (nand_335_out[0], nand_302_out, nand_312_out);
  nand nand_312 (nand_312_out, nand_335_out[0], nand_303_out);
  and and_105 (and_105_out, nand_335_out[6], 1'b0);
  and and_106 (and_106_out, nand_335_out[4], 1'b0);
  and and_107 (and_107_out, nand_335_out[2], 1'b0);
  and and_108 (and_108_out, nand_335_out[0], 1'b0);
  nand nand_313 (nand_313_out, nand_316_out, nand_314_out);
  nand nand_314 (nand_314_out, nand_313_out, clk);
  nand nand_315 (nand_315_out, nand_314_out, clk, nand_316_out);
  nand nand_316 (nand_316_out, nand_315_out, or_8_out[7]);
  nand nand_317 (nand_317_out, nand_320_out, nand_318_out);
  nand nand_318 (nand_318_out, nand_317_out, clk);
  nand nand_319 (nand_319_out, nand_318_out, clk, nand_320_out);
  nand nand_320 (nand_320_out, nand_319_out, or_8_out[5]);
  nand nand_321 (nand_321_out, nand_324_out, nand_322_out);
  nand nand_322 (nand_322_out, nand_321_out, clk);
  nand nand_323 (nand_323_out, nand_322_out, clk, nand_324_out);
  nand nand_324 (nand_324_out, nand_323_out, or_8_out[3]);
  nand nand_325 (nand_325_out, nand_328_out, nand_326_out);
  nand nand_326 (nand_326_out, nand_325_out, clk);
  nand nand_327 (nand_327_out, nand_326_out, clk, nand_328_out);
  nand nand_328 (nand_328_out, nand_327_out, or_8_out[1]);
  nand nand_329 (nand_335_out[7], nand_314_out, nand_330_out);
  nand nand_330 (nand_330_out, nand_335_out[7], nand_315_out);
  and and_109 (and_109_out, nand_335_out[7], 1'b0);
  nand nand_331 (nand_335_out[5], nand_318_out, nand_332_out);
  nand nand_332 (nand_332_out, nand_335_out[5], nand_319_out);
  and and_110 (and_110_out, nand_335_out[5], 1'b0);
  nand nand_333 (nand_335_out[3], nand_322_out, nand_334_out);
  nand nand_334 (nand_334_out, nand_335_out[3], nand_323_out);
  and and_111 (and_111_out, nand_335_out[3], 1'b0);
  nand nand_335 (nand_335_out[1], nand_326_out, nand_336_out);
  nand nand_336 (nand_336_out, nand_335_out[1], nand_327_out);
  and and_112 (and_112_out, nand_335_out[1], 1'b0);
  not not_16 (not_16_out, In_3);
  not not_17 (not_17_out, In_2);
  not not_18 (not_18_out, In_1);
  not not_19 (not_19_out, In_3);
  not not_20 (not_20_out, In_2);
  not not_21 (not_21_out, In_1);
  not not_22 (not_22_out, not_16_out);
  and and_113 (and_113_out, not_18_out, not_17_out);
  and and_114 (and_114_out, In_1, not_17_out);
  and and_115 (and_115_out, not_18_out, In_2);
  and and_116 (and_116_out, In_2, In_1);
  and and_117 (and_117_out, not_21_out, not_20_out);
  and and_118 (and_118_out, In_1, not_20_out);
  and and_119 (and_119_out, not_21_out, In_2);
  and and_120 (and_120_out, In_2, In_1);
  and and_121 (and_121_out, and_113_out, not_19_out);
  and and_122 (and_122_out, and_114_out, not_19_out);
  and and_123 (and_123_out, and_115_out, not_19_out);
  and and_124 (and_124_out, and_116_out, not_19_out);
  and and_125 (and_125_out, and_117_out, not_22_out);
  and and_126 (and_126_out, and_118_out, not_22_out);
  and and_127 (and_127_out, and_119_out, not_22_out);
  // And and_128 has open pins: In_1=and_120_out, In_2=not_22_out, out=open
  or or_9 (or_9_out, Num_1[7], Num_1[6]);
  or or_10 (or_10_out, Num_1[5], Num_1[4]);
  or or_11 (or_11_out, Num_1[3], Num_1[2]);
  or or_12 (or_12_out, Num_1[1], Num_1[0]);
  or or_13 (or_13_out, or_9_out, or_10_out);
  or or_14 (or_14_out, or_13_out, or_15_out);
  or or_15 (or_15_out, or_11_out, or_12_out);
  or or_16 (or_16_out, and_126_out, or_17_out);
  or or_17 (or_17_out, and_125_out, and_121_out);
  or or_18 (or_18_out, and_127_out, or_19_out);
  or or_19 (or_19_out, and_131_out, or_23_out);
  or or_20 (or_20_out, or_19_out, or_18_out);
  or or_21 (or_21_out, and_123_out, and_125_out);
  or or_22 (or_22_out, and_124_out, and_126_out);
  or or_23 (or_23_out, and_130_out, or_25_out);
  or or_24 (Out_0, or_26_out, or_20_out);
  not not_23 (not_23_out, or_14_out);
  not not_24 (not_24_out, Num_1[7]);
  or or_25 (or_25_out, and_129_out, and_132_out);
  or or_26 (or_26_out, or_25_out, or_23_out);
  and and_129 (and_129_out, or_16_out, not_23_out);
  and and_130 (and_130_out, or_14_out, and_122_out);
  and and_131 (and_131_out, or_21_out, not_24_out);
  and and_132 (and_132_out, Num_1[7], or_22_out);
  xor xor_9 (xor_9_out, B_0[7], and_212_out);
  xor xor_10 (xor_10_out, B_0[6], and_212_out);
  xor xor_11 (xor_11_out, B_0[5], and_212_out);
  xor xor_12 (xor_12_out, B_0[4], and_212_out);
  xor xor_13 (xor_13_out, B_0[3], and_212_out);
  xor xor_14 (xor_14_out, B_0[2], and_212_out);
  xor xor_15 (xor_15_out, B_0[1], and_212_out);
  xor xor_16 (xor_16_out, B_0[0], and_212_out);
  and and_133 (and_152_out[0], B_0[0], A_0[0]);
  nand nand_337 (nand_344_out[0], B_0[0], A_0[0]);
  or or_27 (or_42_out[0], B_0[0], A_0[0]);
  nor nor_1 (nor_8_out[0], B_0[0], A_0[0]);
  xor xor_17 (xor_36_out[0], B_0[0], A_0[0]);
  and and_134 (and_152_out[1], B_0[1], A_0[1]);
  nand nand_338 (nand_344_out[1], B_0[1], A_0[1]);
  or or_28 (or_42_out[1], B_0[1], A_0[1]);
  nor nor_2 (nor_8_out[1], B_0[1], A_0[1]);
  xor xor_18 (xor_36_out[1], B_0[1], A_0[1]);
  and and_135 (and_152_out[2], B_0[2], A_0[2]);
  nand nand_339 (nand_344_out[2], B_0[2], A_0[2]);
  or or_29 (or_42_out[2], B_0[2], A_0[2]);
  nor nor_3 (nor_8_out[2], B_0[2], A_0[2]);
  xor xor_19 (xor_36_out[2], B_0[2], A_0[2]);
  and and_136 (and_152_out[3], B_0[3], A_0[3]);
  and and_137 (and_152_out[4], B_0[4], A_0[4]);
  nand nand_340 (nand_344_out[3], B_0[3], A_0[3]);
  nand nand_341 (nand_344_out[4], B_0[4], A_0[4]);
  or or_30 (or_42_out[3], B_0[3], A_0[3]);
  or or_31 (or_42_out[4], B_0[4], A_0[4]);
  nor nor_4 (nor_8_out[3], B_0[3], A_0[3]);
  nor nor_5 (nor_8_out[4], B_0[4], A_0[4]);
  xor xor_20 (xor_36_out[3], B_0[3], A_0[3]);
  xor xor_21 (xor_36_out[4], B_0[4], A_0[4]);
  and and_138 (and_152_out[5], B_0[5], A_0[5]);
  nand nand_342 (nand_344_out[5], B_0[5], A_0[5]);
  or or_32 (or_42_out[5], B_0[5], A_0[5]);
  nor nor_6 (nor_8_out[5], B_0[5], A_0[5]);
  xor xor_22 (xor_36_out[5], B_0[5], A_0[5]);
  and and_139 (and_139_out, xor_9_out, A_0[7]);
  xor xor_23 (xor_23_out, A_0[7], xor_9_out);
  and and_140 (and_140_out, xor_10_out, A_0[6]);
  xor xor_24 (xor_24_out, A_0[6], xor_10_out);
  and and_141 (and_141_out, xor_11_out, A_0[5]);
  xor xor_25 (xor_25_out, A_0[5], xor_11_out);
  and and_142 (and_142_out, xor_12_out, A_0[4]);
  xor xor_26 (xor_26_out, A_0[4], xor_12_out);
  and and_143 (and_143_out, xor_13_out, A_0[3]);
  xor xor_27 (xor_27_out, A_0[3], xor_13_out);
  and and_144 (and_144_out, xor_14_out, A_0[2]);
  xor xor_28 (xor_28_out, A_0[2], xor_14_out);
  and and_145 (and_145_out, xor_15_out, A_0[1]);
  xor xor_29 (xor_29_out, A_0[1], xor_15_out);
  and and_146 (and_146_out, xor_16_out, A_0[0]);
  xor xor_30 (xor_30_out, A_0[0], xor_16_out);
  and and_147 (and_152_out[6], B_0[6], A_0[6]);
  nand nand_343 (nand_344_out[6], B_0[6], A_0[6]);
  or or_33 (or_42_out[6], B_0[6], A_0[6]);
  nor nor_7 (nor_8_out[6], B_0[6], A_0[6]);
  xor xor_31 (xor_36_out[6], B_0[6], A_0[6]);
  or or_34 (or_34_out, and_139_out, and_148_out);
  and and_148 (and_148_out, xor_23_out, or_35_out);
  xor xor_32 (xor_40_out[7], xor_23_out, or_35_out);
  or or_35 (or_35_out, and_140_out, and_149_out);
  and and_149 (and_149_out, xor_24_out, or_36_out);
  xor xor_33 (xor_40_out[6], xor_24_out, or_36_out);
  or or_36 (or_36_out, and_141_out, and_150_out);
  and and_150 (and_150_out, xor_25_out, or_37_out);
  xor xor_34 (xor_40_out[5], xor_25_out, or_37_out);
  or or_37 (or_37_out, and_142_out, and_151_out);
  and and_151 (and_151_out, xor_26_out, or_38_out);
  xor xor_35 (xor_40_out[4], xor_26_out, or_38_out);
  or or_38 (or_38_out, and_143_out, and_153_out);
  or or_39 (or_39_out, and_144_out, and_154_out);
  or or_40 (or_40_out, and_145_out, and_155_out);
  or or_41 (or_41_out, and_146_out, and_156_out);
  and and_152 (and_152_out[7], B_0[7], A_0[7]);
  nand nand_344 (nand_344_out[7], B_0[7], A_0[7]);
  or or_42 (or_42_out[7], B_0[7], A_0[7]);
  nor nor_8 (nor_8_out[7], B_0[7], A_0[7]);
  xor xor_36 (xor_36_out[7], B_0[7], A_0[7]);
  and and_153 (and_153_out, xor_27_out, or_39_out);
  xor xor_37 (xor_40_out[3], xor_27_out, or_39_out);
  and and_154 (and_154_out, xor_28_out, or_40_out);
  xor xor_38 (xor_40_out[2], xor_28_out, or_40_out);
  and and_155 (and_155_out, xor_29_out, or_41_out);
  xor xor_39 (xor_40_out[1], xor_29_out, or_41_out);
  and and_156 (and_156_out, xor_30_out, and_212_out);
  xor xor_40 (xor_40_out[0], xor_30_out, and_212_out);
  and and_157 (and_192_out[0], and_213_out, and_152_out[0]);
  and and_158 (and_192_out[1], and_213_out, and_152_out[1]);
  and and_159 (and_193_out[0], and_214_out, nand_344_out[0]);
  and and_160 (and_193_out[1], and_214_out, nand_344_out[1]);
  and and_161 (and_194_out[0], and_215_out, or_42_out[0]);
  and and_162 (and_194_out[1], and_215_out, or_42_out[1]);
  and and_163 (and_195_out[0], and_216_out, nor_8_out[0]);
  and and_164 (and_195_out[1], and_216_out, nor_8_out[1]);
  and and_165 (and_196_out[0], and_217_out, xor_36_out[0]);
  and and_166 (and_196_out[1], and_217_out, xor_36_out[1]);
  and and_167 (and_192_out[2], and_213_out, and_152_out[2]);
  and and_168 (and_193_out[2], and_214_out, nand_344_out[2]);
  and and_169 (and_194_out[2], and_215_out, or_42_out[2]);
  and and_170 (and_195_out[2], and_216_out, nor_8_out[2]);
  and and_171 (and_196_out[2], and_217_out, xor_36_out[2]);
  and and_172 (and_192_out[3], and_213_out, and_152_out[3]);
  and and_173 (and_193_out[3], and_214_out, nand_344_out[3]);
  and and_174 (and_194_out[3], and_215_out, or_42_out[3]);
  and and_175 (and_195_out[3], and_216_out, nor_8_out[3]);
  and and_176 (and_196_out[3], and_217_out, xor_36_out[3]);
  and and_177 (and_192_out[4], and_213_out, and_152_out[4]);
  and and_178 (and_192_out[5], and_213_out, and_152_out[5]);
  and and_179 (and_193_out[4], and_214_out, nand_344_out[4]);
  and and_180 (and_193_out[5], and_214_out, nand_344_out[5]);
  and and_181 (and_194_out[4], and_215_out, or_42_out[4]);
  and and_182 (and_194_out[5], and_215_out, or_42_out[5]);
  and and_183 (and_195_out[4], and_216_out, nor_8_out[4]);
  and and_184 (and_195_out[5], and_216_out, nor_8_out[5]);
  and and_185 (and_196_out[4], and_217_out, xor_36_out[4]);
  and and_186 (and_196_out[5], and_217_out, xor_36_out[5]);
  and and_187 (and_192_out[6], and_213_out, and_152_out[6]);
  and and_188 (and_193_out[6], and_214_out, nand_344_out[6]);
  and and_189 (and_194_out[6], and_215_out, or_42_out[6]);
  and and_190 (and_195_out[6], and_216_out, nor_8_out[6]);
  and and_191 (and_196_out[6], and_217_out, xor_36_out[6]);
  and and_192 (and_192_out[7], and_213_out, and_152_out[7]);
  and and_193 (and_193_out[7], and_214_out, nand_344_out[7]);
  and and_194 (and_194_out[7], and_215_out, or_42_out[7]);
  and and_195 (and_195_out[7], and_216_out, nor_8_out[7]);
  and and_196 (and_196_out[7], and_217_out, xor_36_out[7]);
  not not_25 (not_25_out, C_2);
  and and_197 (and_220_out[0], or_43_out, xor_40_out[0]);
  not not_26 (not_26_out, C_1);
  not not_27 (not_27_out, C_1);
  and and_198 (and_220_out[1], or_43_out, xor_40_out[1]);
  not not_28 (not_28_out, C_0);
  and and_199 (and_199_out, not_28_out, not_26_out);
  and and_200 (and_200_out, C_0, not_26_out);
  and and_201 (and_201_out, not_28_out, C_1);
  and and_202 (and_202_out, C_1, C_0);
  not not_29 (not_29_out, C_2);
  not not_30 (not_30_out, C_0);
  and and_203 (and_203_out, not_30_out, not_27_out);
  and and_204 (and_204_out, C_0, not_27_out);
  and and_205 (and_205_out, not_30_out, C_1);
  and and_206 (and_206_out, C_1, C_0);
  not not_31 (not_31_out, not_25_out);
  and and_207 (and_220_out[2], or_43_out, xor_40_out[2]);
  and and_208 (and_220_out[3], or_43_out, xor_40_out[3]);
  and and_209 (and_220_out[4], or_43_out, xor_40_out[4]);
  // And and_210 has open pins: In_1=and_199_out, In_2=not_29_out, out=open
  and and_211 (and_211_out, and_200_out, not_29_out);
  and and_212 (and_212_out, and_201_out, not_29_out);
  and and_213 (and_213_out, and_202_out, not_29_out);
  and and_214 (and_214_out, and_203_out, not_31_out);
  and and_215 (and_215_out, and_204_out, not_31_out);
  and and_216 (and_216_out, and_205_out, not_31_out);
  and and_217 (and_217_out, and_206_out, not_31_out);
  and and_218 (and_220_out[5], or_43_out, xor_40_out[5]);
  and and_219 (and_220_out[6], or_43_out, xor_40_out[6]);
  and and_220 (and_220_out[7], or_43_out, xor_40_out[7]);
  or or_43 (or_43_out, and_211_out, and_212_out);
  or or_44 (O_0[0], and_220_out[0], or_80_out[0]);
  or or_45 (or_80_out[0], and_192_out[0], or_81_out[0]);
  or or_46 (or_81_out[0], and_193_out[0], or_82_out[0]);
  or or_47 (or_82_out[0], and_194_out[0], or_83_out[0]);
  or or_48 (or_83_out[0], and_195_out[0], and_196_out[0]);
  or or_49 (O_0[1], and_220_out[1], or_80_out[1]);
  or or_50 (or_80_out[1], and_192_out[1], or_81_out[1]);
  or or_51 (or_81_out[1], and_193_out[1], or_82_out[1]);
  or or_52 (or_82_out[1], and_194_out[1], or_83_out[1]);
  or or_53 (or_83_out[1], and_195_out[1], and_196_out[1]);
  or or_54 (O_0[2], and_220_out[2], or_80_out[2]);
  or or_55 (or_80_out[2], and_192_out[2], or_81_out[2]);
  or or_56 (or_81_out[2], and_193_out[2], or_82_out[2]);
  or or_57 (or_82_out[2], and_194_out[2], or_83_out[2]);
  or or_58 (or_83_out[2], and_195_out[2], and_196_out[2]);
  or or_59 (O_0[3], and_220_out[3], or_80_out[3]);
  or or_60 (O_0[4], and_220_out[4], or_80_out[4]);
  or or_61 (or_80_out[3], and_192_out[3], or_81_out[3]);
  or or_62 (or_80_out[4], and_192_out[4], or_81_out[4]);
  or or_63 (or_81_out[3], and_193_out[3], or_82_out[3]);
  or or_64 (or_81_out[4], and_193_out[4], or_82_out[4]);
  or or_65 (or_82_out[3], and_194_out[3], or_83_out[3]);
  or or_66 (or_82_out[4], and_194_out[4], or_83_out[4]);
  or or_67 (or_83_out[3], and_195_out[3], and_196_out[3]);
  or or_68 (or_83_out[4], and_195_out[4], and_196_out[4]);
  or or_69 (O_0[5], and_220_out[5], or_80_out[5]);
  or or_70 (or_80_out[5], and_192_out[5], or_81_out[5]);
  or or_71 (or_81_out[5], and_193_out[5], or_82_out[5]);
  or or_72 (or_82_out[5], and_194_out[5], or_83_out[5]);
  or or_73 (or_83_out[5], and_195_out[5], and_196_out[5]);
  or or_74 (O_0[6], and_220_out[6], or_80_out[6]);
  or or_75 (or_80_out[6], and_192_out[6], or_81_out[6]);
  or or_76 (or_81_out[6], and_193_out[6], or_82_out[6]);
  or or_77 (or_82_out[6], and_194_out[6], or_83_out[6]);
  or or_78 (or_83_out[6], and_195_out[6], and_196_out[6]);
  or or_79 (O_0[7], and_220_out[7], or_80_out[7]);
  or or_80 (or_80_out[7], and_192_out[7], or_81_out[7]);
  or or_81 (or_81_out[7], and_193_out[7], or_82_out[7]);
  or or_82 (or_82_out[7], and_194_out[7], or_83_out[7]);
  or or_83 (or_83_out[7], and_195_out[7], and_196_out[7]);
  // NotConnected on notconnected_25_out
  // NotConnected on notconnected_26_out
  // NotConnected on notconnected_27_out
  // NotConnected on notconnected_28_out
  // NotConnected on notconnected_29_out
  // NotConnected on notconnected_30_out
  // NotConnected on notconnected_31_out
  // NotConnected on notconnected_32_out
  nand nand_345 (nand_345_out, nand_348_out, nand_346_out);
  nand nand_346 (nand_346_out, nand_345_out, notconnected_26_out);
  nand nand_347 (nand_347_out, nand_346_out, notconnected_26_out, nand_348_out);
  nand nand_348 (nand_348_out, nand_347_out, notconnected_25_out[6]);
  nand nand_349 (nand_349_out, nand_352_out, nand_350_out);
  nand nand_350 (nand_350_out, nand_349_out, notconnected_26_out);
  nand nand_351 (nand_351_out, nand_350_out, notconnected_26_out, nand_352_out);
  nand nand_352 (nand_352_out, nand_351_out, notconnected_25_out[4]);
  nand nand_353 (nand_353_out, nand_356_out, nand_354_out);
  nand nand_354 (nand_354_out, nand_353_out, notconnected_26_out);
  nand nand_355 (nand_355_out, nand_354_out, notconnected_26_out, nand_356_out);
  nand nand_356 (nand_356_out, nand_355_out, notconnected_25_out[2]);
  nand nand_357 (nand_357_out, nand_360_out, nand_358_out);
  nand nand_358 (nand_358_out, nand_357_out, notconnected_26_out);
  nand nand_359 (nand_359_out, nand_358_out, notconnected_26_out, nand_360_out);
  nand nand_360 (nand_360_out, nand_359_out, notconnected_25_out[0]);
  DipSwitch dipswitch_2 (.out(dipswitch_2_out));
  DipSwitch dipswitch_3 (.out(dipswitch_3_out));
  DipSwitch dipswitch_4 (.out(dipswitch_4_out));
  not not_32 (not_32_out, notconnected_30_out[7]);
  and and_221 (and_221_out, notconnected_28_out, notconnected_30_out[7]);
  not not_33 (not_33_out, notconnected_30_out[6]);
  and and_222 (and_222_out, notconnected_28_out, notconnected_30_out[6]);
  not not_34 (not_34_out, notconnected_30_out[5]);
  and and_223 (and_223_out, notconnected_28_out, notconnected_30_out[5]);
  not not_35 (not_35_out, notconnected_30_out[4]);
  and and_224 (and_224_out, notconnected_28_out, notconnected_30_out[4]);
  not not_36 (not_36_out, notconnected_30_out[3]);
  and and_225 (and_225_out, notconnected_28_out, notconnected_30_out[3]);
  not not_37 (not_37_out, notconnected_30_out[2]);
  and and_226 (and_226_out, notconnected_28_out, notconnected_30_out[2]);
  not not_38 (not_38_out, notconnected_30_out[1]);
  and and_227 (and_227_out, notconnected_28_out, notconnected_30_out[1]);
  not not_39 (not_39_out, notconnected_30_out[0]);
  and and_228 (and_228_out, notconnected_28_out, notconnected_30_out[0]);
  and and_229 (and_229_out, not_40_out, dipswitch_3_out);
  not not_40 (not_40_out, dipswitch_4_out);
  and and_230 (and_230_out, dipswitch_3_out, dipswitch_4_out);
  and and_231 (and_231_out, not_32_out, notconnected_28_out);
  and and_232 (and_232_out, not_33_out, notconnected_28_out);
  and and_233 (and_233_out, not_34_out, notconnected_28_out);
  and and_234 (and_234_out, not_35_out, notconnected_28_out);
  and and_235 (and_235_out, not_36_out, notconnected_28_out);
  and and_236 (and_236_out, not_37_out, notconnected_28_out);
  and and_237 (and_237_out, not_38_out, notconnected_28_out);
  and and_238 (and_238_out, not_39_out, notconnected_28_out);
  nor nor_9 (nor_9_out, and_231_out, nor_10_out);
  nor nor_10 (nor_10_out, nor_9_out, and_221_out);
  nor nor_11 (nor_11_out, and_232_out, nor_12_out);
  nor nor_12 (nor_12_out, nor_11_out, and_222_out);
  nor nor_13 (nor_13_out, and_233_out, nor_14_out);
  nor nor_14 (nor_14_out, nor_13_out, and_223_out);
  nor nor_15 (nor_15_out, and_234_out, nor_16_out);
  nor nor_16 (nor_16_out, nor_15_out, and_224_out);
  nor nor_17 (nor_17_out, and_235_out, nor_18_out);
  nor nor_18 (nor_18_out, nor_17_out, and_225_out);
  nor nor_19 (nor_19_out, and_236_out, nor_20_out);
  nor nor_20 (nor_20_out, nor_19_out, and_226_out);
  nor nor_21 (nor_21_out, and_237_out, nor_22_out);
  nor nor_22 (nor_22_out, nor_21_out, and_227_out);
  nor nor_23 (nor_23_out, and_238_out, nor_24_out);
  nor nor_24 (nor_24_out, nor_23_out, and_228_out);
  nand nand_361 (nand_361_out, nand_346_out, nand_362_out);
  nand nand_362 (nand_362_out, nand_361_out, nand_347_out);
  and and_239 (and_239_out, nand_361_out, notconnected_27_out);
  nand nand_363 (nand_363_out, nand_350_out, nand_364_out);
  nand nand_364 (nand_364_out, nand_363_out, nand_351_out);
  and and_240 (and_240_out, nand_363_out, notconnected_27_out);
  nand nand_365 (nand_365_out, nand_354_out, nand_366_out);
  nand nand_366 (nand_366_out, nand_365_out, nand_355_out);
  and and_241 (and_241_out, nand_365_out, notconnected_27_out);
  nand nand_367 (nand_367_out, nand_358_out, nand_368_out);
  nand nand_368 (nand_368_out, nand_367_out, nand_359_out);
  and and_242 (and_242_out, nand_367_out, notconnected_27_out);
  and and_243 (and_243_out, notconnected_31_out[7], notconnected_32_out[7]);
  xor xor_41 (xor_41_out, notconnected_32_out[7], notconnected_31_out[7]);
  and and_244 (and_244_out, notconnected_31_out[6], notconnected_32_out[6]);
  xor xor_42 (xor_42_out, notconnected_32_out[6], notconnected_31_out[6]);
  and and_245 (and_245_out, notconnected_31_out[5], notconnected_32_out[5]);
  xor xor_43 (xor_43_out, notconnected_32_out[5], notconnected_31_out[5]);
  and and_246 (and_246_out, notconnected_31_out[4], notconnected_32_out[4]);
  xor xor_44 (xor_44_out, notconnected_32_out[4], notconnected_31_out[4]);
  and and_247 (and_247_out, notconnected_31_out[3], notconnected_32_out[3]);
  xor xor_45 (xor_45_out, notconnected_32_out[3], notconnected_31_out[3]);
  and and_248 (and_248_out, notconnected_31_out[2], notconnected_32_out[2]);
  xor xor_46 (xor_46_out, notconnected_32_out[2], notconnected_31_out[2]);
  and and_249 (and_249_out, notconnected_31_out[1], notconnected_32_out[1]);
  xor xor_47 (xor_47_out, notconnected_32_out[1], notconnected_31_out[1]);
  and and_250 (and_250_out, notconnected_31_out[0], notconnected_32_out[0]);
  xor xor_48 (xor_48_out, notconnected_32_out[0], notconnected_31_out[0]);
  nor nor_25 (nor_25_out, and_229_out, nor_26_out);
  nor nor_26 (nor_26_out, nor_25_out, and_230_out);
  or or_84 (or_84_out, and_243_out, and_251_out);
  and and_251 (and_251_out, xor_41_out, or_85_out);
  xor xor_49 (xor_49_out, xor_41_out, or_85_out);
  or or_85 (or_85_out, and_244_out, and_252_out);
  and and_252 (and_252_out, xor_42_out, or_86_out);
  xor xor_50 (xor_50_out, xor_42_out, or_86_out);
  or or_86 (or_86_out, and_245_out, and_253_out);
  and and_253 (and_253_out, xor_43_out, or_87_out);
  xor xor_51 (xor_51_out, xor_43_out, or_87_out);
  or or_87 (or_87_out, and_246_out, and_254_out);
  and and_254 (and_254_out, xor_44_out, or_88_out);
  xor xor_52 (xor_52_out, xor_44_out, or_88_out);
  or or_88 (or_88_out, and_247_out, and_263_out);
  or or_89 (or_89_out, and_248_out, and_264_out);
  or or_90 (or_90_out, and_249_out, and_265_out);
  or or_91 (or_91_out, and_250_out, and_266_out);
  // NotConnected on notconnected_33_out
  Reset reset_1 ();  // open: out
  Reset reset_2 ();  // open: out
  and and_255 (and_255_out, nor_9_out, notconnected_29_out);
  Reset reset_3 ();  // open: out
  and and_256 (and_256_out, nor_11_out, notconnected_29_out);
  Reset reset_4 ();  // open: out
  and and_257 (and_257_out, nor_13_out, notconnected_29_out);
  Reset reset_5 ();  // open: out
  and and_258 (and_258_out, nor_15_out, notconnected_29_out);
  Reset reset_6 ();  // open: out
  and and_259 (and_259_out, nor_17_out, notconnected_29_out);
  Reset reset_7 ();  // open: out
  and and_260 (and_260_out, nor_19_out, notconnected_29_out);
  Reset reset_8 ();  // open: out
  and and_261 (and_261_out, nor_21_out, notconnected_29_out);
  Reset reset_9 ();  // open: out
  and and_262 (and_262_out, nor_23_out, notconnected_29_out);
  and and_263 (and_263_out, xor_45_out, or_89_out);
  xor xor_53 (xor_53_out, xor_45_out, or_89_out);
  and and_264 (and_264_out, xor_46_out, or_90_out);
  xor xor_54 (xor_54_out, xor_46_out, or_90_out);
  and and_265 (and_265_out, xor_47_out, or_91_out);
  xor xor_55 (xor_55_out, xor_47_out, or_91_out);
  and and_266 (and_266_out, xor_48_out, notconnected_33_out);
  xor xor_56 (xor_56_out, xor_48_out, notconnected_33_out);
  and and_267 (and_267_out, nor_25_out, dipswitch_2_out);
  nand nand_369 (nand_369_out, nand_372_out, nand_370_out);
  nand nand_370 (nand_370_out, nand_369_out, notconnected_26_out);
  nand nand_371 (nand_371_out, nand_370_out, notconnected_26_out, nand_372_out);
  nand nand_372 (nand_372_out, nand_371_out, notconnected_25_out[7]);
  nand nand_373 (nand_373_out, nand_376_out, nand_374_out);
  nand nand_374 (nand_374_out, nand_373_out, notconnected_26_out);
  nand nand_375 (nand_375_out, nand_374_out, notconnected_26_out, nand_376_out);
  nand nand_376 (nand_376_out, nand_375_out, notconnected_25_out[5]);
  nand nand_377 (nand_377_out, nand_380_out, nand_378_out);
  nand nand_378 (nand_378_out, nand_377_out, notconnected_26_out);
  nand nand_379 (nand_379_out, nand_378_out, notconnected_26_out, nand_380_out);
  nand nand_380 (nand_380_out, nand_379_out, notconnected_25_out[3]);
  nand nand_381 (nand_381_out, nand_384_out, nand_382_out);
  nand nand_382 (nand_382_out, nand_381_out, notconnected_26_out);
  nand nand_383 (nand_383_out, nand_382_out, notconnected_26_out, nand_384_out);
  nand nand_384 (nand_384_out, nand_383_out, notconnected_25_out[1]);
  nand nand_385 (nand_385_out, nand_370_out, nand_386_out);
  nand nand_386 (nand_386_out, nand_385_out, nand_371_out);
  and and_268 (and_268_out, nand_385_out, notconnected_27_out);
  nand nand_387 (nand_387_out, nand_374_out, nand_388_out);
  nand nand_388 (nand_388_out, nand_387_out, nand_375_out);
  and and_269 (and_269_out, nand_387_out, notconnected_27_out);
  nand nand_389 (nand_389_out, nand_378_out, nand_390_out);
  nand nand_390 (nand_390_out, nand_389_out, nand_379_out);
  and and_270 (and_270_out, nand_389_out, notconnected_27_out);
  nand nand_391 (nand_391_out, nand_382_out, nand_392_out);
  nand nand_392 (nand_392_out, nand_391_out, nand_383_out);
  and and_271 (and_271_out, nand_391_out, notconnected_27_out);
  // NotConnected on notconnected_34_out
  // NotConnected on notconnected_35_out
  // NotConnected on notconnected_36_out
  // NotConnected on notconnected_37_out
  and and_272 (and_272_out, notconnected_35_out[0], notconnected_35_out[0]);
  or or_92 (or_92_out, notconnected_36_out[0], notconnected_36_out[0]);
  xor xor_57 (xor_57_out, notconnected_37_out[0], notconnected_37_out[0]);
  and and_273 (and_273_out, notconnected_35_out[1], notconnected_35_out[1]);
  or or_93 (or_93_out, notconnected_36_out[1], notconnected_36_out[1]);
  xor xor_58 (xor_58_out, notconnected_37_out[1], notconnected_37_out[1]);
  not not_41 (not_41_out, notconnected_38_out);
  // NotConnected on notconnected_38_out
  and and_274 (and_274_out, notconnected_35_out[2], notconnected_35_out[2]);
  and and_275 (and_275_out, notconnected_35_out[3], notconnected_35_out[3]);
  or or_94 (or_94_out, notconnected_36_out[2], notconnected_36_out[2]);
  or or_95 (or_95_out, notconnected_36_out[3], notconnected_36_out[3]);
  xor xor_59 (xor_59_out, notconnected_37_out[2], notconnected_37_out[2]);
  xor xor_60 (xor_60_out, notconnected_37_out[3], notconnected_37_out[3]);
  // And and_276 has open pins: In_1=and_277_out, In_2=notconnected_34_out[7], out=open
  xor xor_61 (xor_61_out, notconnected_34_out[7], and_277_out);
  and and_277 (and_277_out, and_278_out, notconnected_34_out[6]);
  xor xor_62 (xor_62_out, notconnected_34_out[6], and_278_out);
  and and_278 (and_278_out, and_279_out, notconnected_34_out[5]);
  xor xor_63 (xor_63_out, notconnected_34_out[5], and_279_out);
  and and_279 (and_279_out, and_280_out, notconnected_34_out[4]);
  xor xor_64 (xor_64_out, notconnected_34_out[4], and_280_out);
  and and_280 (and_280_out, and_281_out, notconnected_34_out[3]);
  xor xor_65 (xor_65_out, notconnected_34_out[3], and_281_out);
  and and_281 (and_281_out, and_282_out, notconnected_34_out[2]);
  xor xor_66 (xor_66_out, notconnected_34_out[2], and_282_out);
  and and_282 (and_282_out, and_283_out, notconnected_34_out[1]);
  xor xor_67 (xor_67_out, notconnected_34_out[1], and_283_out);
  and and_283 (and_283_out, not_41_out, notconnected_34_out[0]);
  xor xor_68 (xor_68_out, notconnected_34_out[0], not_41_out);
  and and_284 (and_284_out, notconnected_35_out[4], notconnected_35_out[4]);
  or or_96 (or_96_out, notconnected_36_out[4], notconnected_36_out[4]);
  xor xor_69 (xor_69_out, notconnected_37_out[4], notconnected_37_out[4]);
  and and_285 (and_285_out, notconnected_35_out[5], notconnected_35_out[5]);
  or or_97 (or_97_out, notconnected_36_out[5], notconnected_36_out[5]);
  xor xor_70 (xor_70_out, notconnected_37_out[5], notconnected_37_out[5]);
  and and_286 (and_286_out, notconnected_35_out[6], notconnected_35_out[6]);
  and and_287 (and_287_out, notconnected_35_out[7], notconnected_35_out[7]);
  or or_98 (or_98_out, notconnected_36_out[6], notconnected_36_out[6]);
  or or_99 (or_99_out, notconnected_36_out[7], notconnected_36_out[7]);
  xor xor_71 (xor_71_out, notconnected_37_out[6], notconnected_37_out[6]);
  xor xor_72 (xor_72_out, notconnected_37_out[7], notconnected_37_out[7]);
  // NotConnected on notconnected_39_out
  // NotConnected on notconnected_40_out
  // NotConnected on notconnected_41_out
  // NotConnected on notconnected_42_out
  // NotConnected on notconnected_43_out
  // NotConnected on notconnected_44_out
  and and_288 (and_288_out, notconnected_45_out, notconnected_39_out[0]);
  nand nand_393 (nand_393_out, notconnected_40_out[0], notconnected_40_out[0]);
  nor nor_27 (nor_27_out, notconnected_41_out[0], notconnected_41_out[0]);
  not not_42 (not_42_out, notconnected_44_out);
  and and_289 (and_289_out, notconnected_45_out, notconnected_39_out[1]);
  and and_290 (and_290_out, notconnected_45_out, notconnected_39_out[2]);
  nand nand_394 (nand_394_out, notconnected_40_out[1], notconnected_40_out[1]);
  nand nand_395 (nand_395_out, notconnected_40_out[2], notconnected_40_out[2]);
  nor nor_28 (nor_28_out, notconnected_41_out[1], notconnected_41_out[1]);
  nor nor_29 (nor_29_out, notconnected_41_out[2], notconnected_41_out[2]);
  not not_43 (not_43_out, notconnected_43_out);
  not not_44 (not_44_out, notconnected_42_out);
  not not_45 (not_45_out, notconnected_44_out);
  not not_46 (not_46_out, notconnected_43_out);
  not not_47 (not_47_out, notconnected_42_out);
  not not_48 (not_48_out, not_42_out);
  // NotConnected on notconnected_45_out
  and and_291 (and_291_out, notconnected_45_out, notconnected_39_out[3]);
  nand nand_396 (nand_396_out, notconnected_40_out[3], notconnected_40_out[3]);
  nor nor_30 (nor_30_out, notconnected_41_out[3], notconnected_41_out[3]);
  and and_292 (and_292_out, not_44_out, not_43_out);
  and and_293 (and_293_out, notconnected_42_out, not_43_out);
  and and_294 (and_294_out, not_44_out, notconnected_43_out);
  and and_295 (and_295_out, notconnected_43_out, notconnected_42_out);
  and and_296 (and_296_out, not_47_out, not_46_out);
  and and_297 (and_297_out, notconnected_42_out, not_46_out);
  and and_298 (and_298_out, not_47_out, notconnected_43_out);
  and and_299 (and_299_out, notconnected_43_out, notconnected_42_out);
  and and_300 (and_300_out, notconnected_45_out, notconnected_39_out[4]);
  nand nand_397 (nand_397_out, notconnected_40_out[4], notconnected_40_out[4]);
  nor nor_31 (nor_31_out, notconnected_41_out[4], notconnected_41_out[4]);
  and and_301 (and_301_out, and_292_out, not_45_out);
  and and_302 (and_302_out, and_293_out, not_45_out);
  and and_303 (and_303_out, and_294_out, not_45_out);
  and and_304 (and_304_out, and_295_out, not_45_out);
  and and_305 (and_305_out, and_296_out, not_48_out);
  and and_306 (and_306_out, and_297_out, not_48_out);
  and and_307 (and_307_out, and_298_out, not_48_out);
  and and_308 (and_308_out, and_299_out, not_48_out);
  and and_309 (and_309_out, notconnected_45_out, notconnected_39_out[5]);
  and and_310 (and_310_out, notconnected_45_out, notconnected_39_out[6]);
  nand nand_398 (nand_398_out, notconnected_40_out[5], notconnected_40_out[5]);
  nand nand_399 (nand_399_out, notconnected_40_out[6], notconnected_40_out[6]);
  nor nor_32 (nor_32_out, notconnected_41_out[5], notconnected_41_out[5]);
  nor nor_33 (nor_33_out, notconnected_41_out[6], notconnected_41_out[6]);
  and and_311 (and_311_out, notconnected_45_out, notconnected_39_out[7]);
  nand nand_400 (nand_400_out, notconnected_40_out[7], notconnected_40_out[7]);
  nor nor_34 (nor_34_out, notconnected_41_out[7], notconnected_41_out[7]);

  // Notes on the sheet:
  //   Disable
  //   2x4 Demux
  //   A_0
  //   A_1
  //   A3
  //   A1
  //   A2
  //   3x8 Demux
  //   Edge Register
  //   Clk
  //   Load
  //   D
  //   Edge Flop
  //   Latch
  //   Always
  //   Loaded
  //   Overwrite Value
  //   Overwrite
  //   COUNTER
  //   B
  //   Select
  //   MUX
  //   A
  //   INCRMNT
  //   SWITCH
  //   OR
  //   Conditional Unit
  //   Is less than 0 Unit
  //   Is!0 Unit
  //   Is0
  //   IsNot0
  //   More
  //   Less
  //   MoreOrEqual
  //   LessOrEqual
  //   Never
  //   ALU
  //   ADDER
  //   AND
  //   NAND
  //   NOR
  //   XOR
  //   .
  //   COMPONENTS
  //   Register - outdated
  //   Save
  //   Save Value
  //   1 Bit mem
  //   SaveVal
  //   Reset
  //   Write
  //   Always OUT
  //   OUT
  //   Always On Out
  //   Out
endmodule

/* Test case:
D C L ALWAYS LOADED
# 1. Randomized Startup: Register state is unknown (X). LOADED is 0 because L=0.
0x00 0 0 X 0x00

# 2. Load 0xAA: ALWAYS updates to 0xAA. LOADED shows it because L=1.
0xAA C 1 0xAA 0xAA

# 3. Transparent Check: ALWAYS stays 0xAA. LOADED drops to 0x00 because L=0.
0x55 0 0 0xAA 0x00
0x21 C 0 0x21 0x00

# 5. Load 0x00: Register becomes 0. Both pins show 0.
0x00 C 1 0x00 0x00

# 6. Edge-Triggering: Data 0xEE only moves to ALWAYS on the rising edge.
0xEE 0 1 0x00 0x00  # L=1, but no clock yet; LOADED is 0 because reg is 0
0xEE 1 1 0xEE 0xEE  # Clock goes high; Reg becomes 0xEE. LOADED now shows it.
0xDD 0 1 0xEE 0xEE  # Clock falls; Reg stays 0xEE.

# 7. High-Clock Stability Test
0xAA 0 1 0xEE 0xEE  # Prepare data 0xAA, but clock is 0. ALWAYS stays 0xEE.
0xAA 1 1 0xAA 0xAA  # Clock goes High. Register captures 0xAA.
0xFF 1 1 0xAA 0xAA  # DATA CHANGES TO 0xFF WHILE CLOCK IS STILL HIGH.
                    # ALWAYS MUST STAY 0xAA. If it changes to 0xFF, it's a latch!
*/

/* Test case:
In_3 In_2 In_1 Num_1 Out_0
0 0 0 4 0
0 0 1 5 1
0 0 0 210 0
0 0 1 253 1
0 1 1 65 0
0 1 0 102 1
0 1 1 237 1
0 1 0 179 0
1 0 0 102 1
1 0 0 0 1
1 0 0 252 0
1 0 1 179 1
1 0 1 0 1
1 0 1 112 0
1 1 0 0 1
1 1 0 243 1
1 1 0 123 1
1 1 1 0 0
1 1 1 243 0
1 1 1 123 0
*/

/* Test case:
C_2 C_1 C_0 A_0 B_0 O_0
0 0 1 9 6 15 #addition and subtraction
0 1 0 9 6 3
0 0 1 6 7 13
0 1 0 111 67 44
0 0 1 32 59 91
0 1 1 51 60 48  #and
0 1 1 3 2 2
0 1 1 5 3 1
0 1 1 12 25 8
0 1 1 4 8 0
1 0 1 5 3 7 #or
1 0 1 2 8 10
1 0 1 12 25 29
1 0 1 0 7 7
1 0 0 1 1 254 #nand
1 0 0 2 4 255
1 0 0 15 3 252
1 1 0 1 0 254 #nor
1 1 0 3 5 248
1 1 0 128 64 63
1 1 1 5 3 6 #xor
1 1 1 10 10 0
1 1 1 85 170 255
1 1 1 14 1 15
*/
